// Logisim project 3202D.circ as structural Verilog: 72 circuits, main circuit C_PLUG_4
module BLOCK_DIAGRAM_1 (
  input  [3:0] PD_4_1
);

  CYC_36 CYC ();  // open: OSC, RRF_n, CSDELAY1, CSALUM1, CSALUM0, CSALUI8, CSALUI7, LBA3, LBA1, LBA0, CSDELAY0, CSDLY, CSECOND, CSLOOP, ACOND_n, MR_n, LUA12, PD1, CGNTCACT_n, HIT, BRK_n, SHORT_n, SLOW_n, PD4, FORM_n, RWCS_n, TRAP_n, VEX, MREQ_n, IORQ_n, LSHADOW, RT_n, CLK, ALUCLK, LCS_n, MCLK, CX_n, TERM_n, MACLK, CC_3_1_n, UCLK, WRFSTB, CYD, EORF_n, ETRAP_n, MAP_n
  IO_37 IO ();  // open: IOCSB_B, IO100I_B, IOABP_B, IDB_7_0_io, IDB_15_8, OSC, IOINT
  CPU_15_Verilog CPU ();
  BIF_5 BIF ();  // open: IORQ_n, MIS0, CGNT_n, CGNT50_n, CC2_n, TERM_n, PD3, PD1, PPN_23_10, CA_9_0, TOUT, ECRQ, OSC, FETCH, CRQ_n, GNT50_n, CLEAR_n, REFRQ_n, MOFF_n, SSEMA_n, BGNT_n, RT_n, MOR25_n, WRITE, LPRERR_n, LERR_n, BGNT50_n, PS_n, MWRITE_n, PA_n, EBUS_n, IBAPR_n, IBREQ_n, IBPERR_n, IBDAP_n, IBDRY_n, IBINPUT_n, ISEMRQ_n, LBD_23_0_io, CD_15_0_io, BD_23_0_n_io, IDB_15_0, SEMRQ50_n, CGNCACT_n, IOXERR_n, MR_n, DBAPR, MOR_n, REF_n, DAP_n, OUTIDENT_n, PARERR_n, RERR_n, OUTGRANT_n, BREF_n, BMEM_n, GNT_n, BDAP50_n, BIOXE_n, BDRY50_n, BINACK_n, BERROR_n, BAPR_n, BDAP_n, BDRY_n, BINPUT_n, SEMRQ_n

  // Notes on the sheet:
  //   ND120 CPU, MM&M
  //   DELILAH TOP LEVEL
  //   BLOCK DIAGRAM
  //   SHEET 1 of 50
endmodule

module A_PLUG_2 (
);


  // Notes on the sheet:
  //   ND120 CPU, MM&M
  //   DELILAH TOP LEVEL
  //   A PLUG
  //   SHEET 2 of 50
endmodule

module B_PLUG_3 (
);


  // Notes on the sheet:
  //   ND120 CPU, MM&M
  //   DELILAH TOP LEVEL
  //   B PLUG
  //   SHEET 3 of 50
endmodule

module C_PLUG_4 (
);


  // Notes on the sheet:
  //   ND120 CPU, MM&M
  //   DELILAH TOP LEVEL
  //   C PLUG
  //   SHEET 4 of 50
endmodule

module BIF_5 (
  input  IORQ_n,
  input  MIS0,
  input  CGNT_n,
  input  CGNT50_n,
  input  CC2_n,
  input  TERM_n,
  input  PD3,
  input  PD1,
  input  [13:0] PPN_23_10,
  input  [9:0] CA_9_0,
  input  TOUT,
  input  ECRQ,
  input  OSC,
  input  FETCH,
  input  CRQ_n,
  input  GNT50_n,
  input  CLEAR_n,
  input  REFRQ_n,
  input  MOFF_n,
  input  SSEMA_n,
  input  BGNT_n,
  input  RT_n,
  input  MOR25_n,
  input  WRITE,
  input  LPRERR_n,
  input  LERR_n,
  input  BGNT50_n,
  input  PS_n,
  input  MWRITE_n,
  input  PA_n,
  input  EBUS_n,
  input  IBAPR_n,
  input  IBREQ_n,
  input  IBPERR_n,
  input  IBDAP_n,
  input  IBDRY_n,
  input  IBINPUT_n,
  input  ISEMRQ_n,
  output [23:0] LBD_23_0_io,
  output [15:0] CD_15_0_io,
  output [23:0] BD_23_0_n_io,
  output [15:0] IDB_15_0,
  output SEMRQ50_n,
  output CGNCACT_n,
  output IOXERR_n,
  output MR_n,
  output DBAPR,
  output MOR_n,
  output REF_n,
  output DAP_n,
  output OUTIDENT_n,
  output PARERR_n,
  output RERR_n,
  output OUTGRANT_n,
  output BREF_n,
  output BMEM_n,
  output GNT_n,
  output BDAP50_n,
  output BIOXE_n,
  output BDRY50_n,
  output BINACK_n,
  output BERROR_n,
  output BAPR_n,
  output BDAP_n,
  output BDRY_n,
  output BINPUT_n,
  output SEMRQ_n
);

  wire BCTL_bdry25_n, BCTL_binput50_n, BCTL_cact_n, BCTL_eadr_n, BCTL_epea_n, BCTL_epes_n, BCTL_iod_n,
       BCTL_spea, BCTL_spes, CBWRITE_n;
  wire [2:0] BCTL_q_2_0_n;

  BIF_BCTL_6 BCTL (
    .MIS0(MIS0), .TOUT(TOUT), .OSC(OSC), .CRQ_n(CRQ_n), .GNT50_n(GNT50_n), .IORQ_n(IORQ_n),
    .CLEAR_n(CLEAR_n), .REFRQ_n(REFRQ_n), .ISEMRQ_n(ISEMRQ_n), .IBINPUT_n(IBINPUT_n), .IBPERR_n(IBPERR_n),
    .MOFF_n(MOFF_n), .CBWRITE_n(CBWRITE_n), .IBDRY_n(IBDRY_n), .IBREQ_n(IBREQ_n), .SSEMA_n(SSEMA_n),
    .IBDAP_n(IBDAP_n), .PD3(PD3), .PD1(PD1), .CC2_n(CC2_n), .CGNT_n(CGNT_n), .CGNT50_n(CGNT50_n),
    .TERM_n(TERM_n), .DBAPR(DBAPR), .MOR25_n(MOR25_n), .LPERR_n(LPRERR_n), .LERR_n(LERR_n), .PS_n(PS_n),
    .PA_n(PA_n), .OUTIDENT_n(OUTIDENT_n), .BIOXE_n(BIOXE_n), .BINACK_n(BINACK_n), .SEMRQ50_n(SEMRQ50_n),
    .IOXERR_n(IOXERR_n), .MR_n(MR_n), .MOR_n(MOR_n), .BERROR_n(BERROR_n), .BDRY_n(BDRY_n),
    .OUTGRANT_n(OUTGRANT_n), .BDAP_n(BDAP_n), .BMEM_n(BMEM_n), .BINPUT_n(BINPUT_n),
    .BINPUT50_n(BCTL_binput50_n), .BREF_n(BREF_n), .BDRY50_n(BDRY50_n), .BAPR_n(BAPR_n), .SEMRQ_n(SEMRQ_n),
    .REF_n(REF_n), .BDAP50_n(BDAP50_n), .GNT_n(GNT_n), .IOD_n(BCTL_iod_n), .CACT_n(BCTL_cact_n),
    .BDRY25_n(BCTL_bdry25_n), .Q_2_0_n(BCTL_q_2_0_n), .DAP_n(DAP_n), .EADR_n(BCTL_eadr_n), .SPEA(BCTL_spea),
    .SPES(BCTL_spes), .PARERR_n(PARERR_n), .RERR_n(RERR_n), .EPES_n(BCTL_epes_n), .EPEA_n(BCTL_epea_n));
  BIF_DPATH_9 DPATH (
    .PPN_23_10(PPN_23_10), .CA_9_0(CA_9_0), .ECREQ(ECRQ), .FETCH(FETCH), .SPES(BCTL_spes),
    .EPES_n(BCTL_epes_n), .SPEA(BCTL_spea), .EPEA_n(BCTL_epea_n), .Q0_n(BCTL_q_2_0_n[0]),
    .Q2_n(BCTL_q_2_0_n[2]), .CC2_n(CC2_n), .BDRY25_n(BCTL_bdry25_n), .BDRY50_n(BDRY50_n), .CGNT_n(CGNT_n),
    .CGNT50_n(CGNT50_n), .CACT_n(BCTL_cact_n), .TERM_n(TERM_n), .BGNT_n(BGNT_n), .RT_n(RT_n),
    .IORQ_n(IORQ_n), .PD3(PD3), .EADDR_n(BCTL_eadr_n), .BINPUT50_n(BCTL_binput50_n), .MIS0(MIS0),
    .IOD_n(BCTL_iod_n), .WRITE(WRITE), .PD1(PD1), .BGNT50_n(BGNT50_n), .MWRITE_n(MWRITE_n),
    .BDAP50_n(BDAP50_n), .EBUS_n(EBUS_n), .IBAPR_n(IBAPR_n), .GNT_n(GNT_n), .LBD_23_0_io(LBD_23_0_io),
    .CD_15_0_io(CD_15_0_io), .BD_23_0_n_io(BD_23_0_n_io), .IDB_15_0(IDB_15_0), .CGNTCACT_n(CGNCACT_n),
    .CBWRITE_n(CBWRITE_n), .DBAPR(DBAPR));

  // Notes on the sheet:
  //   BIF/BCTL
  //   ND120 CPU, MM&M
  //   BUS INTERFACE
  //   SHEET 5 of 50
  //   BIF100I (GROUP)
  //   BIF100O(GROUP OUT)
endmodule

module BIF_BCTL_6 (
  input  MIS0,
  input  TOUT,
  input  OSC,
  input  CRQ_n,
  input  GNT50_n,
  input  IORQ_n,
  input  CLEAR_n,
  input  REFRQ_n,
  input  ISEMRQ_n,
  input  IBINPUT_n,
  input  IBPERR_n,
  input  MOFF_n,
  input  CBWRITE_n,
  input  IBDRY_n,
  input  IBREQ_n,
  input  SSEMA_n,
  input  IBDAP_n,
  input  PD3,
  input  PD1,
  input  CC2_n,
  input  CGNT_n,
  input  CGNT50_n,
  input  TERM_n,
  input  DBAPR,
  input  MOR25_n,
  input  LPERR_n,
  input  LERR_n,
  input  PS_n,
  input  PA_n,
  output OUTIDENT_n,
  output BIOXE_n,
  output BINACK_n,
  output SEMRQ50_n,
  output IOXERR_n,
  output MR_n,
  output MOR_n,
  output BERROR_n,
  output BDRY_n,
  output OUTGRANT_n,
  output BDAP_n,
  output BMEM_n,
  output BINPUT_n,
  output BINPUT50_n,
  output BREF_n,
  output BDRY50_n,
  output BAPR_n,
  output SEMRQ_n,
  output REF_n,
  output BDAP50_n,
  output GNT_n,
  output IOD_n,
  output CACT_n,
  output BDRY25_n,
  output [2:0] Q_2_0_n,
  output DAP_n,
  output EADR_n,
  output SPEA,
  output SPES,
  output PARERR_n,
  output RERR_n,
  output EPES_n,
  output EPEA_n
);

  wire BINPUT75_n, BLOCK_n, PAL_44401_UBTIM_b0_n, PAL_44401_UBTIM_b2_n, PAL_44801_UBARB_q0_n,
       PAL_44801_UBARB_q1_n, PAL_44801_UBARB_q2_n, PAL_44801_UBARB_q3_n, PAL_45001_UBPAR_b3_n,
       PAL_45001_UBPAR_b4_n, PAL_45001_UBPAR_b5_n, SYNC_bdry25_n, SYNC_bdry75_n, SYNC_block25_n,
       SYNC_bperr50_n, SYNC_breq50_n, SYNC_refrq50_n;

  BIF_BCTL_SYNC_8 SYNC (
    .OSC(OSC), .CLEAR_n(CLEAR_n), .REFRQ_n(REFRQ_n), .ISEMRQ_n(ISEMRQ_n), .IBINPUT_n(IBINPUT_n),
    .IBPERR_n(IBPERR_n), .IBDRY_n(IBDRY_n), .CACT_n(CACT_n), .IBREQ_n(IBREQ_n), .IBDAP_n(IBDAP_n),
    .BLOCK_n(BLOCK_n), .PD3(PD3), .PD1(PD1), .MR_n(MR_n), .REFRQ50_n(SYNC_refrq50_n), .SEMRQ50_n(SEMRQ50_n),
    .BINPUT50_n(BINPUT50_n), .BPERR50_n(SYNC_bperr50_n), .BDRY50_n(BDRY50_n), .BDRY75_n(SYNC_bdry75_n),
    .CACT25_n(BDRY25_n), .BREQ50_n(SYNC_breq50_n), .BDAP50_n(BDAP50_n), .BINPUT75_n(BINPUT75_n),
    .BLOCK25_n(SYNC_block25_n), .BDRY25_n(SYNC_bdry25_n));
  nand nand_1 (EPES_n, ~PS_n, ~RERR_n);  // NAND_Gate
  nand nand_2 (EPEA_n, ~PA_n, ~RERR_n);  // NAND_Gate
  PAL_16R8D PAL_44801_UBARB (
    .CK(OSC), .I0(CRQ_n), .I1(IORQ_n), .I2(MR_n), .I3(SYNC_breq50_n), .I4(SYNC_refrq50_n),
    .I5(SYNC_bdry25_n), .I6(SEMRQ50_n), .I7(MOFF_n), .OE_n(PD3), .Q0_n(PAL_44801_UBARB_q0_n),
    .Q1_n(PAL_44801_UBARB_q1_n), .Q2_n(PAL_44801_UBARB_q2_n), .Q3_n(PAL_44801_UBARB_q3_n), .Q4_n(REF_n),
    .Q5_n(IOD_n), .Q6_n(GNT_n), .Q7_n(CACT_n));
  PAL_16R4D PAL_44401_UBTIM (
    .CK(OSC), .I0(CC2_n), .I1(CACT_n), .I2(BDRY25_n), .I3(BDRY50_n), .I4(CGNT_n), .I5(CGNT50_n), .I6(TERM_n),
    .I7(IORQ_n), .OE_n(PD1), .Q0_n(Q_2_0_n[0]), .Q1_n(Q_2_0_n[1]), .Q2_n(Q_2_0_n[2]),
    .B0_n(PAL_44401_UBTIM_b0_n), .B1_n(DAP_n), .B2_n(PAL_44401_UBTIM_b2_n), .B3_n(EADR_n));  // open: Q3_n
  PAL_16L8_12 PAL_45001_UBPAR (
    .I0(BDRY50_n), .I1(SYNC_bdry75_n), .I2(SYNC_block25_n), .I3(SYNC_bperr50_n), .I4(DBAPR), .I5(MOR25_n),
    .I6(LPERR_n), .I7(MR_n), .I8(EPES_n), .I9(EPEA_n), .Y0_n(SPEA), .Y1_n(SPES), .B0_n(BLOCK_n),
    .B1_n(PARERR_n), .B2_n(RERR_n), .B3_n(PAL_45001_UBPAR_b3_n), .B4_n(PAL_45001_UBPAR_b4_n),
    .B5_n(PAL_45001_UBPAR_b5_n));
  BIF_BCTL_BDRV_7 BDRV (
    .MIS0(MIS0), .BINPUT75_n(BINPUT75_n), .EIOD_n(PAL_44401_UBTIM_b2_n), .TOUT(TOUT),
    .BDRY25_n(SYNC_bdry25_n), .SEM_n(PAL_44801_UBARB_q0_n), .GNT50_n(GNT50_n), .DAP_n(DAP_n),
    .BDRY50_n(BDRY50_n), .IBDRY_n(IBDRY_n), .IBREQ_n(IBREQ_n), .IOD_n(IOD_n), .MEM_n(PAL_44801_UBARB_q3_n),
    .CBWRITE_n(CBWRITE_n), .REF_n(REF_n), .APR_n(PAL_44401_UBTIM_b0_n), .SSEMA_n(SSEMA_n), .CACT_n(CACT_n),
    .OUTIDENT_n(OUTIDENT_n), .BIOXE_n(BIOXE_n), .BINACK_n(BINACK_n), .IOXERR_n(IOXERR_n), .MOR_n(MOR_n),
    .BERROR_n(BERROR_n), .BDRY_n(BDRY_n), .OUTGRANT_n(OUTGRANT_n), .BDAP_n(BDAP_n), .BMEM_n(BMEM_n),
    .BINPUT_n(BINPUT_n), .BREF_n(BREF_n), .BAPR_n(BAPR_n), .SEMRQ_n(SEMRQ_n));

  // Notes on the sheet:
  //   BIF/BCTL
  //   BIF CONTROL
  //   SHEET 6 of 50
  //   ND120 CPU, MM&M
  //   The signals needs to be connected in Verilog
  //   EPES_n
  //   EPEA_n
  //   IOREQ_n
  //   MR_n
  //   BREQ50_n
  //   REFRQ50_n
  //   BDRY25_n
  //   CACT_n
  //   CACT25_n
  //   BDRY50_n
  //   BDRY50_n
  //   BDRY75_n
  //   IOREQ_n
  //   The signals needs to be connected in Verilog
  //   SEM_n
  //   ACT_n
  //   DOREF_n
  //   MEM_n
  //   REF_n
  //   IOD_n
  //   GNT_n
  //   CACT_n
  //   n.c.
  //   n.c.
  //   n.c.
  //   APN_n
  //   DAP_n
  //   EIOD_n
  //   n.c.
endmodule

module BIF_BCTL_BDRV_7 (
  input  MIS0,
  input  BINPUT75_n,
  input  EIOD_n,
  input  TOUT,
  input  BDRY25_n,
  input  SEM_n,
  input  GNT50_n,
  input  DAP_n,
  input  BDRY50_n,
  input  IBDRY_n,
  input  IBREQ_n,
  input  IOD_n,
  input  MEM_n,
  input  CBWRITE_n,
  input  REF_n,
  input  APR_n,
  input  SSEMA_n,
  input  CACT_n,
  output OUTIDENT_n,
  output BIOXE_n,
  output BINACK_n,
  output IOXERR_n,
  output MOR_n,
  output BERROR_n,
  output BDRY_n,
  output OUTGRANT_n,
  output BDAP_n,
  output BMEM_n,
  output BINPUT_n,
  output BREF_n,
  output BAPR_n,
  output SEMRQ_n
);

  wire and_1_out, nand_1_out, nand_2_out, not_1_out, not_2_out, not_3_out, not_4_out, or_1_out, or_2_out;

  not not_1 (not_1_out, MIS0);
  not not_2 (not_2_out, IBREQ_n);
  nand nand_1 (nand_1_out, not_2_out, IOD_n);
  not not_3 (not_3_out, DAP_n);
  or or_1 (or_1_out, ~nand_1_out, ~MEM_n);  // OR_Gate
  buf buffer_1 (BINPUT_n, CBWRITE_n);
  buf buffer_2 (BREF_n, REF_n);
  buf buffer_3 (BAPR_n, APR_n);
  and and_1 (and_1_out, ~SSEMA_n, ~CACT_n);  // AND_Gate
  nand nand_2 (nand_2_out, BDRY25_n, BDRY50_n);
  nand nand_3 (BDAP_n, not_3_out, BDRY50_n);
  nand nand_4 (BMEM_n, IBDRY_n, or_1_out);
  TTL_74241 CHIP_3A (
    .I0_1A1(MIS0), .I1_1A2(not_1_out), .I2_1A3(BINPUT75_n), .OE1_1G_n(EIOD_n), .I4_2A1(IOD_n),
    .I5_2A2(MEM_n), .I6_2A3(1'b0), .I7_2A4(BERROR_n), .OE2_2G(TOUT), .O0_1Y1(OUTIDENT_n), .O1_1Y2(BIOXE_n),
    .O2_1Y3(BINACK_n), .O4_2Y1(IOXERR_n), .O5_2Y2(MOR_n), .O6_2Y3(BERROR_n), .O7_2Y4(BDRY_n));  // open: I3_1A4, O3_1Y4
  or or_2 (or_2_out, ~nand_2_out, ~SEM_n);  // OR_Gate
  not not_4 (not_4_out, GNT50_n);
  nand nand_5 (SEMRQ_n, CBWRITE_n, and_1_out);
  nand nand_6 (OUTGRANT_n, or_2_out, not_4_out);

  // Notes on the sheet:
  //   OUTIDENT_n: pull=up
  //   IOXERR_n: pull=up
  //   MOR_n: pull=up
  //   ND120 CPU, MM&M
  //   BIF/BCTL/BDRV
  //   BUS DRIVERS
  //   SHEET 7 of 50
  //   IOD_n
  //   n.c.
endmodule

module BIF_BCTL_SYNC_8 (
  input  OSC,
  input  CLEAR_n,
  input  REFRQ_n,
  input  ISEMRQ_n,
  input  IBINPUT_n,
  input  IBPERR_n,
  input  IBDRY_n,
  input  CACT_n,
  input  IBREQ_n,
  input  IBDAP_n,
  input  BLOCK_n,
  input  PD3,
  input  PD1,
  output MR_n,
  output REFRQ50_n,
  output SEMRQ50_n,
  output BINPUT50_n,
  output BPERR50_n,
  output BDRY50_n,
  output BDRY75_n,
  output CACT25_n,
  output BREQ50_n,
  output BDAP50_n,
  output BINPUT75_n,
  output BLOCK25_n,
  output BDRY25_n
);

  wire CHIP_3D_y0, CHIP_3D_y1, CHIP_3D_y2, CHIP_3D_y3, CHIP_3D_y4, CHIP_3D_y7, CHIP_3D_y8;

  AM29C821 CHIP_3D (
    .CK(OSC), .D0(CLEAR_n), .D1(REFRQ_n), .D2(ISEMRQ_n), .D3(IBINPUT_n), .D4(IBPERR_n), .D5(IBDRY_n),
    .D6(CACT_n), .D7(IBREQ_n), .D8(IBDAP_n), .D9(BLOCK_n), .OE_n(PD3), .Y0(CHIP_3D_y0), .Y1(CHIP_3D_y1),
    .Y2(CHIP_3D_y2), .Y3(CHIP_3D_y3), .Y4(CHIP_3D_y4), .Y5(BDRY25_n), .Y6(CACT25_n), .Y7(CHIP_3D_y7),
    .Y8(CHIP_3D_y8), .Y9(BLOCK25_n));
  AM29C821 CHIP_4D (
    .CK(OSC), .D0(CHIP_3D_y0), .D1(CHIP_3D_y1), .D2(CHIP_3D_y2), .D3(CHIP_3D_y3), .D4(CHIP_3D_y4),
    .D5(BDRY25_n), .D6(BDRY50_n), .D7(CHIP_3D_y7), .D8(CHIP_3D_y8), .D9(BINPUT50_n), .OE_n(PD1), .Y0(MR_n),
    .Y1(REFRQ50_n), .Y2(SEMRQ50_n), .Y3(BINPUT50_n), .Y4(BPERR50_n), .Y5(BDRY50_n), .Y6(BDRY75_n),
    .Y7(BREQ50_n), .Y8(BDAP50_n), .Y9(BINPUT75_n));

  // Notes on the sheet:
  //   ND120 CPU, MM&M
  //   BIF/BCTL/SYNC
  //   BIF SYNC
  //   SHEET 8 of 50
  //   CLEAR25_n
  //   REFRQ25_n
  //   SEMRQ25_n
  //   BINPUT25_n
  //   BPERR25_n
  //   BDRY25_n
  //   BREQ25_n
  //   BDAP25_n
endmodule

module BIF_DPATH_9 (
  input  [13:0] PPN_23_10,
  input  [9:0] CA_9_0,
  input  ECREQ,
  input  FETCH,
  input  SPES,
  input  EPES_n,
  input  SPEA,
  input  EPEA_n,
  input  Q0_n,
  input  Q2_n,
  input  CC2_n,
  input  BDRY25_n,
  input  BDRY50_n,
  input  CGNT_n,
  input  CGNT50_n,
  input  CACT_n,
  input  TERM_n,
  input  BGNT_n,
  input  RT_n,
  input  IORQ_n,
  input  PD3,
  input  EADDR_n,
  input  BINPUT50_n,
  input  MIS0,
  input  IOD_n,
  input  WRITE,
  input  PD1,
  input  BGNT50_n,
  input  MWRITE_n,
  input  BDAP50_n,
  input  EBUS_n,
  input  IBAPR_n,
  input  GNT_n,
  output [23:0] LBD_23_0_io,
  output [15:0] CD_15_0_io,
  output [23:0] BD_23_0_n_io,
  output [15:0] IDB_15_0,
  output CGNTCACT_n,
  output CBWRITE_n,
  output DBAPR
);

  wire LDBCTL_bgntcact, LDBCTL_clkbd, LDBCTL_dstb_n, LDBCTL_ebadr, LDBCTL_ebd_n, LDBCTL_emd_n, LDBCTL_wbd_n,
       LDBCTL_wlbd_n;
  wire [23:0] PPNLBD_lbd_23_0;

  BIF_DPATH_LDBCTL_12 LDBCTL (
    .Q0_n(Q0_n), .Q2_n(Q2_n), .CC2_n(CC2_n), .BDRY25_n(BDRY25_n), .BDRY50_n(BDRY50_n), .CGNT_n(CGNT_n),
    .CGNT50_n(CGNT50_n), .CACT_n(CACT_n), .TERM_n(TERM_n), .BGNT_n(BGNT_n), .RT_n(RT_n), .IORQ_n(IORQ_n),
    .PD3(PD3), .EADR_n(EADDR_n), .BINPUT50_n(BINPUT50_n), .MIS0(MIS0), .IOD_n(IOD_n), .WRITE(WRITE),
    .PD1(PD1), .BGNT50_n(BGNT50_n), .MWRITE_n(MWRITE_n), .BDAP50_n(BDAP50_n), .EBUS_n(EBUS_n),
    .IBAPR_n(IBAPR_n), .GNT_n(GNT_n), .BGNTCACT(LDBCTL_bgntcact), .CGNTCACT_n(CGNTCACT_n),
    .EMD_n(LDBCTL_emd_n), .DSTB_n(LDBCTL_dstb_n), .WBD_n(LDBCTL_wbd_n), .WLBD_n(LDBCTL_wlbd_n),
    .CBWRITE_n(CBWRITE_n), .DBAPR(DBAPR), .EBADR(LDBCTL_ebadr), .CLKBD(LDBCTL_clkbd), .EBD_n(LDBCTL_ebd_n));
  BIF_DPATH_PPNLBD_14 PPNLBD (
    .PPN_23_10(PPN_23_10), .CA_9_0(CA_9_0), .ECREQ(ECREQ), .EADR_n(EADDR_n), .LBD_23_0(PPNLBD_lbd_23_0));
  BIF_DPATH_CDLBD_11 CDLBD (
    .EMD_n(LDBCTL_emd_n), .ECREQ(ECREQ), .DSTB_n(LDBCTL_dstb_n), .WLBD_n(LDBCTL_wlbd_n),
    .LBD_15_0_io(PPNLBD_lbd_23_0[15:0]), .CD_15_0_io(CD_15_0_io));
  BIF_DPATH_BDLBD_10 BDLBD (
    .EBD_n(LDBCTL_ebd_n), .WBD_n(LDBCTL_wbd_n), .BGNT_n(BGNT_n), .BGNTCACT_n(LDBCTL_bgntcact),
    .CLKBD(LDBCTL_clkbd), .EBADR(LDBCTL_ebadr), .BD_23_0_n_io(BD_23_0_n_io), .LBD_23_0_io(LBD_23_0_io));
  BIF_DPATH_PESPEA_13 PESPEA (
    .FETCH(FETCH), .GNT_n(GNT_n), .SPES(SPES), .EPES_n(EPES_n), .SPEA(SPEA), .EPEA_n(EPEA_n),
    .BD_23_0_n(BD_23_0_n_io), .IDB_15_0(IDB_15_0));

  // Notes on the sheet:
  //   ND120 CPU, MM&M
  //   BIF/DPATH
  //   BIF DATA PATH
  //   SHEET 9 of 50
  //   n.c
  //   Add gate here ? The signals needs to be connected in Verilog
endmodule

module BIF_DPATH_BDLBD_10 (
  input  EBD_n,
  input  WBD_n,
  input  BGNT_n,
  input  BGNTCACT_n,
  input  CLKBD,
  input  EBADR,
  input  [23:0] BD_23_0_n_io,
  output [23:0] LBD_23_0_io
);

  TTL_74648 CHIP_4A (
    .OE_n(EBD_n), .DIR(WBD_n), .CLKBA(BGNT_n), .SBA(BGNTCACT_n), .CLKAB(CLKBD), .SAB(EBADR),
    .A1(BD_23_0_n_io[23]), .A2(BD_23_0_n_io[22]), .A3(BD_23_0_n_io[21]), .A4(BD_23_0_n_io[20]),
    .A5(BD_23_0_n_io[19]), .A6(BD_23_0_n_io[18]), .A7(BD_23_0_n_io[17]), .A8(BD_23_0_n_io[16]),
    .B1_n(LBD_23_0_io[23]), .B2_n(LBD_23_0_io[22]), .B3_n(LBD_23_0_io[21]), .B4_n(LBD_23_0_io[20]),
    .B5_n(LBD_23_0_io[19]), .B6_n(LBD_23_0_io[18]), .B7_n(LBD_23_0_io[17]), .B8_n(LBD_23_0_io[16]));
  TTL_74648 CHIP_5A (
    .OE_n(EBD_n), .DIR(WBD_n), .CLKBA(BGNT_n), .SBA(BGNTCACT_n), .CLKAB(CLKBD), .SAB(EBADR),
    .A1(BD_23_0_n_io[15]), .A2(BD_23_0_n_io[14]), .A3(BD_23_0_n_io[13]), .A4(BD_23_0_n_io[12]),
    .A5(BD_23_0_n_io[11]), .A6(BD_23_0_n_io[10]), .A7(BD_23_0_n_io[9]), .A8(BD_23_0_n_io[8]),
    .B1_n(LBD_23_0_io[15]), .B2_n(LBD_23_0_io[14]), .B3_n(LBD_23_0_io[13]), .B4_n(LBD_23_0_io[12]),
    .B5_n(LBD_23_0_io[11]), .B6_n(LBD_23_0_io[10]), .B7_n(LBD_23_0_io[9]), .B8_n(LBD_23_0_io[8]));
  TTL_74648 CHIP_6A (
    .OE_n(EBD_n), .DIR(WBD_n), .CLKBA(BGNT_n), .SBA(BGNTCACT_n), .CLKAB(CLKBD), .SAB(EBADR),
    .A1(BD_23_0_n_io[7]), .A2(BD_23_0_n_io[6]), .A3(BD_23_0_n_io[5]), .A4(BD_23_0_n_io[4]),
    .A5(BD_23_0_n_io[3]), .A6(BD_23_0_n_io[2]), .A7(BD_23_0_n_io[1]), .A8(BD_23_0_n_io[0]),
    .B1_n(LBD_23_0_io[7]), .B2_n(LBD_23_0_io[6]), .B3_n(LBD_23_0_io[5]), .B4_n(LBD_23_0_io[4]),
    .B5_n(LBD_23_0_io[3]), .B6_n(LBD_23_0_io[2]), .B7_n(LBD_23_0_io[1]), .B8_n(LBD_23_0_io[0]));

  // Notes on the sheet:
  //   LBD_23_0_io: pull=up
  //   ND120 CPU, MM&M
  //   BIF/DPATH/BDLBD
  //   BIF BD TO LDB
  //   SHEET 10 of 50
  //   LBD23
  //   LBD16
  //   LBD15
  //   LBD8
  //   LBD7
  //   LBD0
endmodule

module BIF_DPATH_CDLBD_11 (
  input  EMD_n,
  input  ECREQ,
  input  DSTB_n,
  input  WLBD_n,
  input  [15:0] LBD_15_0_io,
  output [15:0] CD_15_0_io
);

  TTL_74646 CHIP_7B (
    .OE_n(EMD_n), .DIR(WLBD_n), .CLKBA(ECREQ), .SBA(1'b1), .CLKAB(DSTB_n), .SAB(DSTB_n),
    .A1(LBD_15_0_io[15]), .A2(LBD_15_0_io[14]), .A3(LBD_15_0_io[13]), .A4(LBD_15_0_io[12]),
    .A5(LBD_15_0_io[11]), .A6(LBD_15_0_io[10]), .A7(LBD_15_0_io[9]), .A8(LBD_15_0_io[8]),
    .B1(CD_15_0_io[15]), .B2(CD_15_0_io[14]), .B3(CD_15_0_io[13]), .B4(CD_15_0_io[12]), .B5(CD_15_0_io[11]),
    .B6(CD_15_0_io[10]), .B7(CD_15_0_io[9]), .B8(CD_15_0_io[8]));
  TTL_74646 CHIP_6B (
    .OE_n(EMD_n), .DIR(WLBD_n), .CLKBA(ECREQ), .SBA(1'b1), .CLKAB(DSTB_n), .SAB(DSTB_n), .A1(LBD_15_0_io[7]),
    .A2(LBD_15_0_io[6]), .A3(LBD_15_0_io[5]), .A4(LBD_15_0_io[4]), .A5(LBD_15_0_io[3]), .A6(LBD_15_0_io[2]),
    .A7(LBD_15_0_io[1]), .A8(LBD_15_0_io[0]), .B1(CD_15_0_io[7]), .B2(CD_15_0_io[6]), .B3(CD_15_0_io[5]),
    .B4(CD_15_0_io[4]), .B5(CD_15_0_io[3]), .B6(CD_15_0_io[2]), .B7(CD_15_0_io[1]), .B8(CD_15_0_io[0]));

  // Notes on the sheet:
  //   CD_15_0_io: pull=up
  //   ND120 CPU, MM&M
  //   BIF/DPATH/CDLBD
  //   BIF CD TO LBD
  //   SHEET 11 of 50
  //   PULLUP via Resistor
endmodule

module BIF_DPATH_LDBCTL_12 (
  input  Q0_n,
  input  Q2_n,
  input  CC2_n,
  input  BDRY25_n,
  input  BDRY50_n,
  input  CGNT_n,
  input  CGNT50_n,
  input  CACT_n,
  input  TERM_n,
  input  BGNT_n,
  input  RT_n,
  input  IORQ_n,
  input  PD3,
  input  EADR_n,
  input  BINPUT50_n,
  input  MIS0,
  input  IOD_n,
  input  WRITE,
  input  PD1,
  input  BGNT50_n,
  input  MWRITE_n,
  input  BDAP50_n,
  input  EBUS_n,
  input  IBAPR_n,
  input  GNT_n,
  output BGNTCACT,
  output CGNTCACT_n,
  output EMD_n,
  output DSTB_n,
  output WBD_n,
  output WLBD_n,
  output CBWRITE_n,
  output DBAPR,
  output EBADR,
  output CLKBD,
  output EBD_n
);

  wire CMWRITE_n, FAPR, PAL_44302_ULBC1_b3_n, PAL_44302_ULBC1_b4_n, PAL_44302_ULBC1_b5_n,
       PAL_44304_ULBC3_b0_n, SAPR;

  PAL_16L8_12 PAL_44302_ULBC1 (
    .I0(Q0_n), .I1(Q2_n), .I2(CC2_n), .I3(BDRY25_n), .I4(BDRY50_n), .I5(CGNT_n), .I6(CGNT50_n), .I7(CACT_n),
    .I8(TERM_n), .I9(BGNT_n), .Y0_n(BGNTCACT), .Y1_n(CGNTCACT_n), .B0_n(EMD_n), .B1_n(DSTB_n),
    .B3_n(PAL_44302_ULBC1_b3_n), .B4_n(PAL_44302_ULBC1_b4_n), .B5_n(PAL_44302_ULBC1_b5_n));  // open: B2_n
  PAL_16L8_12 PAL_44304_ULBC3 (
    .I0(CGNT_n), .I1(BGNT_n), .I2(BGNT50_n), .I3(MWRITE_n), .I4(BDAP50_n), .I5(EBUS_n), .I6(IBAPR_n),
    .I7(GNT_n), .I8(PD3), .Y0_n(DBAPR), .B0_n(PAL_44304_ULBC3_b0_n), .B1_n(EBADR), .B2_n(FAPR), .B3_n(SAPR),
    .B4_n(CLKBD), .B5_n(EBD_n));  // open: I9, Y1_n
  PAL_16L8_12 PAL_44303_ULBC2 (
    .I0(CACT_n), .I1(CGNT_n), .I2(EADR_n), .I3(BINPUT50_n), .I4(MIS0), .I5(IOD_n), .I6(WRITE), .I7(PD1),
    .I9(PAL_44304_ULBC3_b0_n), .Y0_n(WBD_n), .Y1_n(WLBD_n), .B0_n(CBWRITE_n), .B1_n(CMWRITE_n));  // open: I8, B2_n, B3_n, B4_n, B5_n

  // Notes on the sheet:
  //   ND120 CPU, MM&M
  //   BIF/DPATH/LBDCTL
  //   LBD CONTROL
  //   SHEET 12 of 50
  //   PD3 => TEST in PAL
  //   CGNT_n
  //   BGNT_n
  //   PD3
  //   CONNECT SIGNALS B3_n, B4_n and B5_n in Verilog
  //   BACT_n
  //   CACT_n
  //   CGNT_n
endmodule

module BIF_DPATH_PESPEA_13 (
  input  FETCH,
  input  GNT_n,
  input  SPES,
  input  EPES_n,
  input  SPEA,
  input  EPEA_n,
  input  [23:0] BD_23_0_n,
  output [15:0] IDB_15_0
);

  wire not_1_out;
  wire [7:0] CHIP_10A_q8_n, CHIP_12A_q8_n;

  not not_1 (not_1_out, FETCH);
  TTL_74534 CHIP_12A (
    .D1(not_1_out), .D2(GNT_n), .D3(BD_23_0_n[21]), .D4(BD_23_0_n[20]), .D5(BD_23_0_n[19]),
    .D6(BD_23_0_n[18]), .D7(BD_23_0_n[17]), .D8(BD_23_0_n[16]), .CK(SPES), .OE_n(EPES_n),
    .Q1_n(CHIP_12A_q8_n[7]), .Q2_n(CHIP_12A_q8_n[6]), .Q3_n(CHIP_12A_q8_n[5]), .Q4_n(CHIP_12A_q8_n[4]),
    .Q5_n(CHIP_12A_q8_n[3]), .Q6_n(CHIP_12A_q8_n[2]), .Q7_n(CHIP_12A_q8_n[1]), .Q8_n(CHIP_12A_q8_n[0]));
  TTL_74534 CHIP_10A (
    .D1(BD_23_0_n[23]), .D2(BD_23_0_n[22]), .D3(BD_23_0_n[21]), .D4(BD_23_0_n[20]), .D5(BD_23_0_n[19]),
    .D6(BD_23_0_n[18]), .D7(BD_23_0_n[17]), .D8(BD_23_0_n[16]), .CK(SPEA), .OE_n(EPES_n),
    .Q1_n(CHIP_10A_q8_n[7]), .Q2_n(CHIP_10A_q8_n[6]), .Q3_n(CHIP_10A_q8_n[5]), .Q4_n(CHIP_10A_q8_n[4]),
    .Q5_n(CHIP_10A_q8_n[3]), .Q6_n(CHIP_10A_q8_n[2]), .Q7_n(CHIP_10A_q8_n[1]), .Q8_n(CHIP_10A_q8_n[0]));
  // Probe on {CHIP_12A_q8_n, CHIP_10A_q8_n}
  Controlled_Buffer #(.width(16)) controlled_buffer_1 (.in({CHIP_12A_q8_n, CHIP_10A_q8_n}), .en(EPEA_n));  // open: out
  // Probe on IDB_15_0
  TTL_74534 CHIP_9A (
    .D1(BD_23_0_n[15]), .D2(BD_23_0_n[14]), .D3(BD_23_0_n[13]), .D4(BD_23_0_n[12]), .D5(BD_23_0_n[11]),
    .D6(BD_23_0_n[10]), .D7(BD_23_0_n[9]), .D8(BD_23_0_n[8]), .CK(SPEA), .OE_n(EPEA_n), .Q1_n(IDB_15_0[15]),
    .Q2_n(IDB_15_0[14]), .Q3_n(IDB_15_0[13]), .Q4_n(IDB_15_0[12]), .Q5_n(IDB_15_0[11]), .Q6_n(IDB_15_0[10]),
    .Q7_n(IDB_15_0[9]), .Q8_n(IDB_15_0[8]));
  TTL_74534 CHIP_8A (
    .D1(BD_23_0_n[7]), .D2(BD_23_0_n[6]), .D3(BD_23_0_n[5]), .D4(BD_23_0_n[4]), .D5(BD_23_0_n[3]),
    .D6(BD_23_0_n[2]), .D7(BD_23_0_n[1]), .D8(BD_23_0_n[0]), .CK(SPEA), .OE_n(EPEA_n), .Q1_n(IDB_15_0[7]),
    .Q2_n(IDB_15_0[6]), .Q3_n(IDB_15_0[5]), .Q4_n(IDB_15_0[4]), .Q5_n(IDB_15_0[3]), .Q6_n(IDB_15_0[2]),
    .Q7_n(IDB_15_0[1]), .Q8_n(IDB_15_0[0]));

  // Notes on the sheet:
  //   ND120 CPU, MM&M
  //   BIF/DPATH/PESPEA
  //   BIF PES & PEA
  //   SHEET 13 of 50
  //   BD21_n
  //   BD16_n
  //   BD23_n
  //   BD16_n
  //   IDB15
  //   IDB8
  //   IDB7
  //   IDB0
  //   Added gate here, but the signals needs to be connected in Verilog
  //   BD15_n
  //   BD8_n
  //   IDB15
  //   IDB8
  //   IDB7
  //   IDB0
endmodule

module BIF_DPATH_PPNLBD_14 (
  input  [13:0] PPN_23_10,
  input  [9:0] CA_9_0,
  input  ECREQ,
  input  EADR_n,
  output [23:0] LBD_23_0
);

  TTL_74374 CHIP_3B (
    .D1(PPN_23_10[13]), .D2(PPN_23_10[12]), .D3(PPN_23_10[11]), .D4(PPN_23_10[10]), .D5(PPN_23_10[9]),
    .D6(PPN_23_10[8]), .D7(PPN_23_10[7]), .D8(PPN_23_10[6]), .CK(ECREQ), .OE_n(EADR_n), .Q1(LBD_23_0[23]),
    .Q2(LBD_23_0[22]), .Q3(LBD_23_0[21]), .Q4(LBD_23_0[20]), .Q5(LBD_23_0[19]), .Q6(LBD_23_0[18]),
    .Q7(LBD_23_0[17]), .Q8(LBD_23_0[16]));
  TTL_74374 CHIP_4B (
    .D1(PPN_23_10[5]), .D2(PPN_23_10[4]), .D3(PPN_23_10[3]), .D4(PPN_23_10[2]), .D5(PPN_23_10[1]),
    .D6(PPN_23_10[0]), .D7(CA_9_0[9]), .D8(CA_9_0[8]), .CK(ECREQ), .OE_n(EADR_n), .Q1(LBD_23_0[15]),
    .Q2(LBD_23_0[14]), .Q3(LBD_23_0[13]), .Q4(LBD_23_0[12]), .Q5(LBD_23_0[11]), .Q6(LBD_23_0[10]),
    .Q7(LBD_23_0[9]), .Q8(LBD_23_0[8]));
  TTL_74374 CHIP_6C (
    .D1(CA_9_0[7]), .D2(CA_9_0[6]), .D3(CA_9_0[5]), .D4(CA_9_0[4]), .D5(CA_9_0[3]), .D6(CA_9_0[2]),
    .D7(CA_9_0[1]), .D8(CA_9_0[0]), .CK(ECREQ), .OE_n(EADR_n), .Q1(LBD_23_0[7]), .Q2(LBD_23_0[6]),
    .Q3(LBD_23_0[5]), .Q4(LBD_23_0[4]), .Q5(LBD_23_0[3]), .Q6(LBD_23_0[2]), .Q7(LBD_23_0[1]), .Q8(LBD_23_0[0]));

  // Notes on the sheet:
  //   ND120 CPU, MM&M
  //   BIF/DPATH/PPNLBD
  //   BIF PPN TO LBD
  //   SHEET 14 of 50
  //   PPN23
  //   PPN16
  //   PPN15
  //   PPN10
  //   CA9
  //   CA8
  //   CA7
  //   CA0
  //   LBD23
  //   LBD16
  //   LBD15
  //   LBD8
  //   LBD7
  //   LBD0
endmodule

module CPU_15_Verilog (
);


  // Notes on the sheet:
  //   ND120 CPU, MM&M
  //   CPU
  //   CPU TOP LEVEL
  //   SHEET 15 of 50
  //   NEED TO DONE IN VERILOG
endmodule

module CPU_CS_16 (
  input  BLCS_n,
  input  [1:0] RF_1_0,
  input  [12:0] CSA_12_0,
  input  [9:0] CSCA_9_0,
  input  CLK,
  input  MACLK,
  input  PD1,
  input  FORM_n,
  input  [2:0] CC_3_1_n,
  input  LCS_n,
  input  RWCS_n,
  input  WCS_n,
  input  FETCH,
  input  BRK_n,
  input  TERM_n,
  input  WCA_n,
  output [15:0] IDB_15_0_io,
  output [63:0] CSBITS_io,
  output EWCA_n
);

  wire CTL_ecsl_n, CTL_elow_n, CTL_eupp_n;
  wire [3:0] CTL_ew_3_0_n, CTL_wu_3_0_n, CTL_ww_3_0_n;
  wire [11:0] ACAL_uua_11_0;
  wire [12:0] ACAL_lua_12_0;

  CPU_CS_CTL_18 CTL (
    .RF_1_0(RF_1_0), .FORM_n(FORM_n), .CC_3_1_n(CC_3_1_n), .LCS_n(LCS_n), .RWCS_n(RWCS_n), .WCS_n(WCS_n),
    .FETCH(FETCH), .BRK(BRK_n), .TERM_n(TERM_n), .LUA12(ACAL_lua_12_0[12]), .WCA_n(WCA_n),
    .EW_3_0_n(CTL_ew_3_0_n), .WW_3_0_n(CTL_ww_3_0_n), .WU_3_0_n(CTL_wu_3_0_n), .ECSL_n(CTL_ecsl_n),
    .EWCA_n(EWCA_n), .EUPP_n(CTL_eupp_n), .ELOW_n(CTL_elow_n));
  CPU_CS_ACAL_17 ACAL (
    .CSA_12_0(CSA_12_0), .PD1(PD1), .MACLK(MACLK), .CSCA_9_0(CSCA_9_0), .CLK(CLK), .LUA_12_0(ACAL_lua_12_0),
    .UUA_11_0(ACAL_uua_11_0));
  CPU_CS_PROM_19 PROM (.RF_1_0(RF_1_0), .LUA_12_0(ACAL_lua_12_0), .BLCS_n(BLCS_n), .IDB_15_0(IDB_15_0_io));
  CPU_CS_WCS_21_22 WCS (
    .WU3_n(CTL_wu_3_0_n[3]), .WU2_n(CTL_wu_3_0_n[2]), .WU1_n(CTL_wu_3_0_n[1]), .WU0_n(CTL_wu_3_0_n[0]),
    .EUPP_n(CTL_eupp_n), .UUA_11_0(ACAL_uua_11_0), .WW3_n(CTL_ww_3_0_n[3]), .WW2_n(CTL_ww_3_0_n[2]),
    .WW1_n(CTL_ww_3_0_n[1]), .WW0_n(CTL_ww_3_0_n[0]), .ELOW_n(CTL_elow_n), .LUA_11_0(ACAL_lua_12_0[11:0]),
    .CSBITS_63_0_io(CSBITS_io));
  CPU_CS_TCV_20 TCV (
    .CSBITS_io(CSBITS_io), .WCS_n(WCS_n), .ECSL_n(CTL_ecsl_n), .EW_3_0_n(CTL_ew_3_0_n),
    .IDB_15_0_io(IDB_15_0_io));

  // Notes on the sheet:
  //   ND120 CPU, MM&M
  //   CPU/CS
  //   CONTROL STORE
  //   SHEET 16 of 50
endmodule

module CPU_CS_ACAL_17 (
  input  [12:0] CSA_12_0,
  input  PD1,
  input  MACLK,
  input  [9:0] CSCA_9_0,
  input  CLK,
  output [12:0] LUA_12_0,
  output [11:0] UUA_11_0
);

  wire nand_1_out;
  wire [7:3] CHIP_30H_q_7_0, undriven;

  nand nand_1 (nand_1_out, LUA_12_0[12], LUA_12_0[12]);
  or or_1 (undriven[5], CSA_12_0[11], nand_1_out);
  or or_2 (undriven[6], CSA_12_0[10], nand_1_out);
  TTL_74373 CHIP_30H (
    .D_7_0({undriven, CSA_12_0[10], CSA_12_0[11], CSA_12_0[12]}), .C(MACLK), .OE_n(PD1),
    .Q_7_0({CHIP_30H_q_7_0[7], UUA_11_0[10], UUA_11_0[11], CHIP_30H_q_7_0[4:3], LUA_12_0[10], LUA_12_0[11], LUA_12_0[12]}));
  AM29841 CHIP_31F (
    .D0(CSA_12_0[9]), .D1(CSA_12_0[8]), .D2(CSA_12_0[7]), .D3(CSA_12_0[6]), .D4(CSA_12_0[5]),
    .D5(CSA_12_0[4]), .D6(CSA_12_0[3]), .D7(CSA_12_0[2]), .D8(CSA_12_0[1]), .D9(CSA_12_0[0]), .LE(MACLK),
    .OE_n(PD1), .Y0(LUA_12_0[9]), .Y1(LUA_12_0[8]), .Y2(LUA_12_0[7]), .Y3(LUA_12_0[6]), .Y4(LUA_12_0[5]),
    .Y5(LUA_12_0[4]), .Y6(LUA_12_0[3]), .Y7(LUA_12_0[2]), .Y8(LUA_12_0[1]), .Y9(LUA_12_0[0]));
  AM29841 CHIP_32G (
    .D0(CSA_12_0[9]), .D1(CSA_12_0[8]), .D2(CSA_12_0[7]), .D3(CSA_12_0[6]), .D4(CSA_12_0[5]),
    .D5(CSA_12_0[4]), .D6(CSA_12_0[3]), .D7(CSA_12_0[2]), .D8(CSA_12_0[1]), .D9(CSA_12_0[0]), .LE(MACLK),
    .OE_n(nand_1_out), .Y0(UUA_11_0[9]), .Y1(UUA_11_0[8]), .Y2(UUA_11_0[7]), .Y3(UUA_11_0[6]),
    .Y4(UUA_11_0[5]), .Y5(UUA_11_0[4]), .Y6(UUA_11_0[3]), .Y7(UUA_11_0[2]), .Y8(UUA_11_0[1]), .Y9(UUA_11_0[0]));
  AM29841 CHIP_31G (
    .D0(CSCA_9_0[9]), .D1(CSCA_9_0[8]), .D2(CSCA_9_0[7]), .D3(CSCA_9_0[6]), .D4(CSCA_9_0[5]),
    .D5(CSCA_9_0[4]), .D6(CSCA_9_0[3]), .D7(CSCA_9_0[2]), .D8(CSCA_9_0[1]), .D9(CSCA_9_0[0]), .LE(CLK),
    .OE_n(LUA_12_0[12]), .Y0(UUA_11_0[9]), .Y1(UUA_11_0[8]), .Y2(UUA_11_0[7]), .Y3(UUA_11_0[6]),
    .Y4(UUA_11_0[5]), .Y5(UUA_11_0[4]), .Y6(UUA_11_0[3]), .Y7(UUA_11_0[2]), .Y8(UUA_11_0[1]), .Y9(UUA_11_0[0]));

  // Other names for the same wires on the sheet: LUA12 = LUA_12_0[12]

  // Notes on the sheet:
  //   CPU/CS/ACAL
  //   SHEET 18 of 50
  //   ND120 CPU, MM&M
  //   MICRO ADDR CALC
  //   LUA9
  //   LUA0
  //   UUA9
  //   UUA0
  //   UUA9
  //   UUA0
  //   LUA12
  //   LUA11
  //   LUA10
  //   UUA11
  //   UUA10
endmodule

module CPU_CS_CTL_18 (
  input  [1:0] RF_1_0,
  input  FORM_n,
  input  [2:0] CC_3_1_n,
  input  LCS_n,
  input  RWCS_n,
  input  WCS_n,
  input  FETCH,
  input  BRK,
  input  TERM_n,
  input  LUA12,
  input  WCA_n,
  output [3:0] EW_3_0_n,
  output [3:0] WW_3_0_n,
  output [3:0] WU_3_0_n,
  output ECSL_n,
  output EWCA_n,
  output EUPP_n,
  output ELOW_n
);

  wire and_1_out, PAL_44305_UCSCTL_y0_n, PAL_44305_UCSCTL_y1_n;

  PAL_16L8_12 PAL_44305_UCSCTL (
    .I0(FORM_n), .I1(CC_3_1_n[0]), .I2(CC_3_1_n[1]), .I3(CC_3_1_n[2]), .I4(LCS_n), .I5(RWCS_n), .I6(WCS_n),
    .I7(FETCH), .I8(BRK), .I9(TERM_n), .Y0_n(PAL_44305_UCSCTL_y0_n), .Y1_n(PAL_44305_UCSCTL_y1_n),
    .B0_n(ECSL_n), .B1_n(EWCA_n), .B2_n(EUPP_n), .B3_n(ELOW_n), .B4_n(WCA_n));  // open: B5_n
  and and_1 (and_1_out, LCS_n, EWCA_n);
  TTL_74139 CHIP_30B (
    .A1(RF_1_0[0]), .B1(RF_1_0[1]), .G1_n(and_1_out), .A2(RF_1_0[0]), .B2(RF_1_0[1]),
    .G2_n(PAL_44305_UCSCTL_y1_n), .Y1_0_n(EW_3_0_n[0]), .Y1_1_n(EW_3_0_n[1]), .Y1_2_n(EW_3_0_n[2]),
    .Y1_3_n(EW_3_0_n[3]), .Y2_0_n(WW_3_0_n[0]), .Y2_1_n(WW_3_0_n[1]), .Y2_2_n(WW_3_0_n[2]),
    .Y2_3_n(WW_3_0_n[3]));
  nor nor_1 (WU_3_0_n[0], ~WW_3_0_n[0], ~PAL_44305_UCSCTL_y0_n);  // NOR_Gate
  nor nor_2 (WU_3_0_n[1], ~WW_3_0_n[1], ~PAL_44305_UCSCTL_y0_n);  // NOR_Gate
  nor nor_3 (WU_3_0_n[2], ~WW_3_0_n[2], ~PAL_44305_UCSCTL_y0_n);  // NOR_Gate
  nor nor_4 (WU_3_0_n[3], ~WW_3_0_n[3], ~PAL_44305_UCSCTL_y0_n);  // NOR_Gate

  // Notes on the sheet:
  //   CPU/CS/CTL
  //   CS CONTROL
  //   SHEET 18 of 50
  //   ND120 CPU, MM&M
  //   Verilog: Connect LUA12 to PAL.B5n
  //   Connect WCA_n to PAL.B4b
  //   WICA_n
  //   ECSD_n
  //   WCSTB_n
  //   RF0
  //   RF1
endmodule

module CPU_CS_PROM_19 (
  input  [1:0] RF_1_0,
  input  [12:0] LUA_12_0,
  input  BLCS_n,
  output [15:0] IDB_15_0
);

  wire not_1_out;
  wire [15:0] CHIP_23B_45132_data;

  ROM #(.addrWidth(15)) CHIP_23B_45132 (.addr({LUA_12_0, RF_1_0}), .data(CHIP_23B_45132_data[7:0]));
  ROM #(.addrWidth(15)) CHIP_26B_45133 (.addr({LUA_12_0, RF_1_0}), .data(CHIP_23B_45132_data[15:8]));
  not not_1 (not_1_out, BLCS_n);
  assign IDB_15_0 = not_1_out ? CHIP_23B_45132_data : 16'bz;  // Controlled_Buffer controlled_buffer_1

  // Notes on the sheet:
  //   CPU/CS/PROM
  //   PROMS
  //   SHEET 19 of 50
  //   ND120 CPU, MM&M
  //   contents of CHIP_23B_45132 (hex, n*v repeats v):
  //   1 29 83 0 18 0 2a 0 18 0 2a 0 2f 2f 60 80 37 2f 60 80 38 2f 60 80 6 0 8 0 7 0 8 0 8 0 8 0 9 0 8 0 8e
  //   0 8 0 b 0 8 0 c 0 8 0 d 0 8 0 28 20 ef 0 2b 29 29 80 c 6 80 80 0 0 c0 80 0 20 1 0 0 0 8 0 0 21 a0 80
  //   0 20 1 0 ff 0 80 80 65 25 c0 0 48 2d 63 0 1b 80 0 0 0 2 0 80 8*0 20 2 4 80 24 a0 2 0 f0 0 0 0 27 80
  //   0 0 e0 2b a0 80 c3 ac a0 80 c3 80 0 0 48 0 0 0 27 80 0 0 27 2 0 80 0 20 17 8*0 18 f0 0 0 18 0 20 f
  //   8*0 18 e0 0 0 18 69 d c0 80 0 0 60 0 0 9 20 80 0 20 a0 8c fc a 80 0 0 3 0 80 0 20 6 0 3d 20 3 c 39 9
  //   20 80 0 9 80 80 69 d c0 80 0 9 60 80 6*0 1d 0 65 2 0 80 3e 0 0 0 3f 0 0 0 40 0 0 0 65 0 1a 0 65 0 1b
  //   0 6a 0 1a 0 6a 0 1b 0 6c 20 18 0 6c 20 19 0 6f 0 1a 0 6f 0 1b 0 71 20 18 0 71 20 19 0 73 20 18 0 73
  //   20 19 0 78 20 18 0 78 20 19 0 7a 20 18 0 7a 20 19 0 7c 20 18 0 7c 20 19 0 7e 20 18 0 7e 20 19 0 80
  //   20 18 0 80 20 19 0 82 20 18 0 82 20 19 0 84 20 18 0 84 20 19 0 7a 20 18 0 7a 20 19 0 d8 20 18 0 d8
  //   20 19 0 5 20 18 0 5 20 19 0 10 20 18 0 10 20 19 0 0 20 96 0 0 20 97 0 0 20 17 0 65 0 1b 0 65 0 1b 0
  //   65 0 1b 0 65 0 1b 0 65 0 1b 0 6a 0 1b 0 0 25 79 80 0 21 77 80 6c 20 19 0 6a 0 1b 0 6f 0 1b 0 6c 26
  //   79 80 71 20 19 0 0 9 60 80 0 9 1b 80 0 20 15 0 0 20 15 0 73 20 19 0 0 25 77 80 78 20 19 0 0 26 77 80
  //   7a 20 19 0 0 27 77 80 7c 20 19 0 0 25 77 a0 7e 20 19 0 0 25 77 a0 80 20 19 0 0 25 77 80 82 20 19 0 0
  //   25 77 80 84 20 19 0 7a 20 19 0 7a 20 39 80 d8 28 39 80 5 28 39 80 10 20 d9 80 0 20 97 0 0 20 17 0 0
  //   20 15 0 90 0 2a 0 90 0 2a 5*0 65 0 0 0 93 0 0 15 65 20 12 2 93 0 0 15 65 20 12 81 98 20 4f 0 65 45 0
  //   80 10 4*0 40 0 0 98 20 4f 0 65 46 0 80 98 20 4f 0 65 41 0 80 98 20 4f 0 0 45 0 80 65 1 0 0 a5 4 0 80
  //   a8 80 0 0 a6 9 20 90 a7 0 0 81 e0 0 c0 0 0 0 c0 80 65 0 0 60 a6 9 20 90 a7 0 0 81 a6 9 20 90 a7 0 0
  //   81 a5 4 0 80 b2 80 4*0 c0 80 b4 0 0 81 a5 4 0 80 ae 80 4*0 c0 80 0 0 0 81 e8 0 20 10 d5 80 0 0 0 20
  //   17 0 bd a 20 80 65 a 0 e0 0 a 20 80 0 0 c0 80 bd 0 0 60 65 a 0 e0 a5 4 0 80 c1 80 0 0 a6 9 20 90 0 0
  //   0 81 a6 9 20 90 0 0 0 81 a5 4 0 80 c8 80 0 0 0 20 17 0 a5 4 0 80 65 80 0 0 a6 9 20 90 e0 0 0 81 d4
  //   8a 20 80 65 0 0 e0 a5 4 0 80 d1 80 0 0 0 20 17 0 a5 4 0 80 65 80 0 0 a6 9 20 90 e0 0 0 81 cb 8a 20
  //   80 65 0 0 e0 65 2 0 80 34 0 0 0 8f 80 4*0 40 80 4*0 e0 0 80 8 78 0 80 0 d6 27 f 0 d8 0 c0 80 e1 80
  //   20 80 10 4*0 60 3 8b 5*0 22 bd 10 0 27 bb 10 0 26 bb 10 0 25 bb 10 0 21 bb 10 0 24 bb 10 0 20 a0 10
  //   0 0 1b 0 65 23 bb 10 d6 0 0 0 d8 27 f 0 0 a 0 0 0 9 0 0 0 20 1c 0 fd 22 63 10 fd 27 63 10 fd 26 63
  //   10 fd 25 63 10 fd 21 63 10 fd 24 63 10 fd 20 63 10 e1 23 63 10 65 80 0 0 10 4*0 60 a0 8b 0 2 0 0 65
  //   0 0 60 0 20 19 0 d6 0 0 0 1 4*0 20 17 0 0 0 c0 80 da 0 40 80 6 a0 a0 90 ff 0 80 80 9 0 0 81 ff 0 80
  //   0 0 20 3 10 0 20 a0 91 0 5 0 0 d6 0 0 0 d 4*0 20 17 0 0 a 0 0 da 0 40 80 13 80 0 0 17 0 0 1 0 82 5*0
  //   60 4*0 17 20 3 11 ff 80 80 0 0 20 3 10 e4 0 0 81 d0 9 0 14 1b 8d 0 0 70 9 0 80 1e 85 0 94 0 1 0 a0 0
  //   5 0 80 b8 5 0 80 31 8f 0 0 e 21 8f 80 0 8 c0 80 0 20 22 e0 10 25 82 c0 0 45 0 c0 0 0 40 80 0 1 0 0
  //   e0 1 0 0 2a 80 0 60 0 1 0 80 d0 0 0 0 2d 80 0 0 70 0 0 0 2f 85 0 0 0 1 0 80 d1 f 0 80 65 80 0 0 0 8
  //   0 80 0 8 c0 0 0 20 17 60 e8 0 40 94 c0 0 80 0 31 80 4 14 0 20 12 14 0 27 57 80 d6 9 40 80 3f 20 2 0
  //   0 20 17 0 0 29 10 0 41 4*0 20 17 0 ff 0 80 80 0 9 0 0 e8 7 0 80 c0 0 80 0 49 83 0 80 e8 8 0 0 4a 80
  //   8*0 1f 0 0 5 68 80 d0 2f a0 80 d8 2f a0 80 0 2f 3 0 0 20 7 0 c5 4*0 80 4*0 e5 80 ff 5 80 0 e8 0 80 0
  //   57 8c 80 0 0 0 80 0 10 21 f 0 0 0 80 0 0 4c 0 80 0 5 0 0 0 20 c0 80 e0 0 20 0 5f 80 20 0 5d af a0 80
  //   5f 4*0 e 20 80 0 5 0 80 e8 0 20 0 0 8e 20 80 0 5 0 80 e8 5*0 80 0 75 8a 0 0 0 f 20 80 c e 80 80 e0
  //   4*0 2f 22 80 fe f 80 80 0 0 45 80 6d 80 0 0 ef f 80 80 e8 0 3e 0 71 ad 3 0 7f f 80 80 74 0 0 0 e0 f
  //   0 80 74 80 0 0 bf f 80 80 fd 0 5 0 0 2f a0 80 e8 1 0 80 79 8a 0 80 0 a 0 80 2 b 80 80 0 a 0 80 7d 0
  //   80 0 4b 0 0 0 d8 20 c0 80 80 af a0 80 0 5 20 80 e0 0 20 0 61 8e 20 80 e0 1 0 80 4b 80 20 0 4b 4 0 0
  //   0 20 7 0 4c 0 2d 0 e0 1 0 80 8a 8a 20 80 0 1 0 0 e8 a 0 80 4b 80 0 0 4b 8 0 0 d6 0 0 0 99 0 40 80 9d
  //   86 0 0 9f 87 0 0 a2 80 0 0 8e 0 0 0 d6 0 0 0 99 0 40 80 a5 86 0 0 a7 87 0 0 a9 80 0 0 8e 0 0 0 e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
  //   contents of CHIP_26B_45133 (hex, n*v repeats v):
  //   c4 0 0 20 60 0 0 20 50 0 0 20 0 0 2 7b 0 0 2 7b 0 0 2 7b 19*0 20 14*0 2 20 50 0 3 7b 80 80 0 7b 0 80
  //   0 1b 50 80 0 3a 0 80 0 20 0 80 3 7b 0 80 0 39 40 80 0 1b 0 0 2 7b a0 81 2 20 0 4 0 20 0 80 40 61 0
  //   80 0 20 0 80 0 20 0 81 0 65 0 84 0 39 0 81 0 20 0 84 0 20 c0 81 0 3b c5 84 0 3b 5 84 0 20 0 81 0 20
  //   0 4 0 20 0 0 0 65 0 0 c 71 0 80 0 20 0 80 0 20 7 2 c 20 90 80 0 3a 0 80 0 20 0 80 0 20 7 2 c 20 6 30
  //   0 7b 0 80 0 20 0 80 1 bb 0 80 0 1b ff 80 0 73 90 80 1 12 a0 80 c c 0 0 0 39 b0 0 0 7b 58 80 0 7b 6
  //   30 0 7b 90 80 0 6e f0 80 0 3a 90 84 c 3a 0 0 0 65 12*0 90 4 8 3a 90 c 4 3a 50 4 8 3a 50 c 4 3a 0 4 8
  //   20 0 c 4 20 60 4 8 3a 60 c 4 3a 0 4 8 20 0 c 4 20 0 4 8 20 0 c 4 20 0 4 8 20 0 c 4 20 0 4 8 20 0 c 4
  //   20 0 4 8 20 0 c 4 20 0 4 8 20 0 c 4 20 0 4 8 20 0 c 4 20 0 4 8 20 0 c 4 20 0 4 8 20 0 c 4 20 6 4 8
  //   20 6 c 4 20 6 4 8 20 6 c 4 20 7 4 8 20 7 c 4 20 9 4 8 20 9 c 4 20 0 4 b 20 0 c 7 20 0 0 c 71 0 c 0
  //   3a 50 c 0 3a 60 c 0 3a 70 c 0 3a 10 0 c 3a 50 c 0 3a 0 80 c 7b 0 0 c 7b 0 c 0 20 50 0 c 3a 60 c 0 3a
  //   0 0 c 7b 0 c 0 20 0 80 0 7b 0 80 48 61 90 80 c 3a 90 80 8 3a 0 c 0 20 0 0 c 7b 0 c 0 20 0 0 c 7b 0 c
  //   0 20 0 0 c 7b 0 c 0 20 50 0 c 62 0 c 0 20 50 0 4c 66 0 c 0 20 50 0 c 72 0 c 0 20 50 0 c 6e 0 c 0 20
  //   6 c 0 11 f6 c 0 1b 16 c 0 7f 17 c 0 7f 9 c 0 1b 0 c 3 20 0 0 c 20 0 0 8 31 70 0 0 20 90 0 0 20 0 80
  //   0 20 0 0 0 20 0 0 0 7a 0 0 c 79 0 0 0 7e 90 0 c 6c 0 20 0 20 0 14 30 b9 0 81 0 20 0 44 0 20 0 20 0
  //   20 0 14 30 b9 0 20 0 20 0 14 30 b9 10 20 0 1a 0 94 30 99 0 0 0 79 0 30 1 1b 0 84 0 20 0 30 0 7f 90 0
  //   0 70 0 51 0 13 0 50 0 7b 0 0 0 1a 0 30 0 7b 90 0 0 6c 0 30 0 7b 90 0 0 78 0 20 1 1b 0 84 0 20 0 80 0
  //   7b 0 0 0 1d 0 20 1 1b 0 84 0 20 0 80 0 7b 0 80 0 19 0 81 0 33 0 4 0 20 0 0 c 71 20 30 0 7f 0 0 0 30
  //   20 80 0 7b a0 80 0 1a 0 30 0 39 0 0 0 2c 0 30 1 1b 0 84 0 20 0 30 0 7f 90 50 0 70 0 30 0 7b 90 50 0
  //   6c 0 20 1 1b 0 84 0 20 0 0 c 71 0 20 1 1b 0 84 0 20 0 30 0 7b 90 81 0 30 20 84 0 7b a0 0 0 2c 0 20 1
  //   1b 0 84 0 20 0 0 c 71 0 20 1 1b 0 84 0 20 0 30 0 7b 90 81 0 30 20 84 0 7b a0 0 0 34 0 0 40 61 0 81 0
  //   20 0 4 0 20 0 80 0 1b 0 80 0 20 0 81 1 1b 0 50 0 13 0 30 1 20 0 30 0 7b 80 84 0 b 0 b1 0 20 0 94 0
  //   39 70 80 0 3a 0 84 4 20 0 80 c 20 0 80 c 20 0 80 c 20 0 80 c 20 0 80 c 20 0 80 0 13 0 80 c 39 0 0 c
  //   20 0 30 0 20 0 30 1 20 20 80 0 7a 70 80 0 7a 0 84 4 20 0 30 0 20 0 30 0 20 0 30 0 20 0 30 0 20 0 30
  //   0 20 0 30 0 20 0 30 0 20 0 81 0 39 0 84 0 20 0 b1 0 20 0 94 0 7b a0 80 0 7a 0 0 0 3a 0 50 c 20 0 30
  //   0 20 1 30 0 20 0 0 c 71 0 80 0 7b 0 30 0 1b 1 84 0 1b 0 80 0 72 1 0 0 19 0 80 0 13 0 80 0 39 0 80 0
  //   1b 0 40 0 79 0 30 0 20 1 30 0 20 0 0 c 71 20 80 0 7a 0 30 0 1b 1 84 0 20 51 30 0 7a a0 84 0 7a 0 40
  //   0 3a 50 80 0 1a 1 30 0 39 0 84 0 13 0 40 0 39 0 51 1 3b 0 81 0 7a 51 84 0 7a 0 81 40 69 1 84 0 18 0
  //   80 40 69 0 80 80 69 90 81 40 64 1 4 0 79 0 80 0 19 0 80 0 7b 70 80 0 3b 0 b1 9 d9 90 94 e8 c4 0 80 0
  //   1b 50 80 c ba 0 81 1 33 81 84 0 3a 90 80 0 60 f0 81 0 3a d1 84 0 3a 0 81 40 9 1 84 0 79 0 80 40 69
  //   50 81 0 38 0 84 0 20 0 80 1 1b 0 80 0 6f 80 0 c 3a 0 81 0 1a ff 80 0 33 1 4 0 3a 0 0 8 3a 70 0 c 62
  //   0 30 0 7b 1 30 0 20 0 0 c 20 60 80 c 7a 1 30 0 20 0 0 c 20 7 80 0 1b 90 80 0 70 90 81 1 16 0 80 0 3b
  //   91 4 1 16 0 81 1 3b 1 4 0 20 90 80 0 3a 50 84 c 3a 0 50 0 7b e7 2 0 1b e7 2 0 1b e0 80 0 39 0 50 0
  //   39 0 81 0 20 0 84 0 20 0 80 3 1b 0 50 0 73 70 81 1 13 31 4 1 73 20 80 1 f 0 81 1 20 60 b0 1 13 0 94
  //   8 f9 c0 80 0 7a 0 80 1 1b e0 81 0 33 b1 84 0 33 e1 84 0 1b 1 0 0 39 30 80 0 7b e0 80 0 6c 10 81 0 33
  //   0 54 0 7b e0 50 0 6c 0 81 0 20 78 80 0 33 51 4 0 7e 0 80 9 bb 0 80 0 7f 0 81 0 20 e0 80 0 6c ff 80 0
  //   72 50 80 c 32 1 84 0 20 ff 80 0 72 d0 81 c 33 51 4 0 3a ff 80 0 72 1 0 0 20 e0 81 0 34 1 84 0 20 ff
  //   80 0 72 f9 30 8 3a e0 80 0 1b a0 81 1 32 a1 4 1 6e a0 80 1 76 78 80 0 7b b0 80 0 70 0 80 0 13 a1 0 0
  //   c 0 81 1 3b e1 4 0 1b 30 80 0 7b 20 81 0 33 1 54 0 7b 50 81 1 32 21 84 0 f 1 0 1 17 0 80 0 39 71 0 0
  //   17 50 81 1 32 d1 84 0 7b 0 80 1 17 50 81 0 30 1 4 0 20 1 0 1 17 0 30 0 20 1 30 0 1b 1 4 41 27 1 4 41
  //   27 1 4 0 20 0 0 0 20 0 30 0 20 1 30 0 1b 1 4 41 27 1 4 41 27 1 4 0 20 0 0 0 20 0 81 1 13 0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
endmodule

module CPU_CS_TCV_20 (
  input  [63:0] CSBITS_io,
  input  WCS_n,
  input  ECSL_n,
  input  [3:0] EW_3_0_n,
  output [15:0] IDB_15_0_io
);

  TTL_74245 CHIP_16B (
    .A1(CSBITS_io[63]), .A2(CSBITS_io[62]), .A3(CSBITS_io[61]), .A4(CSBITS_io[60]), .A5(CSBITS_io[59]),
    .A6(CSBITS_io[58]), .A7(CSBITS_io[57]), .A8(CSBITS_io[56]), .DIR(WCS_n), .G_n(EW_3_0_n[3]),
    .B1(IDB_15_0_io[15]), .B2(IDB_15_0_io[14]), .B3(IDB_15_0_io[13]), .B4(IDB_15_0_io[12]),
    .B5(IDB_15_0_io[11]), .B6(IDB_15_0_io[10]), .B7(IDB_15_0_io[9]), .B8(IDB_15_0_io[8]));
  TTL_74245 CHIP_20B (
    .A1(CSBITS_io[47]), .A2(CSBITS_io[46]), .A3(CSBITS_io[45]), .A4(CSBITS_io[44]), .A5(CSBITS_io[43]),
    .A6(CSBITS_io[42]), .A7(CSBITS_io[41]), .A8(CSBITS_io[40]), .DIR(WCS_n), .G_n(EW_3_0_n[2]),
    .B1(IDB_15_0_io[15]), .B2(IDB_15_0_io[14]), .B3(IDB_15_0_io[13]), .B4(IDB_15_0_io[12]),
    .B5(IDB_15_0_io[11]), .B6(IDB_15_0_io[10]), .B7(IDB_15_0_io[9]), .B8(IDB_15_0_io[8]));
  TTL_74245 CHIP_24B (
    .A1(CSBITS_io[31]), .A2(CSBITS_io[30]), .A3(CSBITS_io[29]), .A4(CSBITS_io[28]), .A5(CSBITS_io[27]),
    .A6(CSBITS_io[26]), .A7(CSBITS_io[25]), .A8(CSBITS_io[24]), .DIR(WCS_n), .G_n(EW_3_0_n[1]),
    .B1(IDB_15_0_io[15]), .B2(IDB_15_0_io[14]), .B3(IDB_15_0_io[13]), .B4(IDB_15_0_io[12]),
    .B5(IDB_15_0_io[11]), .B6(IDB_15_0_io[10]), .B7(IDB_15_0_io[9]), .B8(IDB_15_0_io[8]));
  TTL_74245 CHIP_28B (
    .A1(CSBITS_io[15]), .A2(CSBITS_io[14]), .A3(CSBITS_io[13]), .A4(CSBITS_io[12]), .A5(CSBITS_io[11]),
    .A6(CSBITS_io[10]), .A7(CSBITS_io[9]), .A8(CSBITS_io[8]), .DIR(WCS_n), .G_n(EW_3_0_n[0]),
    .B1(IDB_15_0_io[15]), .B2(IDB_15_0_io[14]), .B3(IDB_15_0_io[13]), .B4(IDB_15_0_io[12]),
    .B5(IDB_15_0_io[11]), .B6(IDB_15_0_io[10]), .B7(IDB_15_0_io[9]), .B8(IDB_15_0_io[8]));
  TTL_74245 CHIP_19D (
    .A1(CSBITS_io[55]), .A2(CSBITS_io[54]), .A3(CSBITS_io[53]), .A4(CSBITS_io[52]), .A5(CSBITS_io[51]),
    .A6(CSBITS_io[50]), .A7(CSBITS_io[49]), .A8(CSBITS_io[48]), .DIR(WCS_n), .G_n(EW_3_0_n[3]),
    .B1(IDB_15_0_io[7]), .B2(IDB_15_0_io[6]), .B3(IDB_15_0_io[5]), .B4(IDB_15_0_io[4]), .B5(IDB_15_0_io[3]),
    .B6(IDB_15_0_io[2]), .B7(IDB_15_0_io[1]), .B8(IDB_15_0_io[0]));
  TTL_74245 CHIP_21B (
    .A1(CSBITS_io[39]), .A2(CSBITS_io[38]), .A3(CSBITS_io[37]), .A4(CSBITS_io[36]), .A5(CSBITS_io[35]),
    .A6(CSBITS_io[34]), .A7(CSBITS_io[33]), .A8(CSBITS_io[32]), .DIR(WCS_n), .G_n(EW_3_0_n[2]),
    .B1(IDB_15_0_io[7]), .B2(IDB_15_0_io[6]), .B3(IDB_15_0_io[5]), .B4(IDB_15_0_io[4]), .B5(IDB_15_0_io[3]),
    .B6(IDB_15_0_io[2]), .B7(IDB_15_0_io[1]), .B8(IDB_15_0_io[0]));
  TTL_74245 CHIP_27B (
    .A1(CSBITS_io[23]), .A2(CSBITS_io[22]), .A3(CSBITS_io[21]), .A4(CSBITS_io[20]), .A5(CSBITS_io[19]),
    .A6(CSBITS_io[18]), .A7(CSBITS_io[17]), .A8(CSBITS_io[16]), .DIR(WCS_n), .G_n(EW_3_0_n[1]),
    .B1(IDB_15_0_io[7]), .B2(IDB_15_0_io[6]), .B3(IDB_15_0_io[5]), .B4(IDB_15_0_io[4]), .B5(IDB_15_0_io[3]),
    .B6(IDB_15_0_io[2]), .B7(IDB_15_0_io[1]), .B8(IDB_15_0_io[0]));
  TTL_74245 CHIP_29B (
    .A1(CSBITS_io[7]), .A2(CSBITS_io[6]), .A3(CSBITS_io[5]), .A4(CSBITS_io[4]), .A5(CSBITS_io[3]),
    .A6(CSBITS_io[2]), .A7(CSBITS_io[1]), .A8(CSBITS_io[0]), .DIR(WCS_n), .G_n(EW_3_0_n[0]),
    .B1(IDB_15_0_io[7]), .B2(IDB_15_0_io[6]), .B3(IDB_15_0_io[5]), .B4(IDB_15_0_io[4]), .B5(IDB_15_0_io[3]),
    .B6(IDB_15_0_io[2]), .B7(IDB_15_0_io[1]), .B8(IDB_15_0_io[0]));
  TTL_74373 CHIP_8C (.D_7_0(IDB_15_0_io[7:0]), .C(ECSL_n), .OE_n(ECSL_n), .Q_7_0(IDB_15_0_io[7:0]));
  TTL_74373 CHIP_9C (.D_7_0(IDB_15_0_io[15:8]), .C(ECSL_n), .OE_n(ECSL_n), .Q_7_0(IDB_15_0_io[15:8]));

  // Other names for the same wires on the sheet: EW0_n = EW_3_0_n[0]; EW1_n = EW_3_0_n[1]; EW2_n = EW_3_0_n[2];
  //   EW3_n = EW_3_0_n[3]

  // Notes on the sheet:
  //   CPU/CS/TCV
  //   SHEET 20 of 50
  //   ND120 CPU, MM&M
  //   CS TRANSCEIVERS
  //   CSBIT15-CSBIT0
  //   IDB15-8
  //   IDB15-8
  //   IDB15-8
  //   IDB15-8
  //   CSALUI8-CSALU0, CSST1-CSST0, CSRASEL1-CSRASEL0, CSXRF, CSRBSEL1-CSRBSL0
  //   CSCISEL1-CSCICSEL0, CSALUM1-CSALUM0, CSMIS1-CSMIS0, CSIDBS4-CSIDBS-0, CSCOMM4-CSCOMM0
  //   CSSTS6-CSTS4, CSDELAY1-CSDELAY0, CSVECT, CSSCOND, CSECOND, CSLOOP, CSDLY, CSBIY20, CSRB3-CSRB0
  //   IDB7-0
  //   IDB7-0
  //   IDB7-0
  //   IDB7-0
  //   IDB7-0
  //   IDB15-8
endmodule

module CPU_CS_WCS_21_22 (
  input  WU3_n,
  input  WU2_n,
  input  WU1_n,
  input  WU0_n,
  input  EUPP_n,
  input  [11:0] UUA_11_0,
  input  WW3_n,
  input  WW2_n,
  input  WW1_n,
  input  WW0_n,
  input  ELOW_n,
  input  [11:0] LUA_11_0,
  output [63:0] CSBITS_63_0_io
);

  wire [3:0] CHIP_16D_d_3_0, CHIP_17D_d_3_0, CHIP_18D_d_3_0, CHIP_19D_d_3_0, CHIP_20D_d_3_0, CHIP_21D_d_3_0,
       CHIP_22D_d_3_0, CHIP_23D_d_3_0, CHIP_24D_d_3_0, CHIP_25D_d_3_0, CHIP_26D_d_3_0, CHIP_27D_d_3_0,
       CHIP_28D_d_3_0, CHIP_29D_d_3_0, CHIP_30D_d_3_0, CHIP_31D_d_3_0;

  IDT6168A_20 CHIP_16C (.A_11_0(LUA_11_0), .WE_n(WW3_n), .CE_n(ELOW_n), .D_3_0(CSBITS_63_0_io[63:60]));
  IDT6168A_20 CHIP_17C (.A_11_0(LUA_11_0), .WE_n(WW3_n), .CE_n(ELOW_n), .D_3_0(CSBITS_63_0_io[59:56]));
  IDT6168A_20 CHIP_18C (.A_11_0(LUA_11_0), .WE_n(WW3_n), .CE_n(ELOW_n), .D_3_0(CSBITS_63_0_io[55:52]));
  IDT6168A_20 CHIP_19C (.A_11_0(LUA_11_0), .WE_n(WW3_n), .CE_n(ELOW_n), .D_3_0(CSBITS_63_0_io[51:48]));
  IDT6168A_20 CHIP_16D (.A_11_0(UUA_11_0), .WE_n(WU3_n), .CE_n(EUPP_n), .D_3_0(CHIP_16D_d_3_0));
  IDT6168A_20 CHIP_17D (.A_11_0(UUA_11_0), .WE_n(WU3_n), .CE_n(EUPP_n), .D_3_0(CHIP_17D_d_3_0));
  IDT6168A_20 CHIP_18D (.A_11_0(UUA_11_0), .WE_n(WU3_n), .CE_n(EUPP_n), .D_3_0(CHIP_18D_d_3_0));
  IDT6168A_20 CHIP_19D (.A_11_0(UUA_11_0), .WE_n(WU3_n), .CE_n(EUPP_n), .D_3_0(CHIP_19D_d_3_0));
  IDT6168A_20 CHIP_20C (.A_11_0(LUA_11_0), .WE_n(WW2_n), .CE_n(ELOW_n), .D_3_0(CSBITS_63_0_io[47:44]));
  IDT6168A_20 CHIP_21C (.A_11_0(LUA_11_0), .WE_n(WW2_n), .CE_n(ELOW_n), .D_3_0(CSBITS_63_0_io[43:40]));
  IDT6168A_20 CHIP_22C (.A_11_0(LUA_11_0), .WE_n(WW2_n), .CE_n(ELOW_n), .D_3_0(CSBITS_63_0_io[39:36]));
  IDT6168A_20 CHIP_23C (.A_11_0(LUA_11_0), .WE_n(WW2_n), .CE_n(ELOW_n), .D_3_0(CSBITS_63_0_io[35:32]));
  IDT6168A_20 CHIP_20D (.A_11_0(UUA_11_0), .WE_n(WU2_n), .CE_n(EUPP_n), .D_3_0(CHIP_20D_d_3_0));
  IDT6168A_20 CHIP_21D (.A_11_0(UUA_11_0), .WE_n(WU2_n), .CE_n(EUPP_n), .D_3_0(CHIP_21D_d_3_0));
  IDT6168A_20 CHIP_22D (.A_11_0(UUA_11_0), .WE_n(WU2_n), .CE_n(EUPP_n), .D_3_0(CHIP_22D_d_3_0));
  IDT6168A_20 CHIP_23D (.A_11_0(UUA_11_0), .WE_n(WU2_n), .CE_n(EUPP_n), .D_3_0(CHIP_23D_d_3_0));
  IDT6168A_20 CHIP_24C (.A_11_0(LUA_11_0), .WE_n(WW1_n), .CE_n(ELOW_n), .D_3_0(CSBITS_63_0_io[31:28]));
  IDT6168A_20 CHIP_25C (.A_11_0(LUA_11_0), .WE_n(WW1_n), .CE_n(ELOW_n), .D_3_0(CSBITS_63_0_io[27:24]));
  IDT6168A_20 CHIP_26C (.A_11_0(LUA_11_0), .WE_n(WW1_n), .CE_n(ELOW_n), .D_3_0(CSBITS_63_0_io[23:20]));
  IDT6168A_20 CHIP_27C (.A_11_0(LUA_11_0), .WE_n(WW1_n), .CE_n(ELOW_n), .D_3_0(CSBITS_63_0_io[19:16]));
  IDT6168A_20 CHIP_24D (.A_11_0(UUA_11_0), .WE_n(WU1_n), .CE_n(EUPP_n), .D_3_0(CHIP_24D_d_3_0));
  IDT6168A_20 CHIP_25D (.A_11_0(UUA_11_0), .WE_n(WU1_n), .CE_n(EUPP_n), .D_3_0(CHIP_25D_d_3_0));
  IDT6168A_20 CHIP_26D (.A_11_0(UUA_11_0), .WE_n(WU1_n), .CE_n(EUPP_n), .D_3_0(CHIP_26D_d_3_0));
  IDT6168A_20 CHIP_27D (.A_11_0(UUA_11_0), .WE_n(WU1_n), .CE_n(EUPP_n), .D_3_0(CHIP_27D_d_3_0));
  IDT6168A_20 CHIP_28C (.A_11_0(LUA_11_0), .WE_n(WW0_n), .CE_n(ELOW_n), .D_3_0(CSBITS_63_0_io[15:12]));
  IDT6168A_20 CHIP_29C (.A_11_0(LUA_11_0), .WE_n(WW0_n), .CE_n(ELOW_n), .D_3_0(CSBITS_63_0_io[11:8]));
  IDT6168A_20 CHIP_30C (.A_11_0(LUA_11_0), .WE_n(WW0_n), .CE_n(ELOW_n), .D_3_0(CSBITS_63_0_io[7:4]));
  IDT6168A_20 CHIP_31C (.A_11_0(LUA_11_0), .WE_n(WW0_n), .CE_n(ELOW_n), .D_3_0(CSBITS_63_0_io[3:0]));
  IDT6168A_20 CHIP_28D (.A_11_0(UUA_11_0), .WE_n(WU0_n), .CE_n(EUPP_n), .D_3_0(CHIP_28D_d_3_0));
  IDT6168A_20 CHIP_29D (.A_11_0(UUA_11_0), .WE_n(WU0_n), .CE_n(EUPP_n), .D_3_0(CHIP_29D_d_3_0));
  IDT6168A_20 CHIP_30D (.A_11_0(UUA_11_0), .WE_n(WU0_n), .CE_n(EUPP_n), .D_3_0(CHIP_30D_d_3_0));
  IDT6168A_20 CHIP_31D (.A_11_0(UUA_11_0), .WE_n(WU0_n), .CE_n(EUPP_n), .D_3_0(CHIP_31D_d_3_0));

  // Notes on the sheet:
  //   ND120 CPU, MM&M
  //   CPU/CS/WCS
  //   Writable Control Store
  //   SHEET 22 of 50
  //   CSALUI8-CSALU0, CSST1-CSST0, CSRASEL1-CSRASEL0, CSXRF, CSRBSEL1-CSRBSL0
  //   CSALUI8-CSALU0, CSST1-CSST0, CSRASEL1-CSRASEL0, CSXRF, CSRBSEL1-CSRBSL0
  //   CSCISEL1-CSCICSEL0, CSALUM1-CSALUM0, CSMIS1-CSMIS0, CSIDBS4-CSIDBS-0, CSCOMM4-CSCOMM0
  //   CSCISEL1-CSCICSEL0, CSALUM1-CSALUM0, CSMIS1-CSMIS0, CSIDBS4-CSIDBS-0, CSCOMM4-CSCOMM0
  //   CSSTS6-CSTS4, CSDELAY1-CSDELAY0, CSVECT, CSSCOND, CSECOND, CSLOOP, CSDLY, CSBIY20, CSRB3-CSRB0
  //   CSSTS6-CSTS4, CSDELAY1-CSDELAY0, CSVECT, CSSCOND, CSECOND, CSLOOP, CSDLY, CSBIY20, CSRB3-CSRB0
  //   CSBIT15-CSBIT0
  //   CSBIT15-CSBIT0
  //   The signals needs to be connected in Verilog
endmodule

module CPU_LAPA_23 (
  input  [13:0] LA_23_10,
  input  LAPAN,
  output [13:0] PPN_23_10
);

  TTL_74244 CHIP_5G (
    .I2_1A3(LA_23_10[0]), .I3_1A4(LA_23_10[1]), .OE1_1G_n(LAPAN), .I4_2A1(LA_23_10[2]), .I5_2A2(LA_23_10[3]),
    .I6_2A3(LA_23_10[4]), .I7_2A4(LA_23_10[5]), .OE2_2G_n(LAPAN), .O2_1Y3(PPN_23_10[0]),
    .O3_1Y4(PPN_23_10[1]), .O4_2Y1(PPN_23_10[2]), .O5_2Y2(PPN_23_10[3]), .O6_2Y3(PPN_23_10[4]),
    .O7_2Y4(PPN_23_10[5]));  // open: I0_1A1, I1_1A2, O0_1Y1, O1_1Y2
  TTL_74244 CHIP_23H (
    .I0_1A1(LA_23_10[6]), .I1_1A2(LA_23_10[7]), .I2_1A3(LA_23_10[8]), .I3_1A4(LA_23_10[9]), .OE1_1G_n(LAPAN),
    .I4_2A1(LA_23_10[10]), .I5_2A2(LA_23_10[11]), .I6_2A3(LA_23_10[12]), .I7_2A4(LA_23_10[13]),
    .OE2_2G_n(LAPAN), .O0_1Y1(PPN_23_10[6]), .O1_1Y2(PPN_23_10[7]), .O2_1Y3(PPN_23_10[8]),
    .O3_1Y4(PPN_23_10[9]), .O4_2Y1(PPN_23_10[10]), .O5_2Y2(PPN_23_10[11]), .O6_2Y3(PPN_23_10[12]),
    .O7_2Y4(PPN_23_10[13]));

  // Notes on the sheet:
  //   CPU/LAPA
  //   ND120 CPU, MM&M
  //   LA TO PPN BUFF
  //   SHEET 23 of 50
  //   LA23
  //   LA10
  //   74244 = Octal Buffer with three-state outputs
endmodule

module CPU_MMU_CACHE_25 (
  input  [10:0] CA_10_0,
  input  CCLR_n,
  input  ECD_n,
  input  UCLK,
  input  DT_n,
  input  RT_n,
  input  LSHADOW,
  input  FMISS,
  input  CYD,
  input  PD2,
  input  [1:0] HIT_1_0_n,
  input  CWR,
  input  BRK_n,
  input  WCINH_n,
  input  SW1_CONSOLE,
  output WCA_n,
  output HIT,
  output [13:0] CPN_23_10_io,
  output [15:0] CD_15_0_io,
  output CON,
  output CON_n
);

  wire IHIT_n, nand_1_out, PAL_44402_UBITS_b0_n, PAL_44402_UBITS_b2_n, PAL_44402_UBITS_b3_n;
  wire [1:0] CHIP_16F_d0_d7;
  wire [3:0] CHIP_21F_q_4_1, PAL_44402_UBITS_q0_n;

  TMM2018D_25 CHIP_16F (
    .A0_A10(CA_10_0), .OE_n(1'b0), .W_n(WCA_n), .CS_n(PD2), .D0_D7({CPN_23_10_io[13:8], CHIP_16F_d0_d7}));
  TMM2018D_25 CHIP_20F (.A0_A10(CA_10_0), .OE_n(1'b0), .W_n(WCA_n), .CS_n(PD2), .D0_D7(CPN_23_10_io[7:0]));
  TMM2018D_25 CHIP_23F (.A0_A10(CA_10_0), .OE_n(1'b0), .W_n(WCA_n), .CS_n(ECD_n), .D0_D7(CD_15_0_io[15:8]));
  TMM2018D_25 CHIP_24F (.A0_A10(CA_10_0), .OE_n(1'b0), .W_n(WCA_n), .CS_n(ECD_n), .D0_D7(CD_15_0_io[7:0]));
  nand nand_1 (nand_1_out, BRK_n, SW1_CONSOLE, WCINH_n);
  PAL_16R4D PAL_44402_UBITS (
    .CK(UCLK), .I0(DT_n), .I1(RT_n), .I2(LSHADOW), .I3(FMISS), .I4(CYD), .I5(HIT_1_0_n[0]),
    .I6(HIT_1_0_n[1]), .I7(nand_1_out), .OE_n(PD2), .Q0_n(PAL_44402_UBITS_q0_n[0]),
    .Q1_n(PAL_44402_UBITS_q0_n[1]), .Q3_n(IHIT_n), .B0_n(PAL_44402_UBITS_b0_n), .B1_n(WCA_n),
    .B2_n(PAL_44402_UBITS_b2_n), .B3_n(PAL_44402_UBITS_b3_n));  // open: Q2_n
  LED #(.active("false")) LED_1 (.in(SW1_CONSOLE));
  not not_1 (CON_n, SW1_CONSOLE);
  AM9150_20 CHIP_21F (
    .A_9_0(CA_10_0[9:0]), .D_4_1(PAL_44402_UBITS_q0_n), .R_n(CCLR_n), .S_n(1'b0), .W_n(WCA_n), .G_n(1'b0),
    .Q_4_1(CHIP_21F_q_4_1));
  and and_1 (HIT, ~PAL_44402_UBITS_b0_n, ~HIT_1_0_n[1], ~HIT_1_0_n[0], ~CWR, ~1'b0);  // AND_Gate

  assign CON = SW1_CONSOLE;

  // Notes on the sheet:
  //   CON: pull=up
  //   CON_n: pull=up
  //   ND120 CPU, MM&M
  //   CPU/MMU/PT
  //   PAGE TABLES
  //   SHEET 29 of 50
  //   The signals needs to be connected in Verilog
  //   WCA_n
  //   CPN17
  //   CPN10
  //   CPN23
  //   CPN18
  //   D0 and D1 not connected
  //   CPN is bi-directional
  //   WCA_n
  //   CD is bi-directional
  //   HIT1_n
  //   HIT0_n
  //   NUBI
  //   NUBD
  //   USED_n
  //   OUBI
  //   OUBD
  //   The signals needs to be connected in Verilog
  //   OUBI
  //   OUBD
endmodule

module CPU_MMU_24 (
  input  ESTOF_n,
  input  DVACC_n,
  input  WCHIM_n,
  input  DOUBLE,
  input  EMCL_n,
  input  CC2_n,
  input  [10:0] CA_10_0,
  input  CCLR_n,
  input  UCLK,
  input  DT_n,
  input  RT_n,
  input  CYD,
  input  CWR,
  input  BRK_n,
  input  in_15,
  input  [10:0] LA_20_10,
  input  EORF_n,
  input  WRITE,
  input  LSHADOW,
  input  FMISS,
  input  PD2,
  output LAPA_n,
  output [15:0] CD_15_0_io,
  output [15:0] PPN_25_10_io,
  output WCA_n,
  output [15:0] IDB_15_0_io,
  output BSTP,
  output BEMPID_n,
  output BEDO_n,
  output BLCS_n
);

  wire CACHE_con_n, nand_1_out, or_1_out, PAL_44306_UNOCTL_b0_n, PAL_44306_UNOCTL_b1_n,
       PAL_44306_UNOCTL_b2_n, PAL_44306_UNOCTL_b3_n, PAL_44306_UNOCTL_b4_n, PAL_44306_UNOCTL_b5_n,
       PAL_44306_UNOCTL_y0_n, PT_wcinh_n;
  wire [1:0] HIT_hit0_n;
  wire [13:0] WCA_cpn_23_10;
  wire [15:0] PT_pt_15_0;

  or or_1 (or_1_out, WCHIM_n, EORF_n);
  nand nand_1 (nand_1_out, LSHADOW, WRITE, CYD);
  PAL_16L8_12 PAL_44306_UNOCTL (
    .I0(CA_10_0[0]), .I1(WRITE), .I2(DVACC_n), .I3(RT_n), .I4(WCHIM_n), .I5(DOUBLE), .I6(EMCL_n), .I7(CC2_n),
    .I8(WCA_n), .I9(LSHADOW), .Y0_n(PAL_44306_UNOCTL_y0_n), .Y1_n(LAPA_n), .B0_n(PAL_44306_UNOCTL_b0_n),
    .B1_n(PAL_44306_UNOCTL_b1_n), .B2_n(PAL_44306_UNOCTL_b2_n), .B3_n(PAL_44306_UNOCTL_b3_n),
    .B4_n(PAL_44306_UNOCTL_b4_n), .B5_n(PAL_44306_UNOCTL_b5_n));
  CPU_MMU_PT_29 PT (
    .LA_20_10(LA_20_10), .WMAP_n(nand_1_out), .EPMAP_n(PAL_44306_UNOCTL_b4_n), .EPT_n(PAL_44306_UNOCTL_b5_n),
    .WCLIM_n(or_1_out), .WCINH_n(PT_wcinh_n), .PPN_25_10(PPN_25_10_io), .PT_15_0(PT_pt_15_0));
  CPU_MMU_HIT_27 HIT (
    .LSHADOW(LSHADOW), .PPN_23_10(PPN_25_10_io[13:0]), .CPN_23_10(WCA_cpn_23_10), .FMISS(FMISS),
    .CON_n(CACHE_con_n), .HIT1_n(HIT_hit0_n[1]), .HIT0_n(HIT_hit0_n[0]));
  CPU_MMU_PPNX_28 PPNX (
    .ESTOF_n(ESTOF_n), .EIPU_n(PAL_44306_UNOCTL_b1_n), .EIPL_n(PAL_44306_UNOCTL_b2_n),
    .EIPUR_n(PAL_44306_UNOCTL_b0_n), .IDB_15_0_io(IDB_15_0_io), .PPN_25_10_io(PPN_25_10_io));
  CPU_MMU_PTIDB_30 PTIDB (.IDB_15_0(IDB_15_0_io), .WRITE(WRITE), .EPTI_n(PAL_44306_UNOCTL_b3_n), .PT_15_0(PT_pt_15_0));
  CPU_MMU_WCA_31 WCA (.PPN_23_10(PPN_25_10_io[13:0]), .WCA_n(WCA_n), .CPN_23_10(WCA_cpn_23_10));
  CPU_MMU_CSR_26 CSR (
    .PD2(PD2), .BSTP(BSTP), .BEMPID_n(BEMPID_n), .BEDO_n(BEDO_n), .BLCS_n(BLCS_n), .IDB_3_0(IDB_15_0_io[3:0]));  // open: STPN, EMPIDN, EDON, LCSN, CUP, CON, ECSRN
  CPU_MMU_CACHE_25 CACHE (
    .CA_10_0(CA_10_0), .CCLR_n(CCLR_n), .ECD_n(PAL_44306_UNOCTL_y0_n), .UCLK(UCLK), .DT_n(DT_n), .RT_n(RT_n),
    .LSHADOW(LSHADOW), .FMISS(FMISS), .CYD(CYD), .PD2(PD2), .HIT_1_0_n(HIT_hit0_n), .CWR(CWR), .BRK_n(BRK_n),
    .WCINH_n(PT_wcinh_n), .SW1_CONSOLE(in_15), .WCA_n(WCA_n), .CPN_23_10_io(WCA_cpn_23_10),
    .CD_15_0_io(CD_15_0_io), .CON_n(CACHE_con_n));  // open: HIT, CON

  // Notes on the sheet:
  //   ND120 CPU, MM&M
  //   CPU/MMU
  //   MMU TOP LEVEL
  //   SHEET 26 of 50
  //   CA0
  //   EPT_n
  //   ECD_n
  //   EPMAP_n
  //   EPTI_n
  //   EIPUR_n
  //   EIPU_n
  //   EIPL_n
  //   PPN_23_10
endmodule

module CPU_MMU_CSR_26 (
  input  STPN,
  input  EMPIDN,
  input  EDON,
  input  LCSN,
  input  PD2,
  input  CUP,
  input  CON,
  input  ECSRN,
  output BSTP,
  output BEMPID_n,
  output BEDO_n,
  output BLCS_n,
  output [3:0] IDB_3_0
);

  wire not_1_out;

  not not_1 (not_1_out, CON);
  TTL_74244 CHIP_27H (
    .I0_1A1(STPN), .I1_1A2(EMPIDN), .I2_1A3(EDON), .I3_1A4(LCSN), .OE1_1G_n(PD2), .I4_2A1(CUP), .I5_2A2(CON),
    .I6_2A3(not_1_out), .I7_2A4(1'b1), .OE2_2G_n(ECSRN), .O0_1Y1(BSTP), .O1_1Y2(BEMPID_n), .O2_1Y3(BEDO_n),
    .O3_1Y4(BLCS_n), .O4_2Y1(IDB_3_0[0]), .O5_2Y2(IDB_3_0[1]), .O6_2Y3(IDB_3_0[2]), .O7_2Y4(IDB_3_0[3]));

  // Notes on the sheet:
  //   RN9
  //   ND120 CPU, MM&M
  //   CPU/MMU/CSR
  //   CACHE STATUS REG
  //   SHEET 26 of 50
  //   4610X_101_102
  //   Cache Status Register
endmodule

module CPU_MMU_HIT_27 (
  input  LSHADOW,
  input  [13:0] PPN_23_10,
  input  [13:0] CPN_23_10,
  input  FMISS,
  input  CON_n,
  output HIT1_n,
  output HIT0_n
);

  TTL_74521 CHIP_18G (
    .A_7_0({PPN_23_10[8], PPN_23_10[9], PPN_23_10[10], PPN_23_10[11], PPN_23_10[12], PPN_23_10[13], LSHADOW, 1'b0}),
    .B_7_0({CPN_23_10[8], CPN_23_10[9], CPN_23_10[10], CPN_23_10[11], CPN_23_10[12], CPN_23_10[13], 2'b00}),
    .E_n(FMISS), .AB_n(HIT1_n));
  TTL_74521 CHIP_19G (.A_7_0(PPN_23_10[7:0]), .B_7_0(CPN_23_10[7:0]), .E_n(CON_n), .AB_n(HIT0_n));

  // Notes on the sheet:
  //   HIT DETECT
  //   ND120 CPU, MM&M
  //   CPU/MMU/HIT
  //   SHEET 27 of 50
endmodule

module CPU_MMU_PPNX_28 (
  input  ESTOF_n,
  input  EIPU_n,
  input  EIPL_n,
  input  EIPUR_n,
  output [15:0] IDB_15_0_io,
  output [15:0] PPN_25_10_io
);

  TTL_74244 CHIP_8B (
    .I0_1A1(1'b0), .I1_1A2(1'b0), .I2_1A3(1'b0), .I3_1A4(1'b0), .OE1_1G_n(EIPUR_n), .I4_2A1(1'b0),
    .I5_2A2(1'b0), .I6_2A3(1'b0), .I7_2A4(IDB_15_0_io[8]), .OE2_2G_n(EIPUR_n), .O0_1Y1(PPN_25_10_io[15]),
    .O1_1Y2(PPN_25_10_io[14]), .O2_1Y3(PPN_25_10_io[13]), .O3_1Y4(PPN_25_10_io[12]),
    .O4_2Y1(PPN_25_10_io[11]), .O5_2Y2(PPN_25_10_io[10]), .O6_2Y3(PPN_25_10_io[9]), .O7_2Y4(PPN_25_10_io[8]));
  TTL_74245 CHIP_10B (
    .A1(PPN_25_10_io[15]), .A2(PPN_25_10_io[14]), .A3(PPN_25_10_io[13]), .A4(PPN_25_10_io[12]),
    .A5(PPN_25_10_io[11]), .A6(PPN_25_10_io[10]), .A7(PPN_25_10_io[9]), .A8(PPN_25_10_io[8]), .DIR(ESTOF_n),
    .G_n(EIPU_n), .B1(IDB_15_0_io[15]), .B2(IDB_15_0_io[14]), .B3(IDB_15_0_io[13]), .B4(IDB_15_0_io[12]),
    .B5(IDB_15_0_io[11]), .B6(IDB_15_0_io[10]), .B7(IDB_15_0_io[9]), .B8(IDB_15_0_io[8]));
  TTL_74245 CHIP_9B (
    .A1(PPN_25_10_io[7]), .A2(PPN_25_10_io[6]), .A3(PPN_25_10_io[5]), .A4(PPN_25_10_io[4]),
    .A5(PPN_25_10_io[3]), .A6(PPN_25_10_io[2]), .A7(PPN_25_10_io[1]), .A8(PPN_25_10_io[0]), .DIR(ESTOF_n),
    .G_n(EIPL_n), .B1(IDB_15_0_io[7]), .B2(IDB_15_0_io[6]), .B3(IDB_15_0_io[5]), .B4(IDB_15_0_io[4]),
    .B5(IDB_15_0_io[3]), .B6(IDB_15_0_io[2]), .B7(IDB_15_0_io[1]), .B8(IDB_15_0_io[0]));

  // Other names for the same wires on the sheet: IDB8 = IDB_15_0_io[8]

  // Notes on the sheet:
  //   PPN to IDB
  //   ND120 CPU, MM&M
  //   CPU/MMU/CSR
  //   SHEET 28 of 50
  //   PPN25
  //   PPN18
  //   PPN25
  //   PPN18
  //   PPN17
  //   PPN10
  //   IDB15
  //   IDB8
  //   IDB7
  //   IDB0
  //   IDB is bi-directional
  //   PPN is bi-directional
endmodule

module CPU_MMU_PT_29 (
  input  [10:0] LA_20_10,
  input  WMAP_n,
  input  EPMAP_n,
  input  EPT_n,
  input  WCLIM_n,
  output WCINH_n,
  output [15:0] PPN_25_10,
  output [15:0] PT_15_0
);

  TMM2018D_25 CHIP_22G (.A0_A10(LA_20_10), .OE_n(1'b0), .W_n(WMAP_n), .CS_n(EPMAP_n), .D0_D7(PPN_25_10[15:8]));
  TMM2018D_25 CHIP_23G (.A0_A10(LA_20_10), .OE_n(1'b0), .W_n(WMAP_n), .CS_n(EPMAP_n), .D0_D7(PPN_25_10[7:0]));
  TMM2018D_25 CHIP_24g (.A0_A10(LA_20_10), .OE_n(1'b0), .W_n(WMAP_n), .CS_n(EPT_n), .D0_D7(PT_15_0[15:8]));
  TMM2018D_25 CHIP_25G (.A0_A10(LA_20_10), .OE_n(1'b0), .W_n(WMAP_n), .CS_n(EPT_n), .D0_D7(PT_15_0[7:0]));
  IMS1403_25 CHIP_20G (.A0_A13(PPN_25_10[13:0]), .D(PPN_25_10[15]), .W_n(WCLIM_n), .CE_n(1'b0), .Q(WCINH_n));

  // Notes on the sheet:
  //   CACHE
  //   ND120 CPU, MM&M
  //   CPU/MMU/PT
  //   SHEET 29 of 50
  //   WMAP_n
  //   EPMAP_n
  //   WMAP_n
  //   EPMAP_n
  //   WMAP_n
  //   EPT_n
  //   EPT_n
  //   PPN is bi-directional
  //   PT is bi-directional
endmodule

module CPU_MMU_PTIDB_30 (
  input  [15:0] IDB_15_0,
  input  WRITE,
  input  EPTI_n,
  output [15:0] PT_15_0
);

  TTL_74245 CHIP_17B (
    .A1(IDB_15_0[0]), .A2(IDB_15_0[1]), .A3(IDB_15_0[2]), .A4(IDB_15_0[3]), .A5(IDB_15_0[4]),
    .A6(IDB_15_0[5]), .A7(IDB_15_0[6]), .A8(IDB_15_0[7]), .DIR(WRITE), .G_n(EPTI_n), .B1(PT_15_0[0]),
    .B2(PT_15_0[1]), .B3(PT_15_0[2]), .B4(PT_15_0[3]), .B5(PT_15_0[4]), .B6(PT_15_0[5]), .B7(PT_15_0[6]),
    .B8(PT_15_0[7]));
  TTL_74245 CHIP_18B (
    .A1(IDB_15_0[8]), .A2(IDB_15_0[9]), .A3(IDB_15_0[10]), .A4(IDB_15_0[11]), .A5(IDB_15_0[12]),
    .A6(IDB_15_0[13]), .A7(IDB_15_0[14]), .A8(IDB_15_0[15]), .DIR(WRITE), .G_n(EPTI_n), .B1(PT_15_0[8]),
    .B2(PT_15_0[9]), .B3(PT_15_0[10]), .B4(PT_15_0[11]), .B5(PT_15_0[12]), .B6(PT_15_0[13]),
    .B7(PT_15_0[14]), .B8(PT_15_0[15]));

  // Notes on the sheet:
  //   ND120 CPU, MM&M
  //   CPU/MMU/PTIDB
  //   PT TO IDB
  //   SHEET 30 of 50
  //   WRITE / READ_n
endmodule

module CPU_MMU_WCA_31 (
  input  [13:0] PPN_23_10,
  input  WCA_n,
  output [13:0] CPN_23_10
);

  TTL_74244 CHIP_11G (
    .I2_1A3(PPN_23_10[13]), .I3_1A4(PPN_23_10[12]), .OE1_1G_n(WCA_n), .I4_2A1(PPN_23_10[11]),
    .I5_2A2(PPN_23_10[10]), .I6_2A3(PPN_23_10[9]), .I7_2A4(PPN_23_10[8]), .OE2_2G_n(WCA_n),
    .O2_1Y3(CPN_23_10[12]), .O3_1Y4(CPN_23_10[13]), .O4_2Y1(CPN_23_10[11]), .O5_2Y2(CPN_23_10[10]),
    .O6_2Y3(CPN_23_10[9]), .O7_2Y4(CPN_23_10[8]));  // open: I0_1A1, I1_1A2, O0_1Y1, O1_1Y2
  TTL_74244 CHIP_10G (
    .I0_1A1(PPN_23_10[7]), .I1_1A2(PPN_23_10[6]), .I2_1A3(PPN_23_10[5]), .I3_1A4(PPN_23_10[4]),
    .OE1_1G_n(WCA_n), .I4_2A1(PPN_23_10[3]), .I5_2A2(PPN_23_10[2]), .I6_2A3(PPN_23_10[1]),
    .I7_2A4(PPN_23_10[0]), .OE2_2G_n(WCA_n), .O0_1Y1(CPN_23_10[7]), .O1_1Y2(CPN_23_10[6]),
    .O2_1Y3(CPN_23_10[5]), .O3_1Y4(CPN_23_10[4]), .O4_2Y1(CPN_23_10[3]), .O5_2Y2(CPN_23_10[2]),
    .O6_2Y3(CPN_23_10[1]), .O7_2Y4(CPN_23_10[0]));

  // Notes on the sheet:
  //   ND120 CPU, MM&M
  //   CPU/MMU/WCA
  //   PPN TO CPN
  //   SHEET 31 of 50
  //   CPN23-CPN22
  //   CPN21-CPN18
  //   CPN17-CPN14
  //   CPN13-CPN10
endmodule

module CPU_PROC_CMDDEC_34 (
  input  CLK,
  input  [4:0] CSIDBS_4_0,
  input  WRTRF,
  input  in_4,
  input  CGABRK_n,
  input  [4:0] CSCOMM_4_0,
  input  [1:0] CSMIS_1_0,
  input  IDB2,
  input  [3:0] PIL_3_0,
  input  MREQ_n,
  input  WCA_n,
  input  PD1,
  output RRF_n,
  output ERF_n,
  output BRK_n,
  output VEX,
  output OPCLCS,
  output RWCS_n,
  output RT_n,
  output CUP,
  output CWR,
  output LEV0
);

  wire LDEXM_n;

  PAL_16R4D PAL_44407_UERFIX (
    .CK(CLK), .I0(CSIDBS_4_0[0]), .I1(CSIDBS_4_0[1]), .I2(CSIDBS_4_0[2]), .I3(CSIDBS_4_0[3]),
    .I4(CSIDBS_4_0[4]), .I5(WRTRF), .I6(in_4), .OE_n(PD1), .Q0_n(RRF_n), .B0_n(ERF_n));  // open: I7, Q1_n, Q2_n, Q3_n, B1_n, B2_n, B3_n
  PAL_16R6D PAL_444608_UVXFIX (
    .CK(CLK), .I0(CSCOMM_4_0[4]), .I1(CSCOMM_4_0[3]), .I2(CSCOMM_4_0[2]), .I3(CSCOMM_4_0[1]),
    .I4(CSCOMM_4_0[0]), .I5(CSMIS_1_0[1]), .I6(CSMIS_1_0[0]), .OE_n(PD1), .Q1_n(LDEXM_n), .Q2_n(VEX),
    .Q3_n(OPCLCS), .Q4_n(RWCS_n), .Q5_n(RT_n), .B1_n(IDB2));  // open: I7, Q0_n, B0_n
  PAL_16R4D PAL_44511_ULEV0 (
    .CK(CLK), .I0(PIL_3_0[0]), .I1(PIL_3_0[1]), .I2(PIL_3_0[2]), .I3(PIL_3_0[3]), .I4(CLK), .I5(MREQ_n),
    .I6(WCA_n), .OE_n(PD1), .Q0_n(CUP), .B0_n(CWR), .B3_n(LEV0));  // open: I7, Q1_n, Q2_n, Q3_n, B1_n, B2_n
  nand nand_1 (BRK_n, ~CGABRK_n, ~VEX);  // NAND_Gate

  // Notes on the sheet:
  //   ND120 CPU, MM&M
  //   CPU/PROC/CMDDEC
  //   COMMAND & IDB DECODE
  //   SHEET 34 of 50
  //   CSMIS1
  //   CSMIS0
  //   CSIDBS0
  //   CSIDBS4
  //   CSCOMM4
  //   CSCOMM0
  //   CLK
endmodule

module CPU_STOC_35 (
  input  [15:0] IDB_15_0,
  input  STOC,
  output [15:0] CD_15_0
);

  TTL_74244 CHIP_14B (
    .I0_1A1(IDB_15_0[15]), .I1_1A2(IDB_15_0[14]), .I2_1A3(IDB_15_0[13]), .I3_1A4(IDB_15_0[12]),
    .OE1_1G_n(STOC), .I4_2A1(IDB_15_0[11]), .I5_2A2(IDB_15_0[10]), .I6_2A3(IDB_15_0[9]),
    .I7_2A4(IDB_15_0[8]), .OE2_2G_n(STOC), .O0_1Y1(CD_15_0[15]), .O1_1Y2(CD_15_0[14]), .O2_1Y3(CD_15_0[13]),
    .O3_1Y4(CD_15_0[12]), .O4_2Y1(CD_15_0[11]), .O5_2Y2(CD_15_0[10]), .O6_2Y3(CD_15_0[9]), .O7_2Y4(CD_15_0[8]));
  TTL_74244 CHIP_15D (
    .I0_1A1(IDB_15_0[7]), .I1_1A2(IDB_15_0[6]), .I2_1A3(IDB_15_0[5]), .I3_1A4(IDB_15_0[4]), .OE1_1G_n(STOC),
    .I4_2A1(IDB_15_0[3]), .I5_2A2(IDB_15_0[2]), .I6_2A3(IDB_15_0[1]), .I7_2A4(IDB_15_0[0]), .OE2_2G_n(STOC),
    .O0_1Y1(CD_15_0[7]), .O1_1Y2(CD_15_0[6]), .O2_1Y3(CD_15_0[5]), .O3_1Y4(CD_15_0[4]), .O4_2Y1(CD_15_0[3]),
    .O5_2Y2(CD_15_0[2]), .O6_2Y3(CD_15_0[1]), .O7_2Y4(CD_15_0[0]));

  // Notes on the sheet:
  //   ND120 CPU, MM&M
  //   CPU/STOC
  //   IDB TO CD
  //   SHEET 35 of 50
endmodule

module CYC_36 (
  input  OSC,
  input  RRF_n,
  input  CSDELAY1,
  input  CSALUM1,
  input  CSALUM0,
  input  CSALUI8,
  input  CSALUI7,
  input  LBA3,
  input  LBA1,
  input  LBA0,
  input  CSDELAY0,
  input  CSDLY,
  input  CSECOND,
  input  CSLOOP,
  input  ACOND_n,
  input  MR_n,
  input  LUA12,
  input  PD1,
  input  CGNTCACT_n,
  input  HIT,
  input  BRK_n,
  input  SHORT_n,
  input  SLOW_n,
  input  PD4,
  input  FORM_n,
  input  RWCS_n,
  input  TRAP_n,
  input  VEX,
  input  MREQ_n,
  input  IORQ_n,
  input  LSHADOW,
  input  RT_n,
  output CLK,
  output ALUCLK,
  output LCS_n,
  output MCLK,
  output CX_n,
  output TERM_n,
  output MACLK,
  output [2:0] CC_3_1_n,
  output UCLK,
  output WRFSTB,
  output CYD,
  output EORF_n,
  output ETRAP_n,
  output MAP_n
);

  wire and_1_out, CC0_n, DLSHADOW, DMA12_n, DMAP_n, MDLY_n, nand_1_out, nand_2_out, not_1_out, NOWRIT_n,
       or_1_out, or_2_out, PAL_44307_UCYCLK_b3_n, PAL_44307_UCYCLK_y0_n, PAL_44307_UCYCLK_y1_n,
       PAL_44403_UCYIN0_b0_n, PAL_44403_UCYIN0_b2_n, PAL_44404_UCYIN1_b0_n, PAL_44404_UCYIN1_b1_n,
       PAL_44404_UCYIN1_b2_n, PAL_44404_UCYIN1_b3_n, PAL_44601_UCYCFSM_b0_n, PAL_44601_UCYCFSM_b1_n;

  or or_1 (or_1_out, MREQ_n, LSHADOW);
  or or_2 (or_2_out, LSHADOW, RT_n);
  nand nand_1 (nand_1_out, or_1_out, IORQ_n);
  nand nand_2 (nand_2_out, IORQ_n, or_2_out);
  PAL_16R4D PAL_44404_UCYIN1 (
    .CK(CLK), .I0(CSDELAY1), .I1(CSALUM1), .I2(CSALUM0), .I3(CSALUI8), .I4(CSALUI7), .I5(LBA3), .I6(LBA1),
    .I7(LBA0), .OE_n(PD1), .Q0_n(NOWRIT_n), .Q1_n(DLSHADOW), .B0_n(PAL_44404_UCYIN1_b0_n),
    .B1_n(PAL_44404_UCYIN1_b1_n), .B2_n(PAL_44404_UCYIN1_b2_n), .B3_n(PAL_44404_UCYIN1_b3_n));  // open: Q2_n, Q3_n
  PAL_16R4D PAL_44403_UCYIN0 (
    .CK(CLK), .I0(CSDELAY0), .I1(CSDLY), .I2(CSECOND), .I3(CSLOOP), .I4(ACOND_n), .I5(MR_n), .I6(LUA12),
    .I7(MAP_n), .OE_n(PD1), .Q0_n(LCS_n), .Q1_n(MDLY_n), .Q2_n(DMA12_n), .Q3_n(DMAP_n),
    .B0_n(PAL_44403_UCYIN0_b0_n), .B2_n(PAL_44403_UCYIN0_b2_n));  // open: B1_n, B3_n
  and and_1 (and_1_out, MR_n, nand_1_out);
  PAL_16R6D PAL_44601_UCYCFSM (
    .CK(OSC), .I0(PAL_44404_UCYIN1_b3_n), .I1(PAL_44403_UCYIN0_b0_n), .I2(CSDELAY0), .I3(and_1_out),
    .I4(nand_2_out), .I5(CGNTCACT_n), .I6(HIT), .I7(BRK_n), .OE_n(PD4), .Q0_n(CX_n), .Q1_n(TERM_n),
    .Q2_n(CC0_n), .Q3_n(CC_3_1_n[0]), .Q4_n(CC_3_1_n[1]), .Q5_n(CC_3_1_n[2]), .B0_n(PAL_44601_UCYCFSM_b0_n),
    .B1_n(PAL_44601_UCYCFSM_b1_n));
  PAL_16L8_12 PAL_44307_UCYCLK (
    .I0(TERM_n), .I1(CC0_n), .I2(CC_3_1_n[0]), .I3(CC_3_1_n[1]), .I4(CC_3_1_n[2]), .I5(FORM_n), .I6(BRK_n),
    .I7(RWCS_n), .I8(TRAP_n), .I9(VEX), .Y0_n(PAL_44307_UCYCLK_y0_n), .Y1_n(PAL_44307_UCYCLK_y1_n),
    .B0_n(WRFSTB), .B1_n(CYD), .B2_n(EORF_n), .B3_n(PAL_44307_UCYCLK_b3_n), .B4_n(ETRAP_n), .B5_n(MAP_n));
  nand nand_3 (CLK, 1'b1, TERM_n);
  not not_1 (not_1_out, LCS_n);
  nor nor_1 (ALUCLK, TERM_n, not_1_out);
  nand nand_4 (MCLK, TERM_n, PAL_44307_UCYCLK_y0_n);
  nand nand_5 (MACLK, TERM_n, PAL_44307_UCYCLK_y1_n);
  and and_2 (UCLK, TERM_n, PAL_44307_UCYCLK_b3_n);

  // Other names for the same wires on the sheet: CC1_n = CC_3_1_n[0]; CC2_n = CC_3_1_n[1]; CC3_n = CC_3_1_n[2]

  // Notes on the sheet:
  //   CYC
  //   ND120 CPU, MM&M
  //   CYCLE CONTROL
  //   SHEET 36 of 50
  //   MAP_n
  //   The signals needs to be connected in Verilog
  //   The signals needs to be connected in Verilog
  //   15D
  //   The signals needs to be connected in Verilog
  //   14D
  //   NOTE! This logic will not simulate correct in Logisim as PALS needs to be replaced by VERILOG code
  //   LCS_n
  //   DLY0_n
  //   SLCOND_n
  //   SLCOND_n
  //   WAIT1
  //   WAIT2
  //   DLY1_n
  //   The signals needs to be connected in Verilog
  //   DLY1_n
  //   DLY0_n
  //   CSDELAY0
  //   The signals needs to be connected in Verilog
  //   12D
  //   13D
endmodule

module IO_37 (
  input  IOCSB_B,
  input  IO100I_B,
  output [4:0] IOABP_B,
  output [7:0] IDB_7_0_io,
  output [7:0] IDB_15_8,
  output OSC,
  output IOINT
);

  wire DCD_ceuart_n, DCD_eior_n, DCD_pposc, DCD_rinr_n, DCD_ruart_n, DCD_sioc_n, DCD_traald_n,
       REG_MODULE_console_n, UART_da_n, UART_tbmt_n, undriven;
  wire [7:0] REG_MODULE_idb_7_0_io;
  wire [15:0] REG_MODULE_idb_15_0, UART_idb_15_0_io;

  IO_DCD_38 DCD (
    .IDB_7_4(IDB_7_0_io[7:4]), .IDB_3_0_io(IDB_7_0_io[3:0]), .IOCSB_n_0_B(IOCSB_B), .DGA100_n_0_B(IO100I_B),
    .POWSENSE_n(undriven), .PPOSC(DCD_pposc), .OSC(OSC), .IOINT_B(IOINT), .TRAALD_n(DCD_traald_n),
    .SIOC_n(DCD_sioc_n), .RINR_n(DCD_rinr_n), .CEUART_n(DCD_ceuart_n), .RUART_n(DCD_ruart_n),
    .EIOR_n(DCD_eior_n));  // open: OC0, OC1, OSCCL_n, SWMCL_n, SEL5MS_n_B, DCDPANCALI_B, OPCLCS, DCDCNTLI_n_0_B, IOTIM_n_0_B, DCDPANCAL0_B, DCDCNTL0_B
  IO_REG_41 REG_MODULE (
    .TRAALD_n(DCD_traald_n), .SIOC_n(DCD_sioc_n), .DA_n(UART_da_n), .TBMT_n(UART_tbmt_n),
    .RINR_n(DCD_rinr_n), .IDB_15_0(REG_MODULE_idb_15_0), .IDB_7_0_io(REG_MODULE_idb_7_0_io),
    .CONSOLE_n(REG_MODULE_console_n));  // open: CX_n, CLEAR_n, INR_7_0, EMCL_n, BINT12_n, BINT13_n, BINT10_n
  IO_PANCAL_40 PANCAL (
    .DP_5_1_n(IOABP_B), .IDB_15_0({IDB_15_8, IDB_7_0_io}));  // open: PA_7_0, PCR_1_0, PONI, IONI, LHIT, LEV0, EMP_n, PANOSC, CLEAR_n, EPANS, VAL, FUL_n, STAT_4_3, RMM_n
  IO_UART_42 UART (
    .CEUART_n(DCD_ceuart_n), .RUART_n(DCD_ruart_n), .PPOSC(DCD_pposc), .CONSOLE_n(REG_MODULE_console_n),
    .EIOR_n(DCD_eior_n), .IDB_15_0_io(UART_idb_15_0_io), .TBMT_n(UART_tbmt_n), .DA_n(UART_da_n));  // open: LCS_n, MIS_1_0, XTR, I1P, RXD, CLK, EAUTO_n, LOCK_n, O1P, O2P

  // Notes on the sheet:
  //   IO
  //   IO TOP LEVEL
  //   SHEET 37 of 50
  //   ND120 CPU, MM&M
  //   FIX CONNECTIONS IN VERILOG
  //   IDB_7_0
  //   CONNECT IN VERILOG
endmodule

module IO_DCD_38 (
  input  OC0,
  input  OC1,
  input  OSCCL_n,
  input  SWMCL_n,
  input  SEL5MS_n_B,
  input  [3:0] IDB_7_4,
  input  [3:0] IDB_3_0_io,
  input  DCDPANCALI_B,
  input  OPCLCS,
  input  DCDCNTLI_n_0_B,
  input  IOCSB_n_0_B,
  input  IOTIM_n_0_B,
  input  DGA100_n_0_B,
  input  POWSENSE_n,
  output PPOSC,
  output OSC,
  output DCDPANCAL0_B,
  output DCDCNTL0_B,
  output IOINT_B,
  output TRAALD_n,
  output SIOC_n,
  output RINR_n,
  output CEUART_n,
  output RUART_n,
  output EIOR_n
);

  wire CHIP_13C_1_qd, CLOSC, nand_1_out, nand_2_out, nand_4_out, nand_5_out, not_2_out, POWSENSE, PWCL,
       RTOSC, XTAL1_39_3216MHZ_out, XTAL2_35MHZ_out;

  Clock XTAL1_39_3216MHZ (.out(XTAL1_39_3216MHZ_out));
  Clock XTAL2_35MHZ (.out(XTAL2_35MHZ_out));
  not not_1 (POWSENSE, POWSENSE_n);
  not not_2 (not_2_out, OC0);
  nand nand_1 (nand_1_out, XTAL1_39_3216MHZ_out, OC1, OC0);
  nand nand_2 (nand_2_out, OC1, XTAL2_35MHZ_out);
  nand nand_3 (CLOSC, OSCCL_n, 1'b0);
  nand nand_4 (nand_4_out, 1'b0, SWMCL_n);
  nand nand_5 (nand_5_out, not_2_out, nand_2_out);
  or or_1 (PWCL, nand_4_out, OPCLCS);
  nand nand_6 (OSC, nand_1_out, nand_5_out);
  TTL_74393 CHIP_13C_1 (.A_n(XTAL1_39_3216MHZ_out), .CLR(CLOSC), .QC(PPOSC), .QD(CHIP_13C_1_qd));  // open: QA, QB
  TTL_74393 CHIP_13C_2 (.A_n(CHIP_13C_1_qd), .CLR(CLOSC), .QD(RTOSC));  // open: QA, QB, QC

  // Notes on the sheet:
  //   ___DCDABP____
  //   ____DCDCNTLI__B___
  //   ___IO100I_B___
  //   IO/DCD
  //   IO DECODING
  //   SHEET 38 of 50
  //   Estimated HIGH for 500useconds, before going low
  //   Power on clear-oscilator stuff??
  //   ND120 CPU, MM&M
  //   ZENER LOGIC - NOT DRAWN
  //   TODO: FIND OUT WHY THERE IS XTAL2 - AND HOW TO HANDLE IN VERILOG
  //   CONNECT DGA CHIP IN VERILOG
  //   74LS393 Ripple Counter
  //   DIV8
  //   DIV16
  //   =XTAL1 / 8 = 4,9152 MHZ
  //   =XTAL1 / 256 = 153.6KHZ
endmodule

module IO_DCD_DGA_39 (
  input  [3:0] IDB_7_4,
  input  [3:0] IDB_3_0_io,
  input  [1:0] DGAIP,
  input  HIT
);


  // Notes on the sheet:
  //   IO/DCD/DGA
  //   SHEET 39 of 50
  //   ND120 CPU, MM&M
  //   DECODE GATE ARRAY
  //   CONNECT DGA CHIP IN VERILOG
endmodule

module IO_PANCAL_40 (
  input  [7:0] PA_7_0,
  input  [1:0] PCR_1_0,
  input  PONI,
  input  IONI,
  input  LHIT,
  input  LEV0,
  input  EMP_n,
  input  PANOSC,
  input  CLEAR_n,
  input  EPANS,
  input  VAL,
  input  FUL_n,
  output [4:0] DP_5_1_n,
  output [1:0] STAT_4_3,
  output [15:0] IDB_15_0,
  output RMM_n
);


  // Notes on the sheet:
  //   IO/PANCAL
  //   ND120 CPU, MM&M
  //   PANEL PROC & CALENDAR
  //   SHEET 40 of 50
  //   NEEDS TO BE DONE IN VERILOG
  //   DISP1-DISP5 (Display?)
endmodule

module IO_REG_41 (
  input  CX_n,
  input  TRAALD_n,
  input  SIOC_n,
  input  CLEAR_n,
  input  DA_n,
  input  TBMT_n,
  input  [7:0] INR_7_0,
  input  RINR_n,
  output [15:0] IDB_15_0,
  output [7:0] IDB_7_0_io,
  output CONSOLE_n,
  output EMCL_n,
  output BINT12_n,
  output BINT13_n,
  output BINT10_n
);

  wire and_1_out, CHIP_28A_IOC_q2, CHIP_28A_IOC_q4, CHIP_28A_IOC_q5, CHIP_28A_IOC_q6, CHIP_28A_IOC_q7,
       CHIP_28A_IOC_q8, not_1_out, not_2_out, RESET;
  wire [7:0] CHIP_24A_INR_o7_2y4;

  TTL_74244 CHIP_27A_STRAP (
    .I0_1A1(1'b1), .I1_1A2(1'b1), .I2_1A3(1'b1), .I3_1A4(1'b0), .OE1_1G_n(TRAALD_n), .I4_2A1(1'b0),
    .I5_2A2(1'b0), .I6_2A3(1'b0), .I7_2A4(1'b0), .OE2_2G_n(TRAALD_n), .O0_1Y1(IDB_15_0[15]),
    .O1_1Y2(IDB_15_0[14]), .O2_1Y3(IDB_15_0[13]), .O3_1Y4(IDB_15_0[12]), .O4_2Y1(IDB_15_0[11]),
    .O5_2Y2(IDB_15_0[10]), .O6_2Y3(IDB_15_0[9]), .O7_2Y4(IDB_15_0[8]));
  TTL_74244 CHIP_25A_ALD (
    .I0_1A1(CX_n), .I1_1A2(1'b0), .I2_1A3(1'b1), .I3_1A4(1'b1), .OE1_1G_n(TRAALD_n), .I4_2A1(1'b1),
    .I5_2A2(1'b1), .I6_2A3(1'b1), .I7_2A4(1'b1), .OE2_2G_n(TRAALD_n), .O0_1Y1(IDB_7_0_io[7]),
    .O1_1Y2(IDB_7_0_io[6]), .O2_1Y3(IDB_7_0_io[5]), .O3_1Y4(IDB_7_0_io[4]), .O4_2Y1(IDB_7_0_io[3]),
    .O5_2Y2(IDB_7_0_io[2]), .O6_2Y3(IDB_7_0_io[1]), .O7_2Y4(IDB_7_0_io[0]));
  TTL_74244 CHIP_24A_INR (
    .I0_1A1(INR_7_0[7]), .I1_1A2(INR_7_0[6]), .I2_1A3(INR_7_0[5]), .I3_1A4(INR_7_0[4]), .OE1_1G_n(RINR_n),
    .I4_2A1(INR_7_0[3]), .I5_2A2(INR_7_0[2]), .I6_2A3(INR_7_0[1]), .I7_2A4(INR_7_0[0]), .OE2_2G_n(RINR_n),
    .O0_1Y1(CHIP_24A_INR_o7_2y4[7]), .O1_1Y2(CHIP_24A_INR_o7_2y4[6]), .O2_1Y3(CHIP_24A_INR_o7_2y4[5]),
    .O3_1Y4(CHIP_24A_INR_o7_2y4[4]), .O4_2Y1(CHIP_24A_INR_o7_2y4[3]), .O5_2Y2(CHIP_24A_INR_o7_2y4[2]),
    .O6_2Y3(CHIP_24A_INR_o7_2y4[1]), .O7_2Y4(CHIP_24A_INR_o7_2y4[0]));
  LED #(.active("false")) RED (.in(EMCL_n));
  TTL_74273 CHIP_28A_IOC (
    .D1(IDB_7_0_io[7]), .D2(IDB_7_0_io[6]), .D3(IDB_7_0_io[5]), .D4(IDB_7_0_io[4]), .D5(IDB_7_0_io[3]),
    .D6(IDB_7_0_io[2]), .D7(IDB_7_0_io[1]), .D8(IDB_7_0_io[0]), .CK(SIOC_n), .CL_n(CLEAR_n), .Q1(RESET),
    .Q2(CHIP_28A_IOC_q2), .Q3(EMCL_n), .Q4(CHIP_28A_IOC_q4), .Q5(CHIP_28A_IOC_q5), .Q6(CHIP_28A_IOC_q6),
    .Q7(CHIP_28A_IOC_q7), .Q8(CHIP_28A_IOC_q8));
  LED #(.active("false")) GREEN (.in(CHIP_28A_IOC_q4));
  and and_1 (and_1_out, CHIP_28A_IOC_q2, CHIP_28A_IOC_q7);
  not not_1 (not_1_out, DA_n);
  nand nand_1 (BINT13_n, CHIP_28A_IOC_q5, CHIP_28A_IOC_q8);
  nand nand_2 (BINT10_n, CHIP_28A_IOC_q6, TBMT_n);
  not not_2 (not_2_out, CHIP_28A_IOC_q2);
  nand nand_3 (CONSOLE_n, not_2_out, not_2_out);
  nand nand_4 (BINT12_n, and_1_out, not_1_out);

  assign IDB_15_0[7:0] = IDB_7_0_io;

  // Notes on the sheet:
  //   IO/REG
  //   Physical STRAP #2
  //   ALD-SETTINGS = 0 (TH1)
  //   (need config in verilog)
  //   ND120 CPU, MM&M
  //   IOC, ALD & INR REGS
  //   SHEET 41 of 50
  //   probably to be use for STRAP later?
  //   STRAP VALAUE (STR-9 to STR-5)
  //   PRINT VERSION = 011 FOR VERSION D
  //   STR5
  //   STR6
  //   STR7
  //   STR8
  //   STR9
  //   ECO Fixes for 3202D and their strap settings: http://norsk-data.com/library/libeco/libeco100.html
  //   IDB15
  //   IDB14
  //   IDB7
  //   IDB0
  //   The signals needs to be connected in Verilog
  //   IDB7
  //   IDB0
  //   LED2
  //   IOC3
  //   IOC2
  //   IOC1
  //   IOC0
  //   LED3
  //   SCONS_n
endmodule

module IO_UART_42 (
  input  LCS_n,
  input  CEUART_n,
  input  RUART_n,
  input  [1:0] MIS_1_0,
  input  PPOSC,
  input  XTR,
  input  I1P,
  input  RXD,
  input  CLK,
  input  EAUTO_n,
  input  LOCK_n,
  input  CONSOLE_n,
  input  EIOR_n,
  output [15:0] IDB_15_0_io,
  output O1P,
  output TBMT_n,
  output O2P,
  output DA_n
);

  wire not_1_out, RD;
  wire [7:0] CHIP_32H_d_7_0;

  not not_1 (not_1_out, LCS_n);
  SC2661_UART CHIP_32H (
    .RESET(not_1_out), .CE_n(CEUART_n), .READ_n(RUART_n), .A0(MIS_1_0[0]), .A1(MIS_1_0[1]), .BRCLK(PPOSC),
    .RXC_n(XTR), .TXC_n(XTR), .DCD_n(1'b0), .DSR_n(1'b0), .CTS_n(1'b0), .RXD(RD), .D_7_0(CHIP_32H_d_7_0),
    .TXD(O1P), .TXDRDY_n(TBMT_n), .RXDRDY_n(DA_n));  // open: TXEMT_n, DTR_n, RTS_n
  AM29C821 CHIP_33G (
    .CK(CLK), .D0(TBMT_n), .D1(DA_n), .D2(EAUTO_n), .D3(LOCK_n), .D4(CONSOLE_n), .D5(1'b0), .D6(1'b0),
    .D7(1'b0), .D8(1'b0), .D9(1'b0), .OE_n(EIOR_n), .Y0(IDB_15_0_io[15]), .Y1(IDB_15_0_io[14]),
    .Y2(IDB_15_0_io[13]), .Y3(IDB_15_0_io[12]), .Y4(IDB_15_0_io[11]), .Y5(IDB_15_0_io[4]),
    .Y6(IDB_15_0_io[3]), .Y7(IDB_15_0_io[2]), .Y8(IDB_15_0_io[1]), .Y9(IDB_15_0_io[0]));
  or or_1 (RD, I1P, RXD);

  assign O2P = O1P;

  // Notes on the sheet:
  //   ND120 CPU, MM&M
  //   IO/UART
  //   UART & IOR REG
  //   SHEET 42 of 50
  //   MIS0
  //   MIS1
  //   BAUD RATE CONTROL
  //   TH2 Switch not in this drawing
  //   (Not connected)
  //   The signals needs to be connected in Verilog
  //   IDB15
  //   IDB14
  //   IDB13
  //   IDB12
  //   IDB11
  //   IDB4
  //   IDB0
  //   Power supply components not drawn!
  //   RS-232 +/-12 circuit not drawn!
  //   RS-232 receive circuit not drawn (simplified!)
endmodule

module MEM_43 (
);

  MEM_ADEC_45 ADEC ();
  MEM_DATA_46 DATA ();
  MEM_LBDIF_48 LBDIF ();  // open: OSC, BLRQ_n, CGNT_n, BGNT_n, BCGNT25, HIEN_n, LOEN_n, ECCR, BDAP50_n, MR_n, BIOXE_n, RAS, BLOCKL_n, MWRITE_n, REF_n, MOR_n, GNT_n, PD4, BGNT25_n, CGNT25_n, BLRQ50_n, RDATA25_n, BGNT50_n, CGNT50_n, BCGNT50, BCGNT50R_n, RDATA, BIOXL_n, BDRY_n, BLOCKL25_n, MWRITE50_n, MOR25_n, GNT50_n
  MEM_ERROR_47 ERROR ();  // open: FETCH, CGNT50_n, CORR_n, HIERR, LOERR, LBD_23_0, RDATA25, BLOCKL25, BCGNT50, PS_n, RERR_n, PA_n, PD4, LERR_n, MR_n, IDB_15_0, BLOCK_n
  MEM_RAMC_50 RAMC ();  // open: OSC, BDAP50_n, MR_n, RLRQ_n, CLRQ_n, BLRQ50_n, BGNT25_n, SSEMA_n, CGNT25_n, SEMRQ50_n, BDRY50_n, PD3, PD1, RGNT_n, CGNT_n, BGNT_n, QD_n, RAS, CAS, LOEN_n, HIEN_n, BGNT25
  MEM_ADDR_44 ADDR ();  // open: LBD_0_8_18, LOEN_n, BCGNT50, HIEN_n, LBD_9_17_19, PD4, AA_9_0
  MEM_RAM_49 RAM ();  // open: AA_9_0, MWRITE50_n, RAS, BANK0, BANK1, BANK2, CAS, CORR_n, BD_17_0_io

  // Notes on the sheet:
  //   ND120 CPU, MM&M
  //   MEM
  //   MEMORY TOP LEVEL
  //   SHEET 43 of 50
endmodule

module MEM_ADDR_44 (
  input  [9:0] LBD_0_8_18,
  input  LOEN_n,
  input  BCGNT50,
  input  HIEN_n,
  input  [9:0] LBD_9_17_19,
  input  PD4,
  output [9:0] AA_9_0
);

  wire CHIP_4H_COL_ADDRESS_y0, CHIP_4H_COL_ADDRESS_y1, CHIP_4H_COL_ADDRESS_y2, CHIP_4H_COL_ADDRESS_y3,
       CHIP_4H_COL_ADDRESS_y4, CHIP_4H_COL_ADDRESS_y5, CHIP_4H_COL_ADDRESS_y6, CHIP_4H_COL_ADDRESS_y7,
       CHIP_4H_COL_ADDRESS_y8, CHIP_4H_COL_ADDRESS_y9;

  AM29C821 CHIP_3H_ROW_ADDRESS (
    .CK(BCGNT50), .D0(LBD_0_8_18[0]), .D1(LBD_0_8_18[1]), .D2(LBD_0_8_18[2]), .D3(LBD_0_8_18[3]),
    .D4(LBD_0_8_18[4]), .D5(LBD_0_8_18[5]), .D6(LBD_0_8_18[6]), .D7(LBD_0_8_18[7]), .D8(LBD_0_8_18[8]),
    .D9(LBD_0_8_18[9]), .OE_n(LOEN_n));  // open: Y0, Y1, Y2, Y3, Y4, Y5, Y6, Y7, Y8, Y9
  AM29C821 CHIP_4H_COL_ADDRESS (
    .CK(BCGNT50), .D0(LBD_9_17_19[0]), .D1(LBD_9_17_19[1]), .D2(LBD_9_17_19[2]), .D3(LBD_9_17_19[3]),
    .D4(LBD_9_17_19[4]), .D5(LBD_9_17_19[5]), .D6(LBD_9_17_19[6]), .D7(LBD_9_17_19[7]), .D8(LBD_9_17_19[8]),
    .D9(LBD_9_17_19[9]), .OE_n(HIEN_n), .Y0(CHIP_4H_COL_ADDRESS_y0), .Y1(CHIP_4H_COL_ADDRESS_y1),
    .Y2(CHIP_4H_COL_ADDRESS_y2), .Y3(CHIP_4H_COL_ADDRESS_y3), .Y4(CHIP_4H_COL_ADDRESS_y4),
    .Y5(CHIP_4H_COL_ADDRESS_y5), .Y6(CHIP_4H_COL_ADDRESS_y6), .Y7(CHIP_4H_COL_ADDRESS_y7),
    .Y8(CHIP_4H_COL_ADDRESS_y8), .Y9(CHIP_4H_COL_ADDRESS_y9));
  AM29861A CHIP_5H (
    .R0(CHIP_4H_COL_ADDRESS_y0), .R1(CHIP_4H_COL_ADDRESS_y1), .R2(CHIP_4H_COL_ADDRESS_y2),
    .R3(CHIP_4H_COL_ADDRESS_y3), .R4(CHIP_4H_COL_ADDRESS_y4), .R5(CHIP_4H_COL_ADDRESS_y5),
    .R6(CHIP_4H_COL_ADDRESS_y6), .R7(CHIP_4H_COL_ADDRESS_y7), .R8(CHIP_4H_COL_ADDRESS_y8),
    .R9(CHIP_4H_COL_ADDRESS_y9), .OER_n(1'b1), .OET_n(PD4), .T0(AA_9_0[0]), .T1(AA_9_0[1]), .T2(AA_9_0[2]),
    .T3(AA_9_0[3]), .T4(AA_9_0[4]), .T5(AA_9_0[5]), .T6(AA_9_0[6]), .T7(AA_9_0[7]), .T8(AA_9_0[8]),
    .T9(AA_9_0[9]));

  // Notes on the sheet:
  //   ND120 CPU, MM&M
  //   MEM/ADDR
  //   MEM ADDR MUX
  //   SHEET 44 of 50
  //   The signals needs to be connected in Verilog
  //   MEM ADDR MUX
  //   The signals needs to be connected in Verilog
  //   Not included: resistor network A->AA
endmodule

module MEM_ADEC_45 (
);


  // Notes on the sheet:
  //   ND120 CPU, MM&M
  //   MEM/ADEC
  //   ADDRESS DECODERS
  //   SHEET 45 of 50
endmodule

module MEM_DATA_46 (
);


  // Notes on the sheet:
  //   ND120 CPU, MM&M
  //   MEM/DATA
  //   DATA & PARITY TCV
  //   SHEET 46 of 50
endmodule

module MEM_ERROR_47 (
  input  FETCH,
  input  CGNT50_n,
  input  CORR_n,
  input  HIERR,
  input  LOERR,
  input  [23:0] LBD_23_0,
  input  RDATA25,
  input  BLOCKL25,
  input  BCGNT50,
  input  PS_n,
  input  RERR_n,
  input  PA_n,
  input  PD4,
  input  LERR_n,
  input  MR_n,
  output [15:0] IDB_15_0,
  output BLOCK_n
);

  wire PAL_45009_UERROR_b0_n, PAL_45009_UERROR_b1_n, PAL_45009_UERROR_y0_n, PAL_45009_UERROR_y1_n;
  wire [7:0] CHIP_3C_PESL_LO_q8, CHIP_7C_PESL_HI_q8;

  TTL_74374 CHIP_7C_PESL_HI (
    .D1(FETCH), .D2(CGNT50_n), .D3(1'b1), .D4(1'b1), .D5(1'b1), .D6(CORR_n), .D7(HIERR), .D8(LOERR),
    .CK(PAL_45009_UERROR_y0_n), .OE_n(PAL_45009_UERROR_b0_n), .Q1(CHIP_7C_PESL_HI_q8[7]),
    .Q2(CHIP_7C_PESL_HI_q8[6]), .Q3(CHIP_7C_PESL_HI_q8[5]), .Q4(CHIP_7C_PESL_HI_q8[4]),
    .Q5(CHIP_7C_PESL_HI_q8[3]), .Q6(CHIP_7C_PESL_HI_q8[2]), .Q7(CHIP_7C_PESL_HI_q8[1]),
    .Q8(CHIP_7C_PESL_HI_q8[0]));
  TTL_74374 CHIP_3C_PESL_LO (
    .D1(LBD_23_0[23]), .D2(LBD_23_0[22]), .D3(LBD_23_0[21]), .D4(LBD_23_0[20]), .D5(LBD_23_0[19]),
    .D6(LBD_23_0[18]), .D7(LBD_23_0[17]), .D8(LBD_23_0[16]), .CK(PAL_45009_UERROR_y1_n),
    .OE_n(PAL_45009_UERROR_b0_n), .Q1(CHIP_3C_PESL_LO_q8[7]), .Q2(CHIP_3C_PESL_LO_q8[6]),
    .Q3(CHIP_3C_PESL_LO_q8[5]), .Q4(CHIP_3C_PESL_LO_q8[4]), .Q5(CHIP_3C_PESL_LO_q8[3]),
    .Q6(CHIP_3C_PESL_LO_q8[2]), .Q7(CHIP_3C_PESL_LO_q8[1]), .Q8(CHIP_3C_PESL_LO_q8[0]));
  PAL_16L8_12 PAL_45009_UERROR (
    .I0(RDATA25), .I1(BLOCKL25), .I2(BCGNT50), .I3(PS_n), .I4(RERR_n), .I5(PA_n), .I6(PD4), .I7(LERR_n),
    .I9(MR_n), .Y0_n(PAL_45009_UERROR_y0_n), .Y1_n(PAL_45009_UERROR_y1_n), .B0_n(PAL_45009_UERROR_b0_n),
    .B1_n(PAL_45009_UERROR_b1_n), .B2_n(BLOCK_n));  // open: I8, B3_n, B4_n, B5_n
  TTL_74374 CHIP_4C_PEAL_HI (
    .D1(LBD_23_0[15]), .D2(LBD_23_0[14]), .D3(LBD_23_0[13]), .D4(LBD_23_0[12]), .D5(LBD_23_0[11]),
    .D6(LBD_23_0[10]), .D7(LBD_23_0[9]), .D8(LBD_23_0[8]), .CK(PAL_45009_UERROR_y1_n),
    .OE_n(PAL_45009_UERROR_b1_n), .Q1(IDB_15_0[15]), .Q2(IDB_15_0[14]), .Q3(IDB_15_0[13]), .Q4(IDB_15_0[12]),
    .Q5(IDB_15_0[11]), .Q6(IDB_15_0[10]), .Q7(IDB_15_0[9]), .Q8(IDB_15_0[8]));
  TTL_74374 CHIP_6D_PEAL_LO (
    .D1(LBD_23_0[7]), .D2(LBD_23_0[6]), .D3(LBD_23_0[5]), .D4(LBD_23_0[4]), .D5(LBD_23_0[3]),
    .D6(LBD_23_0[2]), .D7(LBD_23_0[1]), .D8(LBD_23_0[0]), .CK(PAL_45009_UERROR_y1_n),
    .OE_n(PAL_45009_UERROR_b1_n), .Q1(IDB_15_0[7]), .Q2(IDB_15_0[6]), .Q3(IDB_15_0[5]), .Q4(IDB_15_0[4]),
    .Q5(IDB_15_0[3]), .Q6(IDB_15_0[2]), .Q7(IDB_15_0[1]), .Q8(IDB_15_0[0]));

  // Notes on the sheet:
  //   ND120 CPU, MM&M
  //   MEM/ERROR
  //   LOCAL PES & PEA
  //   SHEET 47 of 50
  //   The signals needs to be connected in Verilog
  //   FATAL
  //   SPEAL
  //   EPESL_n
  //   SPESL
  //   IDB15
  //   IDB8
  //   IDB7
  //   IDB0
  //   SPESL
  //   SPEAL
  //   EPESL_n
  //   EPEAL_n
  //   LBD15
  //   LBD8
  //   LBD7
  //   LBD0
  //   The signals needs to be connected in Verilog
  //   IDB15
  //   IDB8
  //   IDB7
  //   IDB0
endmodule

module MEM_LBDIF_48 (
  input  OSC,
  input  BLRQ_n,
  input  CGNT_n,
  input  BGNT_n,
  input  BCGNT25,
  input  HIEN_n,
  input  LOEN_n,
  input  ECCR,
  input  BDAP50_n,
  input  MR_n,
  input  BIOXE_n,
  input  RAS,
  input  BLOCKL_n,
  input  MWRITE_n,
  input  REF_n,
  input  MOR_n,
  input  GNT_n,
  input  PD4,
  output BGNT25_n,
  output CGNT25_n,
  output BLRQ50_n,
  output RDATA25_n,
  output BGNT50_n,
  output CGNT50_n,
  output BCGNT50,
  output BCGNT50R_n,
  output RDATA,
  output BIOXL_n,
  output BDRY_n,
  output BLOCKL25_n,
  output MWRITE50_n,
  output MOR25_n,
  output GNT50_n
);

  wire CHIP_13F_y0, CHIP_13F_y8, CHIP_14F_y1, CHIP_14F_y3, CHIP_14F_y4, CHIP_14F_y5, CHIP_14F_y6,
       CHIP_14F_y8, PAL_44310_ULBDIF_b0_n, PAL_44310_ULBDIF_b2_n, PAL_44310_ULBDIF_b3_n,
       PAL_44310_ULBDIF_b4_n, PAL_44310_ULBDIF_b5_n, undriven, undriven_2, undriven_3, undriven_4;

  AM29C821 CHIP_13F (
    .CK(OSC), .D0(BLRQ_n), .D1(CHIP_13F_y0), .D2(RDATA), .D4(CGNT_n), .D5(CGNT25_n), .D6(BGNT_n),
    .D7(BGNT25_n), .D8(BGNT50_n), .D9(BCGNT25), .OE_n(PD4), .Y0(CHIP_13F_y0), .Y1(BLRQ50_n), .Y2(RDATA25_n),
    .Y4(CGNT25_n), .Y5(CGNT50_n), .Y6(BGNT25_n), .Y7(BGNT50_n), .Y8(CHIP_13F_y8), .Y9(BCGNT50));  // open: D3, Y3
  AM29C821 CHIP_14F (
    .CK(OSC), .D0(BLOCKL_n), .D1(MWRITE_n), .D2(CHIP_14F_y1), .D3(REF_n), .D4(undriven), .D5(undriven_2),
    .D6(undriven_3), .D7(MOR_n), .D8(GNT_n), .D9(undriven_4), .OE_n(PD4), .Y0(BLOCKL25_n), .Y1(CHIP_14F_y1),
    .Y2(MWRITE50_n), .Y3(CHIP_14F_y3), .Y4(CHIP_14F_y4), .Y5(CHIP_14F_y5), .Y6(CHIP_14F_y6), .Y7(MOR25_n),
    .Y8(CHIP_14F_y8), .Y9(GNT50_n));
  PAL_16L8_12 PAL_44310_ULBDIF (
    .I0(HIEN_n), .I1(BGNT_n), .I2(CGNT_n), .I3(LOEN_n), .I4(CGNT50_n), .I5(ECCR), .I6(BGNT50_n),
    .I7(CHIP_13F_y8), .I8(BDAP50_n), .I9(MR_n), .Y0_n(BCGNT50R_n), .Y1_n(RDATA),
    .B0_n(PAL_44310_ULBDIF_b0_n), .B1_n(BIOXL_n), .B2_n(PAL_44310_ULBDIF_b2_n), .B3_n(PAL_44310_ULBDIF_b3_n),
    .B4_n(PAL_44310_ULBDIF_b4_n), .B5_n(PAL_44310_ULBDIF_b5_n));
  buf buffer_1 (BDRY_n, PAL_44310_ULBDIF_b0_n);

  // Notes on the sheet:
  //   ND120 CPU, MM&M
  //   MEM/LBDIF
  //   LOCAL BD CONTROL
  //   SHEET 48 of 50
  //   The signals needs to be connected in Verilog
  //   n.c.
  //   CONNECT IN VERILOG
  //   CONNECT IN VERILOG
  //   CONNECT IN VERILOG
  //   n.c.
  //   CGNT25_n
  //   CGNT50_n
  //   BGNT25_n
  //   BGNT50_n
  //   BGNT75_n
  //   REF100_n
  //   The signals needs to be connected in Verilog
  //   REF100_n
endmodule

module MEM_RAM_49 (
  input  [9:0] AA_9_0,
  input  MWRITE50_n,
  input  RAS,
  input  BANK0,
  input  BANK1,
  input  BANK2,
  input  CAS,
  output CORR_n,
  output [17:0] BD_17_0_io
);

  wire CHIP_15H_d9, CHIP_15H_prd_n, CHIP_15H_q9, CHIP_15J_d9, CHIP_15J_prd_n, CHIP_15J_q9, CHIP_15K_d9,
       CHIP_15K_prd_n, CHIP_15K_q9, CHIP_15L_d9, CHIP_15L_prd_n, CHIP_15L_q9, CHIP_15M_d9, CHIP_15M_prd_n,
       CHIP_15M_q9, CHIP_15N_d9, CHIP_15N_prd_n, CHIP_15N_q9, nand_1_out, nand_2_out, nand_3_out, nand_4_out,
       nand_5_out, nand_6_out, or_7_out;
  wire [7:0] CHIP_15K_dq_8_1_io, CHIP_15L_dq_8_1_io, CHIP_15M_dq_8_1_io, CHIP_15N_dq_8_1_io;
  wire [17:0] CHIP_15H_dq_8_1_io;
  wire [17:8] or_3_out, or_5_out;

  nand nand_1 (nand_1_out, RAS, BANK0);
  nand nand_2 (nand_2_out, BANK0, CAS);
  SIP1M9 CHIP_15H (
    .AA_9_0(AA_9_0), .RAS_n(nand_1_out), .CAS_n(nand_2_out), .CAS9_n(nand_2_out), .W_n(MWRITE50_n),
    .DQ_8_1_io(CHIP_15H_dq_8_1_io[7:0]), .Q9(CHIP_15H_q9), .D9(CHIP_15H_d9), .PRD_n(CHIP_15H_prd_n));
  or or_1 (CHIP_15H_dq_8_1_io[8], CHIP_15H_q9, CHIP_15H_d9);
  SIP1M9 CHIP_15J (
    .AA_9_0(AA_9_0), .RAS_n(nand_1_out), .CAS_n(nand_2_out), .CAS9_n(nand_2_out), .W_n(MWRITE50_n),
    .DQ_8_1_io(CHIP_15H_dq_8_1_io[16:9]), .Q9(CHIP_15J_q9), .D9(CHIP_15J_d9), .PRD_n(CHIP_15J_prd_n));
  or or_2 (CHIP_15H_dq_8_1_io[17], CHIP_15J_q9, CHIP_15J_d9);
  nand nand_3 (nand_3_out, RAS, BANK1);
  nand nand_4 (nand_4_out, BANK1, CAS);
  SIP1M9 CHIP_15K (
    .AA_9_0(AA_9_0), .RAS_n(nand_3_out), .CAS_n(nand_4_out), .CAS9_n(nand_4_out), .W_n(MWRITE50_n),
    .DQ_8_1_io(CHIP_15K_dq_8_1_io), .Q9(CHIP_15K_q9), .D9(CHIP_15K_d9), .PRD_n(CHIP_15K_prd_n));
  or or_3 (or_3_out[8], CHIP_15K_q9, CHIP_15K_d9);
  SIP1M9 CHIP_15L (
    .AA_9_0(AA_9_0), .RAS_n(nand_3_out), .CAS_n(nand_4_out), .CAS9_n(nand_4_out), .W_n(MWRITE50_n),
    .DQ_8_1_io(CHIP_15L_dq_8_1_io), .Q9(CHIP_15L_q9), .D9(CHIP_15L_d9), .PRD_n(CHIP_15L_prd_n));
  or or_4 (or_3_out[17], CHIP_15L_q9, CHIP_15L_d9);
  nand nand_5 (nand_5_out, RAS, BANK2);
  nand nand_6 (nand_6_out, BANK2, CAS);
  SIP1M9 CHIP_15M (
    .AA_9_0(AA_9_0), .RAS_n(nand_5_out), .CAS_n(nand_6_out), .CAS9_n(nand_6_out), .W_n(MWRITE50_n),
    .DQ_8_1_io(CHIP_15M_dq_8_1_io), .Q9(CHIP_15M_q9), .D9(CHIP_15M_d9), .PRD_n(CHIP_15M_prd_n));
  SIP1M9 CHIP_15N (
    .AA_9_0(AA_9_0), .RAS_n(nand_5_out), .CAS_n(nand_6_out), .CAS9_n(nand_6_out), .W_n(MWRITE50_n),
    .DQ_8_1_io(CHIP_15N_dq_8_1_io), .Q9(CHIP_15N_q9), .D9(CHIP_15N_d9), .PRD_n(CHIP_15N_prd_n));
  or or_5 (or_5_out[8], CHIP_15M_q9, CHIP_15M_d9);
  or or_6 (or_5_out[17], CHIP_15N_q9, CHIP_15N_d9);
  or or_7 (or_7_out, ~CHIP_15M_prd_n, ~CHIP_15K_prd_n, ~CHIP_15H_prd_n, ~CHIP_15J_prd_n, ~CHIP_15L_prd_n, ~CHIP_15N_prd_n);  // OR_Gate
  not not_1 (CORR_n, or_7_out);

  // Notes on the sheet:
  //   ND120 CPU, MM&M
  //   MEM/RAM
  //   LOCAL RAM
  //   SHEET 49 of 50
  //   The signals needs to be connected in Verilog
  //   Redesigned Q9/D9 logic to use OR
  //   PRD_n bus signal to use OR
  //   The signals needs to be connected in Verilog
  //   Re-Architected the CORR_n signal bus
endmodule

module MEM_RAMC_50 (
  input  OSC,
  input  BDAP50_n,
  input  MR_n,
  input  RLRQ_n,
  input  CLRQ_n,
  input  BLRQ50_n,
  input  BGNT25_n,
  input  SSEMA_n,
  input  CGNT25_n,
  input  SEMRQ50_n,
  input  BDRY50_n,
  input  PD3,
  input  PD1,
  output RGNT_n,
  output CGNT_n,
  output BGNT_n,
  output QD_n,
  output RAS,
  output CAS,
  output LOEN_n,
  output HIEN_n,
  output BGNT25
);

  PAL_16R8D PAL_44803_URAMA (
    .CK(OSC), .I0(LOEN_n), .I1(RLRQ_n), .I2(MR_n), .I3(CLRQ_n), .I4(BLRQ50_n), .I5(SSEMA_n), .I6(SEMRQ50_n),
    .OE_n(PD1), .Q0_n(RGNT_n), .Q1_n(CGNT_n), .Q2_n(BGNT_n), .Q7_n(BGNT25));  // open: I7, Q3_n, Q4_n, Q5_n, Q6_n
  LED #(.active("false")) CPU_GRANT_INDICATOR (.in(CGNT_n));
  LED #(.active("false")) BUS_GRANT_INDICATOR (.in(BGNT_n));
  PAL_16R8D PAL_44902_URAMC (
    .CK(OSC), .I0(RGNT_n), .I1(CGNT_n), .I2(BGNT_n), .I3(BDAP50_n), .I4(MR_n), .I5(BGNT25_n), .I6(CGNT25_n),
    .I7(BDRY50_n), .OE_n(PD3), .Q3_n(QD_n), .Q4_n(RAS), .Q5_n(CAS), .Q6_n(LOEN_n), .Q7_n(HIEN_n));  // open: Q0_n, Q1_n, Q2_n

  // Notes on the sheet:
  //   ND120 CPU, MM&M
  //   MEM/RAMC
  //   LOCAL RAM CONTROL
  //   SHEET 50 of 50
  //   RAM ARBITER
  //   5F
  //   LOEN25_n (n.c)
  //   LDR_n (n.c)
  //   CSEM_n (n.c)
  //   BSEM_n (n.c)
  //   RGNT_n
  //   CGNT_n
  //   BGNT_n
  //   NB! Grant indicator circuits simplified (not as the schematics)
  //   RAM CONTROL
  //   6F
  //   QA_n (n.c)
  //   QB_n (n.c)
  //   QC_n (n.c)
endmodule

module AM29C821 (
  input  CK,
  input  D0,
  input  D1,
  input  D2,
  input  D3,
  input  D4,
  input  D5,
  input  D6,
  input  D7,
  input  D8,
  input  D9,
  input  OE_n,
  output Y0,
  output Y1,
  output Y2,
  output Y3,
  output Y4,
  output Y5,
  output Y6,
  output Y7,
  output Y8,
  output Y9
);

  wire d_ff_1_q, d_ff_2_q, d_ff_3_q, d_ff_4_q, d_ff_5_q, d_ff_6_q, d_ff_7_q, d_ff_8_q, d_ff_9_q, d_ff_10_q,
       not_1_out;

  not not_1 (not_1_out, OE_n);
  D_Flip_Flop d_ff_1 (.D(D0), .clk(CK), .Q(d_ff_1_q));  // open: Qn, preset, reset
  D_Flip_Flop d_ff_2 (.D(D1), .clk(CK), .Q(d_ff_2_q));  // open: Qn, preset, reset
  D_Flip_Flop d_ff_3 (.D(D2), .clk(CK), .Q(d_ff_3_q));  // open: Qn, preset, reset
  D_Flip_Flop d_ff_4 (.D(D3), .clk(CK), .Q(d_ff_4_q));  // open: Qn, preset, reset
  D_Flip_Flop d_ff_5 (.D(D4), .clk(CK), .Q(d_ff_5_q));  // open: Qn, preset, reset
  D_Flip_Flop d_ff_6 (.D(D5), .clk(CK), .Q(d_ff_6_q));  // open: Qn, preset, reset
  D_Flip_Flop d_ff_7 (.D(D6), .clk(CK), .Q(d_ff_7_q));  // open: Qn, preset, reset
  D_Flip_Flop d_ff_8 (.D(D7), .clk(CK), .Q(d_ff_8_q));  // open: Qn, preset, reset
  D_Flip_Flop d_ff_9 (.D(D8), .clk(CK), .Q(d_ff_9_q));  // open: Qn, preset, reset
  D_Flip_Flop d_ff_10 (.D(D9), .clk(CK), .Q(d_ff_10_q));  // open: Qn, preset, reset
  assign Y0 = not_1_out ? d_ff_1_q : 1'bz;  // Controlled_Buffer controlled_buffer_1
  assign Y1 = not_1_out ? d_ff_2_q : 1'bz;  // Controlled_Buffer controlled_buffer_2
  assign Y2 = not_1_out ? d_ff_3_q : 1'bz;  // Controlled_Buffer controlled_buffer_3
  assign Y3 = not_1_out ? d_ff_4_q : 1'bz;  // Controlled_Buffer controlled_buffer_4
  assign Y4 = not_1_out ? d_ff_5_q : 1'bz;  // Controlled_Buffer controlled_buffer_5
  assign Y5 = not_1_out ? d_ff_6_q : 1'bz;  // Controlled_Buffer controlled_buffer_6
  assign Y6 = not_1_out ? d_ff_7_q : 1'bz;  // Controlled_Buffer controlled_buffer_7
  assign Y7 = not_1_out ? d_ff_8_q : 1'bz;  // Controlled_Buffer controlled_buffer_8
  assign Y8 = not_1_out ? d_ff_9_q : 1'bz;  // Controlled_Buffer controlled_buffer_9
  assign Y9 = not_1_out ? d_ff_10_q : 1'bz;  // Controlled_Buffer controlled_buffer_10

  // Notes on the sheet:
  //   AM29C821
  //   Bus Driver 10 bits  - Bus Driver 10 bits. Positive edge-triggered registeres with D-type flip-flops and 3-state
  //   https://www.digikey.com/en/products/detail/rochester-electronics-llc/AM29C821-BLA/12095382
endmodule

module AM29841 (
  input  D0,
  input  D1,
  input  D2,
  input  D3,
  input  D4,
  input  D5,
  input  D6,
  input  D7,
  input  D8,
  input  D9,
  input  LE,
  input  OE_n,
  output Y0,
  output Y1,
  output Y2,
  output Y3,
  output Y4,
  output Y5,
  output Y6,
  output Y7,
  output Y8,
  output Y9
);

  wire LATCH_1_q, LATCH_2_q, LATCH_3_q, LATCH_4_q, LATCH_5_q, LATCH_6_q, LATCH_7_q, LATCH_8_q, LATCH_9_q,
       LATCH_10_q, not_1_out;

  not not_1 (not_1_out, OE_n);
  LATCH LATCH_1 (.D(D0), .ENABLE(LE), .Q(LATCH_1_q));  // open: QN
  LATCH LATCH_2 (.D(D1), .ENABLE(LE), .Q(LATCH_2_q));  // open: QN
  LATCH LATCH_3 (.D(D2), .ENABLE(LE), .Q(LATCH_3_q));  // open: QN
  LATCH LATCH_4 (.D(D3), .ENABLE(LE), .Q(LATCH_4_q));  // open: QN
  LATCH LATCH_5 (.D(D4), .ENABLE(LE), .Q(LATCH_5_q));  // open: QN
  LATCH LATCH_6 (.D(D5), .ENABLE(LE), .Q(LATCH_6_q));  // open: QN
  LATCH LATCH_7 (.D(D6), .ENABLE(LE), .Q(LATCH_7_q));  // open: QN
  LATCH LATCH_8 (.D(D7), .ENABLE(LE), .Q(LATCH_8_q));  // open: QN
  LATCH LATCH_9 (.D(D8), .ENABLE(LE), .Q(LATCH_9_q));  // open: QN
  LATCH LATCH_10 (.D(D9), .ENABLE(LE), .Q(LATCH_10_q));  // open: QN
  assign Y0 = not_1_out ? LATCH_1_q : 1'bz;  // Controlled_Buffer controlled_buffer_1
  assign Y1 = not_1_out ? LATCH_2_q : 1'bz;  // Controlled_Buffer controlled_buffer_2
  assign Y2 = not_1_out ? LATCH_3_q : 1'bz;  // Controlled_Buffer controlled_buffer_3
  assign Y3 = not_1_out ? LATCH_4_q : 1'bz;  // Controlled_Buffer controlled_buffer_4
  assign Y4 = not_1_out ? LATCH_5_q : 1'bz;  // Controlled_Buffer controlled_buffer_5
  assign Y5 = not_1_out ? LATCH_6_q : 1'bz;  // Controlled_Buffer controlled_buffer_6
  assign Y6 = not_1_out ? LATCH_7_q : 1'bz;  // Controlled_Buffer controlled_buffer_7
  assign Y7 = not_1_out ? LATCH_8_q : 1'bz;  // Controlled_Buffer controlled_buffer_8
  assign Y8 = not_1_out ? LATCH_9_q : 1'bz;  // Controlled_Buffer controlled_buffer_9
  assign Y9 = not_1_out ? LATCH_10_q : 1'bz;  // Controlled_Buffer controlled_buffer_10

  // Notes on the sheet:
  //   AM29841
  //   High Performance Bus Interface Latches
  //   https://pdf1.alldatasheet.com/datasheet-pdf/view/107079/AMD/AM29841.html
endmodule

module AM29861A (
  input  R0,
  input  R1,
  input  R2,
  input  R3,
  input  R4,
  input  R5,
  input  R6,
  input  R7,
  input  R8,
  input  R9,
  input  OER_n,
  input  OET_n,
  output T0,
  output T1,
  output T2,
  output T3,
  output T4,
  output T5,
  output T6,
  output T7,
  output T8,
  output T9
);

  wire and_1_out, and_2_out, controlled_buffer_1_out, controlled_buffer_2_out, controlled_buffer_3_out,
       controlled_buffer_4_out, controlled_buffer_5_out, controlled_buffer_6_out, controlled_buffer_7_out,
       controlled_buffer_8_out, controlled_buffer_9_out, controlled_buffer_10_out, not_1_out, not_2_out;

  not not_1 (not_1_out, OER_n);
  not not_2 (not_2_out, OET_n);
  and and_1 (and_1_out, OER_n, not_2_out);
  and and_2 (and_2_out, not_1_out, OET_n);
  assign controlled_buffer_1_out = and_2_out ? T0 : 1'bz;  // Controlled_Buffer controlled_buffer_1
  assign controlled_buffer_2_out = and_2_out ? T1 : 1'bz;  // Controlled_Buffer controlled_buffer_2
  assign controlled_buffer_3_out = and_2_out ? T2 : 1'bz;  // Controlled_Buffer controlled_buffer_3
  assign controlled_buffer_4_out = and_2_out ? T3 : 1'bz;  // Controlled_Buffer controlled_buffer_4
  assign controlled_buffer_5_out = and_2_out ? T4 : 1'bz;  // Controlled_Buffer controlled_buffer_5
  assign controlled_buffer_6_out = and_2_out ? T5 : 1'bz;  // Controlled_Buffer controlled_buffer_6
  assign controlled_buffer_7_out = and_2_out ? T6 : 1'bz;  // Controlled_Buffer controlled_buffer_7
  assign controlled_buffer_8_out = and_2_out ? T7 : 1'bz;  // Controlled_Buffer controlled_buffer_8
  assign controlled_buffer_9_out = and_2_out ? T8 : 1'bz;  // Controlled_Buffer controlled_buffer_9
  assign controlled_buffer_10_out = and_2_out ? T9 : 1'bz;  // Controlled_Buffer controlled_buffer_10
  assign T0 = and_1_out ? R0 : 1'bz;  // Controlled_Buffer controlled_buffer_11
  assign T1 = and_1_out ? R1 : 1'bz;  // Controlled_Buffer controlled_buffer_12
  assign T2 = and_1_out ? R2 : 1'bz;  // Controlled_Buffer controlled_buffer_13
  assign T3 = and_1_out ? R3 : 1'bz;  // Controlled_Buffer controlled_buffer_14
  assign T4 = and_1_out ? R4 : 1'bz;  // Controlled_Buffer controlled_buffer_15
  assign T5 = and_1_out ? R5 : 1'bz;  // Controlled_Buffer controlled_buffer_16
  assign T6 = and_1_out ? R6 : 1'bz;  // Controlled_Buffer controlled_buffer_17
  assign T7 = and_1_out ? R7 : 1'bz;  // Controlled_Buffer controlled_buffer_18
  assign T8 = and_1_out ? R8 : 1'bz;  // Controlled_Buffer controlled_buffer_19
  assign T9 = and_1_out ? R9 : 1'bz;  // Controlled_Buffer controlled_buffer_20

  // Notes on the sheet:
  //   10 Bit Bus Tranceivers
  //   RECEIVE
  //   TRANSMIT
  //   OER_n - When LOW in conjunction with OET_n HIGH activates RECEIVE mode
  //   OET_n - When LOW in conjunction with OER_n HIGH activates TRANSMIT mode
  //   NEEDS TO BE REWRITTEN IN VERILOG(Because Logisim doesnt handle IN and OUT on the same pin)
  //   https://datasheetspdf.com/datasheet/AM29861.html
endmodule
module AM9150_20 (
  input  [9:0] A_9_0,
  input  [3:0] D_4_1,
  input  R_n,
  input  S_n,
  input  W_n,
  input  G_n,
  output [3:0] Q_4_1
);

  wire not_1_out;

  not not_1 (not_1_out, G_n);
  assign Q_4_1 = not_1_out ? D_4_1 : 4'bz;  // Controlled_Buffer controlled_buffer_1

  // Notes on the sheet:
  //   Q_4_1: pull=up
  //   AM9150_20
  //   1024 x 4 High-Speed Static R/W RAM
  //    http://www.sintran.com/library/libother/extern/AM9150.pdf
  //   RESET_n
  //   CHIP_SELECT_n
  //   Output_Enable_n
  //   WRITE_ENALE_n
  //   !! RAM HERE !!
  //   NOTE! Must be implemented in Verilog
endmodule

module TTL_74139 (
  input  A1,
  input  B1,
  input  G1_n,
  input  A2,
  input  B2,
  input  G2_n,
  output Y1_0_n,
  output Y1_1_n,
  output Y1_2_n,
  output Y1_3_n,
  output Y2_0_n,
  output Y2_1_n,
  output Y2_2_n,
  output Y2_3_n
);

  wire decoder_1_out0, decoder_1_out1, decoder_1_out2, decoder_1_out3, decoder_2_out0, decoder_2_out1,
       decoder_2_out2, decoder_2_out3, not_1_out, not_2_out;

  not not_1 (not_1_out, G1_n);
  not not_2 (not_2_out, G2_n);
  Decoder #(.select(2)) decoder_1 (
    .out0(decoder_1_out0), .out1(decoder_1_out1), .out2(decoder_1_out2), .out3(decoder_1_out3),
    .sel({B1, A1}), .en(not_1_out));
  Decoder #(.select(2)) decoder_2 (
    .out0(decoder_2_out0), .out1(decoder_2_out1), .out2(decoder_2_out2), .out3(decoder_2_out3),
    .sel({B2, A2}), .en(not_2_out));
  not not_3 (Y1_0_n, decoder_1_out0);
  not not_4 (Y1_2_n, decoder_1_out2);
  not not_5 (Y2_0_n, decoder_2_out0);
  not not_6 (Y2_2_n, decoder_2_out2);
  not not_7 (Y1_1_n, decoder_1_out1);
  not not_8 (Y1_3_n, decoder_1_out3);
  not not_9 (Y2_1_n, decoder_2_out1);
  not not_10 (Y2_3_n, decoder_2_out3);

  // Notes on the sheet:
  //   TTL 74139 - Dual 2-to-4 line decoder/demultiplexer integrated circuit. 
  //   https://www.ti.com/lit/ds/symlink/sn54ls139a-sp.pdf?ts=1702906423213
endmodule

module TTL_74241 (
  input  I0_1A1,
  input  I1_1A2,
  input  I2_1A3,
  input  I3_1A4,
  input  OE1_1G_n,
  input  I4_2A1,
  input  I5_2A2,
  input  I6_2A3,
  input  I7_2A4,
  input  OE2_2G,
  output O0_1Y1,
  output O1_1Y2,
  output O2_1Y3,
  output O3_1Y4,
  output O4_2Y1,
  output O5_2Y2,
  output O6_2Y3,
  output O7_2Y4
);

  wire not_1_out;

  not not_1 (not_1_out, OE1_1G_n);
  assign O0_1Y1 = not_1_out ? I0_1A1 : 1'bz;  // Controlled_Buffer controlled_buffer_1
  assign O1_1Y2 = not_1_out ? I1_1A2 : 1'bz;  // Controlled_Buffer controlled_buffer_2
  assign O2_1Y3 = not_1_out ? I2_1A3 : 1'bz;  // Controlled_Buffer controlled_buffer_3
  assign O3_1Y4 = not_1_out ? I3_1A4 : 1'bz;  // Controlled_Buffer controlled_buffer_4
  assign O4_2Y1 = OE2_2G ? I4_2A1 : 1'bz;  // Controlled_Buffer controlled_buffer_5
  assign O5_2Y2 = OE2_2G ? I5_2A2 : 1'bz;  // Controlled_Buffer controlled_buffer_6
  assign O6_2Y3 = OE2_2G ? I6_2A3 : 1'bz;  // Controlled_Buffer controlled_buffer_7
  assign O7_2Y4 = OE2_2G ? I7_2A4 : 1'bz;  // Controlled_Buffer controlled_buffer_8

  // Notes on the sheet:
  //   74F241 - Octal Buffers/Line Drivers with 3-STATE Outputs
  //   https://www.mouser.com/datasheet/2/308/74F241-1190323.pdf
endmodule

module TTL_74273 (
  input  D1,
  input  D2,
  input  D3,
  input  D4,
  input  D5,
  input  D6,
  input  D7,
  input  D8,
  input  CK,
  input  CL_n,
  output Q1,
  output Q2,
  output Q3,
  output Q4,
  output Q5,
  output Q6,
  output Q7,
  output Q8
);

  wire not_1_out;

  not not_1 (not_1_out, CL_n);
  D_Flip_Flop d_ff_1 (.D(D1), .clk(CK), .Q(Q1), .reset(not_1_out));  // open: Qn, preset
  D_Flip_Flop d_ff_2 (.D(D2), .clk(CK), .Q(Q2), .reset(not_1_out));  // open: Qn, preset
  D_Flip_Flop d_ff_3 (.D(D3), .clk(CK), .Q(Q3), .reset(not_1_out));  // open: Qn, preset
  D_Flip_Flop d_ff_4 (.D(D4), .clk(CK), .Q(Q4), .reset(not_1_out));  // open: Qn, preset
  D_Flip_Flop d_ff_5 (.D(D5), .clk(CK), .Q(Q5), .reset(not_1_out));  // open: Qn, preset
  D_Flip_Flop d_ff_6 (.D(D6), .clk(CK), .Q(Q6), .reset(not_1_out));  // open: Qn, preset
  D_Flip_Flop d_ff_7 (.D(D7), .clk(CK), .Q(Q7), .reset(not_1_out));  // open: Qn, preset
  D_Flip_Flop d_ff_8 (.D(D8), .clk(CK), .Q(Q8), .reset(not_1_out));  // open: Qn, preset

  // Notes on the sheet:
  //   TTL 74273 8-bit D-type register
  //   8-bt register. Latched on RISING EDGE (Clock going LOW->HIGH). With /CLEAR
endmodule

module TTL_74244 (
  input  I0_1A1,
  input  I1_1A2,
  input  I2_1A3,
  input  I3_1A4,
  input  OE1_1G_n,
  input  I4_2A1,
  input  I5_2A2,
  input  I6_2A3,
  input  I7_2A4,
  input  OE2_2G_n,
  output O0_1Y1,
  output O1_1Y2,
  output O2_1Y3,
  output O3_1Y4,
  output O4_2Y1,
  output O5_2Y2,
  output O6_2Y3,
  output O7_2Y4
);

  wire not_1_out, not_2_out;

  not not_1 (not_1_out, OE1_1G_n);
  not not_2 (not_2_out, OE2_2G_n);
  assign O0_1Y1 = not_1_out ? I0_1A1 : 1'bz;  // Controlled_Buffer controlled_buffer_1
  assign O1_1Y2 = not_1_out ? I1_1A2 : 1'bz;  // Controlled_Buffer controlled_buffer_2
  assign O2_1Y3 = not_1_out ? I2_1A3 : 1'bz;  // Controlled_Buffer controlled_buffer_3
  assign O3_1Y4 = not_1_out ? I3_1A4 : 1'bz;  // Controlled_Buffer controlled_buffer_4
  assign O4_2Y1 = not_2_out ? I4_2A1 : 1'bz;  // Controlled_Buffer controlled_buffer_5
  assign O5_2Y2 = not_2_out ? I5_2A2 : 1'bz;  // Controlled_Buffer controlled_buffer_6
  assign O6_2Y3 = not_2_out ? I6_2A3 : 1'bz;  // Controlled_Buffer controlled_buffer_7
  assign O7_2Y4 = not_2_out ? I7_2A4 : 1'bz;  // Controlled_Buffer controlled_buffer_8

  // Notes on the sheet:
  //   NOT Negated output
  //   Octal Buffers and Line Drivers With 3-State Outputs
  //   https://www.ti.com/lit/ds/symlink/sn74ls244.pdf
endmodule

module TTL_74245 (
  input  A1,
  input  A2,
  input  A3,
  input  A4,
  input  A5,
  input  A6,
  input  A7,
  input  A8,
  input  DIR,
  input  G_n,
  output B1,
  output B2,
  output B3,
  output B4,
  output B5,
  output B6,
  output B7,
  output B8
);

  wire not_1_out, not_2_out;
  wire [7:0] controlled_buffer_2_out, controlled_buffer_3_out;

  not not_1 (not_1_out, G_n);
  Controlled_Buffer #(.width(8)) controlled_buffer_1 (.in(controlled_buffer_3_out), .en(not_1_out));  // open: out
  assign controlled_buffer_2_out = DIR ? {A8, A7, A6, A5, A4, A3, A2, A1} : 8'bz;  // Controlled_Buffer controlled_buffer_2
  assign controlled_buffer_3_out = not_2_out ? controlled_buffer_2_out : 8'bz;  // Controlled_Buffer controlled_buffer_3
  not not_2 (not_2_out, DIR);
  assign {B8, B7, B6, B5, B4, B3, B2, B1} = not_1_out ? controlled_buffer_2_out : 8'bz;  // Controlled_Buffer controlled_buffer_4

  // Notes on the sheet:
  //   WRITE / READ_n
  //   SNx4LS245 Octal Bus Transceivers With 3-State Outputs
  //   OE
  //   These octal bus transceivers are designed for asynchronous two-way communication between data buses. The control-function implementation minimizes external timing requirements.
  //   The SNx4LS245 devices allow data transmission from the A bus to the B bus or from the B bus to the A bus, depending on the logic level at the directioncontrol (DIR) input. The output-enable (OE) input can disable the device so that the buses are effectively isolated.
endmodule

module TTL_74373 (
  input  [7:0] D_7_0,
  input  C,
  input  OE_n,
  output [7:0] Q_7_0
);

  wire not_1_out;
  wire [7:0] Latch_qa;

  not not_1 (not_1_out, OE_n);
  L8 Latch (
    .A(D_7_0[0]), .B(D_7_0[1]), .C(D_7_0[2]), .D(D_7_0[3]), .E(D_7_0[4]), .F(D_7_0[5]), .G(D_7_0[6]),
    .H(D_7_0[7]), .L(C), .QA(Latch_qa[0]), .QB(Latch_qa[1]), .QC(Latch_qa[2]), .QD(Latch_qa[3]),
    .QE(Latch_qa[4]), .QF(Latch_qa[5]), .QG(Latch_qa[6]), .QH(Latch_qa[7]));  // open: QAN, QBN, QCN, QDN, QEN, QFN, QGN, QHN
  assign Q_7_0 = not_1_out ? Latch_qa : 8'bz;  // Controlled_Buffer controlled_buffer_1

  // Notes on the sheet:
  //   74PCT373 Octal Transparent Latch with 3-state
  //   The 74HC373; 74HCT373 is an octal D-type transparent latch with 3-state outputs. The device features latch enable (LE) and output enable (OE) inputs. When LE is HIGH, data at the inputs enter the latches. In this condition the latches are transparent, a latch output will change each time its corresponding D-input changes. When LE is LOW the latches store the information that was present at the inputs a set-up time preceding the HIGH-to-LOW transition of LE. A HIGH on OE causes the outputs to assume a high-impedance OFF-state. Operation of the OE input does not affect the state of the latches. 
endmodule

module TTL_74374 (
  input  D1,
  input  D2,
  input  D3,
  input  D4,
  input  D5,
  input  D6,
  input  D7,
  input  D8,
  input  CK,
  input  OE_n,
  output Q1,
  output Q2,
  output Q3,
  output Q4,
  output Q5,
  output Q6,
  output Q7,
  output Q8
);

  wire d_ff_1_q, d_ff_2_q, d_ff_3_q, d_ff_4_q, d_ff_5_q, d_ff_6_q, d_ff_7_q, d_ff_8_q, not_1_out;

  D_Flip_Flop d_ff_1 (.D(D1), .clk(CK), .Q(d_ff_1_q));  // open: Qn, preset, reset
  D_Flip_Flop d_ff_2 (.D(D2), .clk(CK), .Q(d_ff_2_q));  // open: Qn, preset, reset
  D_Flip_Flop d_ff_3 (.D(D3), .clk(CK), .Q(d_ff_3_q));  // open: Qn, preset, reset
  D_Flip_Flop d_ff_4 (.D(D4), .clk(CK), .Q(d_ff_4_q));  // open: Qn, preset, reset
  D_Flip_Flop d_ff_5 (.D(D5), .clk(CK), .Q(d_ff_5_q));  // open: Qn, preset, reset
  D_Flip_Flop d_ff_6 (.D(D6), .clk(CK), .Q(d_ff_6_q));  // open: Qn, preset, reset
  D_Flip_Flop d_ff_7 (.D(D7), .clk(CK), .Q(d_ff_7_q));  // open: Qn, preset, reset
  D_Flip_Flop d_ff_8 (.D(D8), .clk(CK), .Q(d_ff_8_q));  // open: Qn, preset, reset
  not not_1 (not_1_out, OE_n);
  assign Q1 = not_1_out ? d_ff_1_q : 1'bz;  // Controlled_Buffer controlled_buffer_1
  assign Q2 = not_1_out ? d_ff_2_q : 1'bz;  // Controlled_Buffer controlled_buffer_2
  assign Q3 = not_1_out ? d_ff_3_q : 1'bz;  // Controlled_Buffer controlled_buffer_3
  assign Q4 = not_1_out ? d_ff_4_q : 1'bz;  // Controlled_Buffer controlled_buffer_4
  assign Q5 = not_1_out ? d_ff_5_q : 1'bz;  // Controlled_Buffer controlled_buffer_5
  assign Q6 = not_1_out ? d_ff_6_q : 1'bz;  // Controlled_Buffer controlled_buffer_6
  assign Q7 = not_1_out ? d_ff_7_q : 1'bz;  // Controlled_Buffer controlled_buffer_7
  assign Q8 = not_1_out ? d_ff_8_q : 1'bz;  // Controlled_Buffer controlled_buffer_8

  // Notes on the sheet:
  //   TTL 74374 - Octal D flip-flop (3-State)
  //   8-bt register. Latched on RISING EDGE (Clock going LOW->HIGH)
endmodule

module TTL_74521 (
  input  [7:0] A_7_0,
  input  [7:0] B_7_0,
  input  E_n,
  output AB_n
);

  wire comparator_1_eq, not_1_out;

  not not_1 (not_1_out, E_n);
  Comparator comparator_1 (.a(A_7_0), .b(B_7_0), .eq(comparator_1_eq));  // open: gt, lt
  assign AB_n = not_1_out ? ~comparator_1_eq : 1'bz;  // Controlled_Inverter controlled_inverter_1

  // Notes on the sheet:
  //   FAST CMOS 8-BIT IDT74FCT521AT/CT IDENTITY COMPARATOR 
endmodule

module TTL_74393 (
  input  A_n,
  input  CLR,
  output QA,
  output QB,
  output QC,
  output QD
);

  wire d_ff_1_q, d_ff_1_qn, d_ff_2_q, d_ff_2_qn, d_ff_3_q, d_ff_3_qn, d_ff_4_q, d_ff_4_qn, not_1_out,
       not_2_out, not_3_out, not_4_out;

  D_Flip_Flop #(.trigger("falling")) d_ff_1 (
    .D(not_1_out), .clk(A_n), .Q(d_ff_1_q), .Qn(d_ff_1_qn), .reset(CLR));  // open: preset
  not not_1 (not_1_out, d_ff_1_q);
  D_Flip_Flop d_ff_2 (.D(not_2_out), .clk(d_ff_1_q), .Q(d_ff_2_q), .Qn(d_ff_2_qn), .reset(CLR));  // open: preset
  not not_2 (not_2_out, d_ff_2_q);
  D_Flip_Flop d_ff_3 (.D(not_3_out), .clk(d_ff_2_q), .Q(d_ff_3_q), .Qn(d_ff_3_qn), .reset(CLR));  // open: preset
  not not_3 (not_3_out, d_ff_3_q);
  D_Flip_Flop d_ff_4 (.D(not_4_out), .clk(d_ff_3_q), .Q(d_ff_4_q), .Qn(d_ff_4_qn), .reset(CLR));  // open: preset
  not not_4 (not_4_out, d_ff_4_q);
  not not_5 (QA, d_ff_1_qn);
  not not_6 (QB, d_ff_2_qn);
  not not_7 (QC, d_ff_3_qn);
  not not_8 (QD, d_ff_4_qn);

  // Notes on the sheet:
  //   74393 - Dual 4-Stage Binary Ripple Counter
  //   https://www.onsemi.com/pdf/datasheet/mc74hc393a-d.pdf
endmodule

module TTL_74534 (
  input  D1,
  input  D2,
  input  D3,
  input  D4,
  input  D5,
  input  D6,
  input  D7,
  input  D8,
  input  CK,
  input  OE_n,
  output Q1_n,
  output Q2_n,
  output Q3_n,
  output Q4_n,
  output Q5_n,
  output Q6_n,
  output Q7_n,
  output Q8_n
);

  wire d_ff_1_q, d_ff_2_q, d_ff_3_q, d_ff_4_q, d_ff_5_q, d_ff_6_q, d_ff_7_q, d_ff_8_q, not_1_out;

  D_Flip_Flop d_ff_1 (.D(D1), .clk(CK), .Q(d_ff_1_q));  // open: Qn, preset, reset
  D_Flip_Flop d_ff_2 (.D(D2), .clk(CK), .Q(d_ff_2_q));  // open: Qn, preset, reset
  D_Flip_Flop d_ff_3 (.D(D3), .clk(CK), .Q(d_ff_3_q));  // open: Qn, preset, reset
  D_Flip_Flop d_ff_4 (.D(D4), .clk(CK), .Q(d_ff_4_q));  // open: Qn, preset, reset
  D_Flip_Flop d_ff_5 (.D(D5), .clk(CK), .Q(d_ff_5_q));  // open: Qn, preset, reset
  D_Flip_Flop d_ff_6 (.D(D6), .clk(CK), .Q(d_ff_6_q));  // open: Qn, preset, reset
  D_Flip_Flop d_ff_7 (.D(D7), .clk(CK), .Q(d_ff_7_q));  // open: Qn, preset, reset
  D_Flip_Flop d_ff_8 (.D(D8), .clk(CK), .Q(d_ff_8_q));  // open: Qn, preset, reset
  not not_1 (not_1_out, OE_n);
  assign Q1_n = not_1_out ? ~d_ff_1_q : 1'bz;  // Controlled_Inverter controlled_inverter_1
  assign Q2_n = not_1_out ? ~d_ff_2_q : 1'bz;  // Controlled_Inverter controlled_inverter_2
  assign Q3_n = not_1_out ? ~d_ff_3_q : 1'bz;  // Controlled_Inverter controlled_inverter_3
  assign Q4_n = not_1_out ? ~d_ff_4_q : 1'bz;  // Controlled_Inverter controlled_inverter_4
  assign Q5_n = not_1_out ? ~d_ff_5_q : 1'bz;  // Controlled_Inverter controlled_inverter_5
  assign Q6_n = not_1_out ? ~d_ff_6_q : 1'bz;  // Controlled_Inverter controlled_inverter_6
  assign Q7_n = not_1_out ? ~d_ff_7_q : 1'bz;  // Controlled_Inverter controlled_inverter_7
  assign Q8_n = not_1_out ? ~d_ff_8_q : 1'bz;  // Controlled_Inverter controlled_inverter_8

  // Notes on the sheet:
  //   TTL 74574 - Octal D flip-flop (3-State)
  //   IDENTICAL TO 74373 execept that output is negated (Q_n)
  //   8-bt register. Latched on RISING EDGE (Clock going LOW->HIGH)
  //   https://www.ti.com/lit/ds/symlink/sn74als534a.pdf
endmodule

module TTL_74646 (
  input  OE_n,
  input  DIR,
  input  CLKBA,
  input  SBA,
  input  CLKAB,
  input  SAB,
  input  A1,
  input  A2,
  input  A3,
  input  A4,
  input  A5,
  input  A6,
  input  A7,
  input  A8,
  output B1,
  output B2,
  output B3,
  output B4,
  output B5,
  output B6,
  output B7,
  output B8
);

  wire and_1_out, and_2_out, and_3_out, and_4_out, and_5_out, and_6_out, controlled_inverter_1_out,
       controlled_inverter_2_out, d_ff_1_qn, d_ff_2_qn, nand_1_out, nand_2_out, not_1_out, not_2_out,
       not_3_out, not_4_out, or_1_out, or_2_out;

  not not_1 (not_1_out, CLKAB);
  and and_1 (and_1_out, ~OE_n, ~DIR);  // AND_Gate
  and and_2 (and_2_out, ~OE_n, DIR);  // AND_Gate
  assign controlled_inverter_1_out = and_1_out ? ~or_1_out : 1'bz;  // Controlled_Inverter controlled_inverter_1
  or or_1 (or_1_out, and_3_out, and_4_out);
  D_Flip_Flop #(.trigger("falling")) d_ff_1 (.D(A1), .clk(not_1_out), .Qn(d_ff_1_qn));  // open: Q, preset, reset
  not not_2 (not_2_out, A1);
  and and_3 (and_3_out, SBA, d_ff_2_qn);
  and and_4 (and_4_out, nand_1_out, not_3_out);
  nand nand_1 (nand_1_out, SBA, SBA);
  nand nand_2 (nand_2_out, SAB, SAB);
  not not_3 (not_3_out, B1);
  not not_4 (not_4_out, CLKBA);
  and and_5 (and_5_out, SAB, d_ff_1_qn);
  and and_6 (and_6_out, nand_2_out, not_2_out);
  D_Flip_Flop #(.trigger("falling")) d_ff_2 (.D(B1), .clk(not_4_out), .Qn(d_ff_2_qn));  // open: Q, preset, reset
  or or_2 (or_2_out, and_5_out, and_6_out);
  assign controlled_inverter_2_out = and_2_out ? ~or_2_out : 1'bz;  // Controlled_Inverter controlled_inverter_2

  // Notes on the sheet:
  //   CONNECT  IN VERILOG
  //   Duplicate the channel A1-B1 for all others (2-8)
  //   74646 OCTAL BUS TRANSCEIVERS AND REGISTERS WITH 3-STATE OUTPUTS
  //   Output 3-state, Logic =TRUE (the 648 is Inverting/Negating else identical)
  //   THIS "NOT" is not in 648
  //   8  Bit Bus Tranceivers
  //   NEEDS TO BE REWRITTEN IN VERILOG(Because Logisim doesnt handle IN and OUT on the same pin)
  //   THIS "NOT" is not in 648
  //   https://www.ti.com/lit/ds/symlink/sn54as646.pdf
  //   CONNECT  IN VERILOG
endmodule

module TTL_74648 (
  input  OE_n,
  input  DIR,
  input  CLKBA,
  input  SBA,
  input  CLKAB,
  input  SAB,
  input  A1,
  input  A2,
  input  A3,
  input  A4,
  input  A5,
  input  A6,
  input  A7,
  input  A8,
  output B1_n,
  output B2_n,
  output B3_n,
  output B4_n,
  output B5_n,
  output B6_n,
  output B7_n,
  output B8_n
);

  wire and_1_out, and_2_out, and_3_out, and_4_out, and_5_out, and_6_out, controlled_inverter_1_out,
       controlled_inverter_2_out, d_ff_1_qn, d_ff_2_qn, nand_1_out, nand_2_out, not_1_out, not_2_out,
       or_1_out, or_2_out;

  not not_1 (not_1_out, CLKAB);
  and and_1 (and_1_out, ~OE_n, ~DIR);  // AND_Gate
  and and_2 (and_2_out, ~OE_n, DIR);  // AND_Gate
  assign controlled_inverter_1_out = and_1_out ? ~or_1_out : 1'bz;  // Controlled_Inverter controlled_inverter_1
  or or_1 (or_1_out, and_3_out, and_4_out);
  D_Flip_Flop #(.trigger("falling")) d_ff_1 (.D(A1), .clk(not_1_out), .Qn(d_ff_1_qn));  // open: Q, preset, reset
  and and_3 (and_3_out, SBA, d_ff_2_qn);
  and and_4 (and_4_out, nand_1_out, B1_n);
  nand nand_1 (nand_1_out, SBA, SBA);
  nand nand_2 (nand_2_out, SAB, SAB);
  not not_2 (not_2_out, CLKBA);
  and and_5 (and_5_out, SAB, d_ff_1_qn);
  and and_6 (and_6_out, nand_2_out, A1);
  D_Flip_Flop #(.trigger("falling")) d_ff_2 (.D(B1_n), .clk(not_2_out), .Qn(d_ff_2_qn));  // open: Q, preset, reset
  or or_2 (or_2_out, and_5_out, and_6_out);
  assign controlled_inverter_2_out = and_2_out ? ~or_2_out : 1'bz;  // Controlled_Inverter controlled_inverter_2

  // Notes on the sheet:
  //   CONNECT  IN VERILOG
  //   Duplicate the channel A1-B1 for all others (2-8)
  //   74648 OCTAL BUS TRANSCEIVERS AND REGISTERS WITH 3-STATE OUTPUTS (Inverting)
  //   Output 3-state, Logic =Inverting/Negated (the 646 is Logic=true
  //   8  Bit Bus Tranceivers
  //   NEEDS TO BE REWRITTEN IN VERILOG(Because Logisim doesnt handle IN and OUT on the same pin)
  //   https://www.ti.com/lit/ds/symlink/sn54as646.pdf
  //   CONNECT  IN VERILOG
endmodule

module TMM2018D_25 (
  input  [10:0] A0_A10,
  input  OE_n,
  input  W_n,
  input  CS_n,
  output [7:0] D0_D7
);

  wire not_1_out;

  not not_1 (not_1_out, OE_n);

  // Notes on the sheet:
  //   (Implement in Verilog)
  //   TMM2018D_25 16K Static RAM (Cache)
endmodule

module IMS1403_25 (
  input  [13:0] A0_A13,
  input  D,
  input  W_n,
  input  CE_n,
  output Q
);

  wire not_1_out;

  not not_1 (not_1_out, W_n);

  // Notes on the sheet:
  //   NEEDS TO BE IMPLEMENTED IN VERILOG!
  //   IMS1403_25 16K x 1 Static RAM
endmodule

module IDT6168A_20 (
  input  [11:0] A_11_0,
  input  WE_n,
  input  CE_n,
  output [3:0] D_3_0
);

  wire not_1_out, not_2_out;

  not not_1 (not_1_out, WE_n);
  not not_2 (not_2_out, CE_n);

  // Notes on the sheet:
  //   IDT6168A 16K (4Kx4) Static RAM
  //   Write Enable
  //   Output Enable
endmodule

module PAL_16R4D (
  input  CK,
  input  I0,
  input  I1,
  input  I2,
  input  I3,
  input  I4,
  input  I5,
  input  I6,
  input  I7,
  input  OE_n,
  output Q0_n,
  output Q1_n,
  output Q2_n,
  output Q3_n,
  output B0_n,
  output B1_n,
  output B2_n,
  output B3_n
);

  // NOT_Gate not_1 has open pins: in=OE_n, out=open
  assign Q0_n = 1'b0 ? I0 : 1'bz;  // Controlled_Buffer controlled_buffer_1
  assign Q1_n = 1'b0 ? I1 : 1'bz;  // Controlled_Buffer controlled_buffer_2
  assign Q2_n = 1'b0 ? I2 : 1'bz;  // Controlled_Buffer controlled_buffer_3
  assign Q3_n = 1'b0 ? I3 : 1'bz;  // Controlled_Buffer controlled_buffer_4
  assign B0_n = 1'b0 ? I4 : 1'bz;  // Controlled_Buffer controlled_buffer_5
  assign B1_n = 1'b0 ? I5 : 1'bz;  // Controlled_Buffer controlled_buffer_6
  assign B2_n = 1'b0 ? I6 : 1'bz;  // Controlled_Buffer controlled_buffer_7
  assign B3_n = 1'b0 ? I7 : 1'bz;  // Controlled_Buffer controlled_buffer_8

  // Notes on the sheet:
  //   Placeholder for the VERILOG drawings. Needs to be replaced with VERILOG code
endmodule

module PAL_16R6D (
  input  CK,
  input  I0,
  input  I1,
  input  I2,
  input  I3,
  input  I4,
  input  I5,
  input  I6,
  input  I7,
  input  OE_n,
  output Q0_n,
  output Q1_n,
  output Q2_n,
  output Q3_n,
  output Q4_n,
  output Q5_n,
  output B0_n,
  output B1_n
);

  // NOT_Gate not_1 has open pins: in=OE_n, out=open
  assign Q0_n = 1'b0 ? I0 : 1'bz;  // Controlled_Buffer controlled_buffer_1
  assign Q1_n = 1'b0 ? I1 : 1'bz;  // Controlled_Buffer controlled_buffer_2
  assign Q2_n = 1'b0 ? I2 : 1'bz;  // Controlled_Buffer controlled_buffer_3
  assign Q3_n = 1'b0 ? I3 : 1'bz;  // Controlled_Buffer controlled_buffer_4
  assign Q4_n = 1'b0 ? I4 : 1'bz;  // Controlled_Buffer controlled_buffer_5
  assign Q5_n = 1'b0 ? I5 : 1'bz;  // Controlled_Buffer controlled_buffer_6
  assign B0_n = 1'b0 ? I6 : 1'bz;  // Controlled_Buffer controlled_buffer_7
  assign B1_n = 1'b0 ? I7 : 1'bz;  // Controlled_Buffer controlled_buffer_8

  // Notes on the sheet:
  //   Placeholder for the VERILOG drawings. Needs to be replaced with VERILOG code
endmodule

module PAL_16R8D (
  input  CK,
  input  I0,
  input  I1,
  input  I2,
  input  I3,
  input  I4,
  input  I5,
  input  I6,
  input  I7,
  input  OE_n,
  output Q0_n,
  output Q1_n,
  output Q2_n,
  output Q3_n,
  output Q4_n,
  output Q5_n,
  output Q6_n,
  output Q7_n
);

  // NOT_Gate not_1 has open pins: in=OE_n, out=open
  assign Q0_n = 1'b0 ? I0 : 1'bz;  // Controlled_Buffer controlled_buffer_1
  assign Q1_n = 1'b0 ? I1 : 1'bz;  // Controlled_Buffer controlled_buffer_2
  assign Q2_n = 1'b0 ? I2 : 1'bz;  // Controlled_Buffer controlled_buffer_3
  assign Q3_n = 1'b0 ? I3 : 1'bz;  // Controlled_Buffer controlled_buffer_4
  assign Q4_n = 1'b0 ? I4 : 1'bz;  // Controlled_Buffer controlled_buffer_5
  assign Q5_n = 1'b0 ? I5 : 1'bz;  // Controlled_Buffer controlled_buffer_6
  assign Q6_n = 1'b0 ? I6 : 1'bz;  // Controlled_Buffer controlled_buffer_7
  assign Q7_n = 1'b0 ? I7 : 1'bz;  // Controlled_Buffer controlled_buffer_8

  // Notes on the sheet:
  //   Placeholder for the VERILOG drawings. Needs to be replaced with VERILOG code
endmodule

module PAL_16L8_12 (
  input  I0,
  input  I1,
  input  I2,
  input  I3,
  input  I4,
  input  I5,
  input  I6,
  input  I7,
  input  I8,
  input  I9,
  output Y0_n,
  output Y1_n,
  output B0_n,
  output B1_n,
  output B2_n,
  output B3_n,
  output B4_n,
  output B5_n
);

  wire and_1_out, and_2_out;

  and and_1 (and_1_out, I6, I7);
  and and_2 (and_2_out, I8, I9);
  assign Y0_n = 1'b0 ? I0 : 1'bz;  // Controlled_Buffer controlled_buffer_1
  assign Y1_n = 1'b0 ? I1 : 1'bz;  // Controlled_Buffer controlled_buffer_2
  assign B0_n = 1'b0 ? I2 : 1'bz;  // Controlled_Buffer controlled_buffer_3
  assign B1_n = 1'b0 ? I3 : 1'bz;  // Controlled_Buffer controlled_buffer_4
  assign B2_n = 1'b0 ? I4 : 1'bz;  // Controlled_Buffer controlled_buffer_5
  assign B3_n = 1'b0 ? I5 : 1'bz;  // Controlled_Buffer controlled_buffer_6
  Controlled_Buffer controlled_buffer_7 (.in(and_1_out), .en(1'b0));  // open: out
  Controlled_Buffer controlled_buffer_8 (.in(and_2_out), .en(1'b0));  // open: out

  // Notes on the sheet:
  //   Placeholder for the VERILOG drawings. Needs to be replaced with VERILOG code
endmodule

module SC2661_UART (
  input  RESET,
  input  CE_n,
  input  READ_n,
  input  A0,
  input  A1,
  input  BRCLK,
  input  RXC_n,
  input  TXC_n,
  input  DCD_n,
  input  DSR_n,
  input  CTS_n,
  input  RXD,
  output [7:0] D_7_0,
  output TXEMT_n,
  output DTR_n,
  output RTS_n,
  output TXD,
  output TXDRDY_n,
  output RXDRDY_n
);


  // Notes on the sheet:
  //   Microchip SC2661 UART
  //   https://datasheetspdf.com/pdf-file/1412058/SMSC/COM2661-3/1 
  //   http://bitsavers.org/components/microchipTechnology/_dataBooks/1990_Microchip_Data_Book.pdf
  //   Needs to be made with Verilog
endmodule

module SIP1M9 (
  input  [9:0] AA_9_0,
  input  RAS_n,
  input  CAS_n,
  input  CAS9_n,
  input  W_n,
  output [7:0] DQ_8_1_io,
  output Q9,
  output D9,
  output PRD_n
);


  assign D9 = 1'b0;
  assign PRD_n = 1'b1;
  assign Q9 = 1'b0;

  // Notes on the sheet:
  //   RAM  1KB ? 1MB ?? How dows RAS AND CAS work ?
  //   10 BIT ADDRESS RAM, RAS, CAS
  //   8 bit data
  //   NEEDS TO BE IMPLEMENTED IN VERILOG!!
endmodule
