// Logisim project ND_DGA.circ as structural Verilog: 13 circuits, main circuit DECODE_DGA_COMM
module DECODE_DGA (
);


  // Notes on the sheet:
  //   Page 1 DECODE - DECODE_DGA- Sheet 1 of 6
endmodule

module DECODE_DGA_POW (
  input  EMCLN,
  input  LOADN,
  input  CLRTIN,
  input  CONTINUEN,
  input  SSTOPN,
  input  STOPN,
  input  STARTN,
  input  PWCL,
  input  RTOSC,
  input  TESTE,
  input  POWSENSE,
  input  PRQN,
  output MCL,
  output CLEAR,
  output POWFAILN,
  output IDB2,
  output IDB1,
  output IDB0,
  output PANN
);

  wire A569_n02, A572_qn, A580_out, A590_out, A591_qn, A592_out, A593_qn, A594_qn, A596_qn, A597_out,
       A598_out, A599_out, A601_n01, A602_qn, A605_qn, A609_out, A613_n01, A619_qn, A620_n01, A621_qn,
       A622_qn, A623_qn, A632_qn, A634_qn, CONN, f103_1_f_out, f595_1_n02, LODN, MCLN, MS20, nand_1_out,
       nand_2_out, nor_1_out, not_1_out, not_2_out, not_4_out, not_5_out, not_6_out, not_7_out, not_8_out,
       not_10_out, not_11_out, not_12_out, not_13_out, not_14_out, not_16_out, not_17_out, POWFAIL, RSTN,
       RTCN, STP, STPN, undriven, ZZ1;

  not not_1 (not_1_out, CONTINUEN);
  not not_2 (not_2_out, PWCL);
  not not_3 (POWFAILN, POWFAIL);
  not not_4 (not_4_out, LOADN);
  nand nand_1 (nand_1_out, MCLN, CLRTIN, STP);
  nand nand_2 (nand_2_out, STPN, not_2_out);
  F091 A613 (.N01(A613_n01));  // open: N02
  F103 f103_1 (.F_IN(undriven), .F_OUT(f103_1_f_out));
  F595 A576 (.H01(not_4_out), .H02(nand_1_out), .H03(ZZ1), .N02(LODN));  // open: N01
  F595 A574 (.H01(A572_qn), .H02(nand_1_out), .H03(ZZ1), .N02(RSTN));  // open: N01
  F571 A601 (.H01(MS20), .H02(RTOSC), .H03(TESTE), .H04(1'b0), .N01(A601_n01));
  not not_5 (not_5_out, CONN);
  not not_6 (not_6_out, A613_n01);
  not not_7 (not_7_out, PRQN);
  not not_8 (not_8_out, RTCN);
  F595 A575 (.H01(not_1_out), .H02(nand_1_out), .H03(ZZ1), .N02(CONN));  // open: N01
  F595 A569 (.H01(nand_2_out), .H02(POWFAILN), .H03(ZZ1), .N02(A569_n02));  // open: N01
  F714 A623 (.S(1'b0), .T(RTOSC), .R(f103_1_f_out), .QN(A623_qn));  // open: Q
  not not_9 (CLEAR, A569_n02);
  F091 f091_1 (.N01(ZZ1));  // open: N02
  F714 A596 (.S(1'b0), .T(A601_n01), .R(POWSENSE), .QN(A596_qn));  // open: Q
  F714 A632 (.S(1'b0), .T(A623_qn), .R(f103_1_f_out), .QN(A632_qn));  // open: Q
  nand A597 (A597_out, CONN, LODN, not_7_out);
  nand A609 (A609_out, CONN, LODN, not_6_out);
  nand A598 (A598_out, RSTN, not_5_out);
  nand A599 (A599_out, not_8_out, PRQN, LODN, RSTN);
  not not_10 (not_10_out, STARTN);
  nand A590 (A590_out, not_6_out, LODN, RSTN);
  nand A580 (A580_out, SSTOPN, A569_n02, STOPN);
  F714 A602 (.S(1'b0), .T(A596_qn), .R(POWSENSE), .QN(A602_qn));  // open: Q
  nand A606 (IDB2, LODN, CONN, RSTN, MCLN);
  nand A592 (A592_out, MCLN, RSTN, CONN, LODN, A613_n01, PRQN, RTCN, STPN);
  F714 A634 (.S(1'b0), .T(A632_qn), .R(f103_1_f_out), .QN(A634_qn));  // open: Q
  F595 f595_1 (.H01(STPN), .H02(PWCL), .H03(ZZ1), .N02(f595_1_n02));  // open: N01
  nand A603 (IDB1, A597_out, RSTN, MCLN, A609_out);
  nand A604 (IDB0, MCLN, A598_out, A599_out, A590_out);
  nand A595 (PANN, SSTOPN, A592_out);
  F595 A571 (.H01(A580_out), .H02(not_10_out), .H03(ZZ1), .N01(STP), .N02(STPN));
  not not_11 (not_11_out, CLRTIN);
  not not_12 (not_12_out, ZZ1);
  F714 A593 (.S(1'b0), .T(A602_qn), .R(POWSENSE), .QN(A593_qn));  // open: Q
  F714 A621 (.S(1'b0), .T(A634_qn), .R(f103_1_f_out), .QN(A621_qn));  // open: Q
  nand nand_3 (MCL, EMCLN, A569_n02);
  not not_13 (not_13_out, CLRTIN);
  D_Flip_Flop d_ff_1 (.D(1'b0), .clk(MS20), .Q(RTCN), .preset(not_13_out), .reset(not_14_out));  // open: Qn
  not not_14 (not_14_out, ZZ1);
  D_Flip_Flop A572 (.D(f595_1_n02), .clk(A569_n02), .Qn(A572_qn), .preset(not_11_out), .reset(not_12_out));  // open: Q
  not not_15 (MCLN, MCL);
  F714 A594 (.S(1'b0), .T(A593_qn), .R(POWSENSE), .QN(A594_qn));  // open: Q
  F714 A622 (.S(1'b0), .T(A621_qn), .R(f103_1_f_out), .QN(A622_qn));  // open: Q
  F714 A619 (.S(1'b0), .T(A622_qn), .R(f103_1_f_out), .QN(A619_qn));  // open: Q
  F714 A591 (.S(1'b0), .T(A594_qn), .R(POWSENSE), .QN(A591_qn));  // open: Q
  F714 A605 (.S(1'b0), .T(A591_qn), .R(POWSENSE), .QN(A605_qn));  // open: Q
  nor nor_1 (nor_1_out, POWSENSE, PWCL);
  F571 A620 (.H01(A619_qn), .H02(RTOSC), .H03(TESTE), .H04(1'b0), .N01(A620_n01));
  not not_16 (not_16_out, nor_1_out);
  D_Flip_Flop A600 (.D(1'b0), .clk(A605_qn), .Q(POWFAIL), .preset(not_16_out), .reset(not_17_out));  // open: Qn
  not not_17 (not_17_out, POWFAIL);
  F714 A624 (.S(1'b0), .T(A620_n01), .R(f103_1_f_out));  // open: Q, QN

  // Notes on the sheet:
  //   Page 8 DECODE - DECODE_DGA_POW- Sheet 1 of 3
  //   Page 9 DECODE - DECODE_DGA_POW- Sheet 2 of 3
  //   Page 10 DECODE - DECODE_DGA_POW- Sheet 3 of 3
  //   CONTINUE
  //   CLRTIN
  //   RESCL
  //   TO BE FINISHED
  //   CLEARN
  //   START
  //   CLEARN
  //   CLRTIN
  //   CLEARN
  //   STPN
  //   RTCN
  //   POWSN
endmodule

module DECODE_DGA_PFIFD (
  input  [7:0] IDBI_7_0,
  input  [12:0] WEL_12_0,
  input  [12:0] WEU_12_0,
  output [7:0] AD_7_0
);

  wire d_ff_1_q, d_ff_2_q, d_ff_3_q, d_ff_4_q, d_ff_5_q, d_ff_6_q, d_ff_7_q, d_ff_8_q, d_ff_9_q, d_ff_10_q,
       d_ff_11_q, d_ff_12_q, d_ff_13_q, d_ff_14_q, d_ff_15_q, d_ff_16_q, d_ff_17_q, d_ff_18_q, d_ff_19_q,
       d_ff_20_q, d_ff_21_q, d_ff_22_q, d_ff_23_q, d_ff_24_q, d_ff_25_q, d_ff_26_q, d_ff_27_q, d_ff_28_q,
       d_ff_29_q, d_ff_30_q, d_ff_31_q, d_ff_32_q, d_ff_33_q, d_ff_34_q, d_ff_35_q, d_ff_36_q, d_ff_37_q,
       d_ff_38_q, d_ff_39_q, d_ff_40_q, d_ff_41_q, d_ff_42_q, d_ff_43_q, d_ff_44_q, d_ff_45_q, d_ff_46_q,
       d_ff_47_q, d_ff_48_q, d_ff_49_q, d_ff_50_q, d_ff_51_q, d_ff_52_q, d_ff_53_q, d_ff_54_q, d_ff_55_q,
       d_ff_56_q, d_ff_57_q, d_ff_58_q, d_ff_59_q, d_ff_60_q, d_ff_61_q, d_ff_62_q, d_ff_63_q, d_ff_64_q,
       d_ff_65_q, d_ff_66_q, d_ff_67_q, d_ff_68_q, d_ff_69_q, d_ff_70_q, d_ff_71_q, d_ff_72_q, d_ff_73_q,
       d_ff_74_q, d_ff_75_q, d_ff_76_q, d_ff_77_q, d_ff_78_q, d_ff_79_q, d_ff_80_q, d_ff_81_q, d_ff_82_q,
       d_ff_83_q, d_ff_84_q, d_ff_85_q, d_ff_86_q, d_ff_87_q, d_ff_88_q, d_ff_89_q, d_ff_90_q, d_ff_91_q,
       d_ff_92_q, d_ff_93_q, d_ff_94_q, d_ff_95_q, d_ff_96_q, WEU112;

  D_Flip_Flop d_ff_1 (.D(IDBI_7_0[7]), .clk(WEU_12_0[0]), .Q(d_ff_1_q));  // open: Qn, preset, reset
  D_Flip_Flop d_ff_2 (.D(IDBI_7_0[6]), .clk(WEU_12_0[0]), .Q(d_ff_2_q));  // open: Qn, preset, reset
  D_Flip_Flop d_ff_3 (.D(IDBI_7_0[5]), .clk(WEU_12_0[0]), .Q(d_ff_3_q));  // open: Qn, preset, reset
  D_Flip_Flop d_ff_4 (.D(IDBI_7_0[4]), .clk(WEU_12_0[0]), .Q(d_ff_4_q));  // open: Qn, preset, reset
  D_Flip_Flop d_ff_5 (.D(IDBI_7_0[3]), .clk(WEL_12_0[0]), .Q(d_ff_5_q));  // open: Qn, preset, reset
  D_Flip_Flop d_ff_6 (.D(IDBI_7_0[2]), .clk(WEL_12_0[0]), .Q(d_ff_6_q));  // open: Qn, preset, reset
  D_Flip_Flop d_ff_7 (.D(IDBI_7_0[1]), .clk(WEL_12_0[0]), .Q(d_ff_7_q));  // open: Qn, preset, reset
  D_Flip_Flop d_ff_8 (.D(IDBI_7_0[0]), .clk(WEL_12_0[0]), .Q(d_ff_8_q));  // open: Qn, preset, reset
  D_Flip_Flop d_ff_9 (.D(d_ff_1_q), .clk(WEU_12_0[1]), .Q(d_ff_9_q));  // open: Qn, preset, reset
  D_Flip_Flop d_ff_10 (.D(d_ff_2_q), .clk(WEU_12_0[1]), .Q(d_ff_10_q));  // open: Qn, preset, reset
  D_Flip_Flop d_ff_11 (.D(d_ff_3_q), .clk(WEU_12_0[1]), .Q(d_ff_11_q));  // open: Qn, preset, reset
  D_Flip_Flop d_ff_12 (.D(d_ff_4_q), .clk(WEU_12_0[1]), .Q(d_ff_12_q));  // open: Qn, preset, reset
  D_Flip_Flop d_ff_13 (.D(d_ff_5_q), .clk(WEL_12_0[1]), .Q(d_ff_13_q));  // open: Qn, preset, reset
  D_Flip_Flop d_ff_14 (.D(d_ff_6_q), .clk(WEL_12_0[1]), .Q(d_ff_14_q));  // open: Qn, preset, reset
  D_Flip_Flop d_ff_15 (.D(d_ff_7_q), .clk(WEL_12_0[1]), .Q(d_ff_15_q));  // open: Qn, preset, reset
  D_Flip_Flop d_ff_16 (.D(d_ff_8_q), .clk(WEL_12_0[1]), .Q(d_ff_16_q));  // open: Qn, preset, reset
  D_Flip_Flop d_ff_17 (.D(d_ff_9_q), .clk(WEU_12_0[2]), .Q(d_ff_17_q));  // open: Qn, preset, reset
  D_Flip_Flop d_ff_18 (.D(d_ff_10_q), .clk(WEU_12_0[2]), .Q(d_ff_18_q));  // open: Qn, preset, reset
  D_Flip_Flop d_ff_19 (.D(d_ff_11_q), .clk(WEU_12_0[2]), .Q(d_ff_19_q));  // open: Qn, preset, reset
  D_Flip_Flop d_ff_20 (.D(d_ff_12_q), .clk(WEU_12_0[2]), .Q(d_ff_20_q));  // open: Qn, preset, reset
  D_Flip_Flop d_ff_21 (.D(d_ff_13_q), .clk(WEL_12_0[2]), .Q(d_ff_21_q));  // open: Qn, preset, reset
  D_Flip_Flop d_ff_22 (.D(d_ff_14_q), .clk(WEL_12_0[2]), .Q(d_ff_22_q));  // open: Qn, preset, reset
  D_Flip_Flop d_ff_23 (.D(d_ff_15_q), .clk(WEL_12_0[2]), .Q(d_ff_23_q));  // open: Qn, preset, reset
  D_Flip_Flop d_ff_24 (.D(d_ff_16_q), .clk(WEL_12_0[2]), .Q(d_ff_24_q));  // open: Qn, preset, reset
  D_Flip_Flop d_ff_25 (.D(d_ff_17_q), .clk(WEU_12_0[3]), .Q(d_ff_25_q));  // open: Qn, preset, reset
  D_Flip_Flop d_ff_26 (.D(d_ff_18_q), .clk(WEU_12_0[3]), .Q(d_ff_26_q));  // open: Qn, preset, reset
  D_Flip_Flop d_ff_27 (.D(d_ff_19_q), .clk(WEU_12_0[3]), .Q(d_ff_27_q));  // open: Qn, preset, reset
  D_Flip_Flop d_ff_28 (.D(d_ff_20_q), .clk(WEU_12_0[3]), .Q(d_ff_28_q));  // open: Qn, preset, reset
  D_Flip_Flop d_ff_29 (.D(d_ff_21_q), .clk(WEL_12_0[3]), .Q(d_ff_29_q));  // open: Qn, preset, reset
  D_Flip_Flop d_ff_30 (.D(d_ff_22_q), .clk(WEL_12_0[3]), .Q(d_ff_30_q));  // open: Qn, preset, reset
  D_Flip_Flop d_ff_31 (.D(d_ff_23_q), .clk(WEL_12_0[3]), .Q(d_ff_31_q));  // open: Qn, preset, reset
  D_Flip_Flop d_ff_32 (.D(d_ff_24_q), .clk(WEL_12_0[3]), .Q(d_ff_32_q));  // open: Qn, preset, reset
  D_Flip_Flop d_ff_33 (.D(d_ff_25_q), .clk(WEU_12_0[4]), .Q(d_ff_33_q));  // open: Qn, preset, reset
  D_Flip_Flop d_ff_34 (.D(d_ff_26_q), .clk(WEU_12_0[4]), .Q(d_ff_34_q));  // open: Qn, preset, reset
  D_Flip_Flop d_ff_35 (.D(d_ff_27_q), .clk(WEU_12_0[4]), .Q(d_ff_35_q));  // open: Qn, preset, reset
  D_Flip_Flop d_ff_36 (.D(d_ff_28_q), .clk(WEU_12_0[4]), .Q(d_ff_36_q));  // open: Qn, preset, reset
  D_Flip_Flop d_ff_37 (.D(d_ff_29_q), .clk(WEL_12_0[4]), .Q(d_ff_37_q));  // open: Qn, preset, reset
  D_Flip_Flop d_ff_38 (.D(d_ff_30_q), .clk(WEL_12_0[4]), .Q(d_ff_38_q));  // open: Qn, preset, reset
  D_Flip_Flop d_ff_39 (.D(d_ff_31_q), .clk(WEL_12_0[4]), .Q(d_ff_39_q));  // open: Qn, preset, reset
  D_Flip_Flop d_ff_40 (.D(d_ff_32_q), .clk(WEL_12_0[4]), .Q(d_ff_40_q));  // open: Qn, preset, reset
  D_Flip_Flop d_ff_41 (.D(d_ff_33_q), .clk(WEU_12_0[5]), .Q(d_ff_41_q));  // open: Qn, preset, reset
  D_Flip_Flop d_ff_42 (.D(d_ff_34_q), .clk(WEU_12_0[5]), .Q(d_ff_42_q));  // open: Qn, preset, reset
  D_Flip_Flop d_ff_43 (.D(d_ff_35_q), .clk(WEU_12_0[5]), .Q(d_ff_43_q));  // open: Qn, preset, reset
  D_Flip_Flop d_ff_44 (.D(d_ff_36_q), .clk(WEU_12_0[5]), .Q(d_ff_44_q));  // open: Qn, preset, reset
  D_Flip_Flop d_ff_45 (.D(d_ff_37_q), .clk(WEL_12_0[5]), .Q(d_ff_45_q));  // open: Qn, preset, reset
  D_Flip_Flop d_ff_46 (.D(d_ff_38_q), .clk(WEL_12_0[5]), .Q(d_ff_46_q));  // open: Qn, preset, reset
  D_Flip_Flop d_ff_47 (.D(d_ff_39_q), .clk(WEL_12_0[5]), .Q(d_ff_47_q));  // open: Qn, preset, reset
  D_Flip_Flop d_ff_48 (.D(d_ff_40_q), .clk(WEL_12_0[5]), .Q(d_ff_48_q));  // open: Qn, preset, reset
  D_Flip_Flop d_ff_49 (.D(d_ff_41_q), .clk(WEU_12_0[6]), .Q(d_ff_49_q));  // open: Qn, preset, reset
  D_Flip_Flop d_ff_50 (.D(d_ff_42_q), .clk(WEU_12_0[6]), .Q(d_ff_50_q));  // open: Qn, preset, reset
  D_Flip_Flop d_ff_51 (.D(d_ff_43_q), .clk(WEU_12_0[6]), .Q(d_ff_51_q));  // open: Qn, preset, reset
  D_Flip_Flop d_ff_52 (.D(d_ff_44_q), .clk(WEU_12_0[6]), .Q(d_ff_52_q));  // open: Qn, preset, reset
  D_Flip_Flop d_ff_53 (.D(d_ff_45_q), .clk(WEL_12_0[6]), .Q(d_ff_53_q));  // open: Qn, preset, reset
  D_Flip_Flop d_ff_54 (.D(d_ff_46_q), .clk(WEL_12_0[6]), .Q(d_ff_54_q));  // open: Qn, preset, reset
  D_Flip_Flop d_ff_55 (.D(d_ff_47_q), .clk(WEL_12_0[6]), .Q(d_ff_55_q));  // open: Qn, preset, reset
  D_Flip_Flop d_ff_56 (.D(d_ff_48_q), .clk(WEL_12_0[6]), .Q(d_ff_56_q));  // open: Qn, preset, reset
  D_Flip_Flop d_ff_57 (.D(d_ff_49_q), .clk(WEU_12_0[7]), .Q(d_ff_57_q));  // open: Qn, preset, reset
  D_Flip_Flop d_ff_58 (.D(d_ff_50_q), .clk(WEU_12_0[7]), .Q(d_ff_58_q));  // open: Qn, preset, reset
  D_Flip_Flop d_ff_59 (.D(d_ff_51_q), .clk(WEU_12_0[7]), .Q(d_ff_59_q));  // open: Qn, preset, reset
  D_Flip_Flop d_ff_60 (.D(d_ff_52_q), .clk(WEU_12_0[7]), .Q(d_ff_60_q));  // open: Qn, preset, reset
  D_Flip_Flop d_ff_61 (.D(d_ff_53_q), .clk(WEL_12_0[7]), .Q(d_ff_61_q));  // open: Qn, preset, reset
  D_Flip_Flop d_ff_62 (.D(d_ff_54_q), .clk(WEL_12_0[7]), .Q(d_ff_62_q));  // open: Qn, preset, reset
  D_Flip_Flop d_ff_63 (.D(d_ff_55_q), .clk(WEL_12_0[7]), .Q(d_ff_63_q));  // open: Qn, preset, reset
  D_Flip_Flop d_ff_64 (.D(d_ff_56_q), .clk(WEL_12_0[7]), .Q(d_ff_64_q));  // open: Qn, preset, reset
  D_Flip_Flop d_ff_65 (.D(d_ff_57_q), .clk(WEU_12_0[8]), .Q(d_ff_65_q));  // open: Qn, preset, reset
  D_Flip_Flop d_ff_66 (.D(d_ff_58_q), .clk(WEU_12_0[8]), .Q(d_ff_66_q));  // open: Qn, preset, reset
  D_Flip_Flop d_ff_67 (.D(d_ff_59_q), .clk(WEU_12_0[8]), .Q(d_ff_67_q));  // open: Qn, preset, reset
  D_Flip_Flop d_ff_68 (.D(d_ff_60_q), .clk(WEU_12_0[8]), .Q(d_ff_68_q));  // open: Qn, preset, reset
  D_Flip_Flop d_ff_69 (.D(d_ff_61_q), .clk(WEL_12_0[8]), .Q(d_ff_69_q));  // open: Qn, preset, reset
  D_Flip_Flop d_ff_70 (.D(d_ff_62_q), .clk(WEL_12_0[8]), .Q(d_ff_70_q));  // open: Qn, preset, reset
  D_Flip_Flop d_ff_71 (.D(d_ff_63_q), .clk(WEL_12_0[8]), .Q(d_ff_71_q));  // open: Qn, preset, reset
  D_Flip_Flop d_ff_72 (.D(d_ff_64_q), .clk(WEL_12_0[8]), .Q(d_ff_72_q));  // open: Qn, preset, reset
  D_Flip_Flop d_ff_73 (.D(d_ff_65_q), .clk(WEU_12_0[9]), .Q(d_ff_73_q));  // open: Qn, preset, reset
  D_Flip_Flop d_ff_74 (.D(d_ff_66_q), .clk(WEU_12_0[9]), .Q(d_ff_74_q));  // open: Qn, preset, reset
  D_Flip_Flop d_ff_75 (.D(d_ff_67_q), .clk(WEU_12_0[9]), .Q(d_ff_75_q));  // open: Qn, preset, reset
  D_Flip_Flop d_ff_76 (.D(d_ff_68_q), .clk(WEU_12_0[9]), .Q(d_ff_76_q));  // open: Qn, preset, reset
  D_Flip_Flop d_ff_77 (.D(d_ff_69_q), .clk(WEL_12_0[9]), .Q(d_ff_77_q));  // open: Qn, preset, reset
  D_Flip_Flop d_ff_78 (.D(d_ff_70_q), .clk(WEL_12_0[9]), .Q(d_ff_78_q));  // open: Qn, preset, reset
  D_Flip_Flop d_ff_79 (.D(d_ff_71_q), .clk(WEL_12_0[9]), .Q(d_ff_79_q));  // open: Qn, preset, reset
  D_Flip_Flop d_ff_80 (.D(d_ff_72_q), .clk(WEL_12_0[9]), .Q(d_ff_80_q));  // open: Qn, preset, reset
  D_Flip_Flop d_ff_81 (.D(d_ff_73_q), .clk(WEU_12_0[10]), .Q(d_ff_81_q));  // open: Qn, preset, reset
  D_Flip_Flop d_ff_82 (.D(d_ff_74_q), .clk(WEU_12_0[10]), .Q(d_ff_82_q));  // open: Qn, preset, reset
  D_Flip_Flop d_ff_83 (.D(d_ff_75_q), .clk(WEU_12_0[10]), .Q(d_ff_83_q));  // open: Qn, preset, reset
  D_Flip_Flop d_ff_84 (.D(d_ff_76_q), .clk(WEU_12_0[10]), .Q(d_ff_84_q));  // open: Qn, preset, reset
  D_Flip_Flop d_ff_85 (.D(d_ff_77_q), .clk(WEL_12_0[10]), .Q(d_ff_85_q));  // open: Qn, preset, reset
  D_Flip_Flop d_ff_86 (.D(d_ff_78_q), .clk(WEL_12_0[10]), .Q(d_ff_86_q));  // open: Qn, preset, reset
  D_Flip_Flop d_ff_87 (.D(d_ff_79_q), .clk(WEL_12_0[10]), .Q(d_ff_87_q));  // open: Qn, preset, reset
  D_Flip_Flop d_ff_88 (.D(d_ff_80_q), .clk(WEL_12_0[10]), .Q(d_ff_88_q));  // open: Qn, preset, reset
  D_Flip_Flop d_ff_89 (.D(d_ff_81_q), .clk(WEU_12_0[11]), .Q(d_ff_89_q));  // open: Qn, preset, reset
  D_Flip_Flop d_ff_90 (.D(d_ff_82_q), .clk(WEU_12_0[11]), .Q(d_ff_90_q));  // open: Qn, preset, reset
  D_Flip_Flop d_ff_91 (.D(d_ff_83_q), .clk(WEU_12_0[11]), .Q(d_ff_91_q));  // open: Qn, preset, reset
  D_Flip_Flop d_ff_92 (.D(d_ff_84_q), .clk(WEU_12_0[11]), .Q(d_ff_92_q));  // open: Qn, preset, reset
  D_Flip_Flop d_ff_93 (.D(d_ff_85_q), .clk(WEL_12_0[11]), .Q(d_ff_93_q));  // open: Qn, preset, reset
  D_Flip_Flop d_ff_94 (.D(d_ff_86_q), .clk(WEL_12_0[11]), .Q(d_ff_94_q));  // open: Qn, preset, reset
  D_Flip_Flop d_ff_95 (.D(d_ff_87_q), .clk(WEL_12_0[11]), .Q(d_ff_95_q));  // open: Qn, preset, reset
  D_Flip_Flop d_ff_96 (.D(d_ff_88_q), .clk(WEL_12_0[11]), .Q(d_ff_96_q));  // open: Qn, preset, reset
  D_Flip_Flop d_ff_97 (.D(d_ff_89_q), .clk(WEU112), .Q(AD_7_0[7]));  // open: Qn, preset, reset
  D_Flip_Flop d_ff_98 (.D(d_ff_90_q), .clk(WEU112), .Q(AD_7_0[6]));  // open: Qn, preset, reset
  D_Flip_Flop d_ff_99 (.D(d_ff_91_q), .clk(WEU112), .Q(AD_7_0[5]));  // open: Qn, preset, reset
  D_Flip_Flop d_ff_100 (.D(d_ff_92_q), .clk(WEU112), .Q(AD_7_0[4]));  // open: Qn, preset, reset
  D_Flip_Flop d_ff_101 (.D(d_ff_93_q), .clk(WEL_12_0[12]), .Q(AD_7_0[3]));  // open: Qn, preset, reset
  D_Flip_Flop d_ff_102 (.D(d_ff_94_q), .clk(WEL_12_0[12]), .Q(AD_7_0[2]));  // open: Qn, preset, reset
  D_Flip_Flop d_ff_103 (.D(d_ff_95_q), .clk(WEL_12_0[12]), .Q(AD_7_0[1]));  // open: Qn, preset, reset
  D_Flip_Flop d_ff_104 (.D(d_ff_96_q), .clk(WEL_12_0[12]), .Q(AD_7_0[0]));  // open: Qn, preset, reset

  // Other names for the same wires on the sheet: AD0 = AD_7_0[0]; AD1 = AD_7_0[1]; AD2 = AD_7_0[2]; AD3 = AD_7_0[3];
  //   AD4 = AD_7_0[4]; AD5 = AD_7_0[5]; AD6 = AD_7_0[6]; AD7 = AD_7_0[7]; IDBI0 = IDBI_7_0[0]; IDBI1 = IDBI_7_0[1];
  //   IDBI2 = IDBI_7_0[2]; IDBI3 = IDBI_7_0[3]; IDBI4 = IDBI_7_0[4]; IDBI5 = IDBI_7_0[5]; IDBI6 = IDBI_7_0[6];
  //   IDBI7 = IDBI_7_0[7]; WEL0 = WEL_12_0[0]; WEL1 = WEL_12_0[1]; WEL2 = WEL_12_0[2]; WEL3 = WEL_12_0[3];
  //   WEL4 = WEL_12_0[4]; WEL5 = WEL_12_0[5]; WEL6 = WEL_12_0[6]; WEL7 = WEL_12_0[7]; WEL8 = WEL_12_0[8];
  //   WEL9 = WEL_12_0[9]; WEL10 = WEL_12_0[10]; WEL11 = WEL_12_0[11]; WEL12 = WEL_12_0[12]; WEU0 = WEU_12_0[0];
  //   WEU1 = WEU_12_0[1]; WEU2 = WEU_12_0[2]; WEU3 = WEU_12_0[3]; WEU4 = WEU_12_0[4]; WEU5 = WEU_12_0[5];
  //   WEU6 = WEU_12_0[6]; WEU7 = WEU_12_0[7]; WEU8 = WEU_12_0[8]; WEU9 = WEU_12_0[9]; WEU10 = WEU_12_0[10];
  //   WEU11 = WEU_12_0[11]; WEU12 = WEU_12_0[12]

  // Notes on the sheet:
  //   Page 11 DECODE - DECODE_DGA_PFIFD Sheet 1 of 1
endmodule

module DECODE_DGA_PFIFC (
  input  CLEAR,
  input  LDPANCN,
  input  RMMN,
  output FULN,
  output [12:0] WEL_12_0,
  output [12:0] WEU_12_0,
  output EMPN
);

  wire A292_out, A300_out, A301_n01, A301_n02, A302_n01, A302_n02, A304_n01, A304_n02, A305_n01, A308_n01,
       A308_n02, A314_n01, A314_n02, A315_n01, A315_n02, A316_n01, A316_n02, A321_n01, A321_n02, A322_n01,
       A322_n02, A334_n01, A334_n02, A339_n01, A339_n02, A343_n02, and_1_out, and_2_out, and_3_out,
       and_4_out, and_5_out, and_6_out, and_7_out, and_8_out, and_9_out, and_10_out, and_11_out, and_12_out,
       and_13_out, CLEARN, decode_dga_pfifc_delay_1_pin_out, decode_dga_pfifc_delay_2_pin_out,
       decode_dga_pfifc_delay_3_pin_out, decode_dga_pfifc_delay_4_pin_out, decode_dga_pfifc_delay_5_pin_out,
       decode_dga_pfifc_delay_6_pin_out, decode_dga_pfifc_delay_7_pin_out, decode_dga_pfifc_delay_8_pin_out,
       decode_dga_pfifc_delay_9_pin_out, decode_dga_pfifc_delay_10_pin_out,
       decode_dga_pfifc_delay_11_pin_out, decode_dga_pfifc_delay_12_pin_out, nand_1_out, nand_2_out,
       nand_3_out, nand_4_out, nand_5_out, nand_6_out, nand_7_out, nand_8_out, nand_9_out, nand_10_out,
       nand_11_out, nand_12_out, nand_13_out, nand_14_out, nand_15_out, nand_16_out, nand_17_out,
       nand_18_out, nand_19_out, nand_20_out, nand_21_out, nand_22_out, nand_23_out, not_15_out, not_16_out,
       not_17_out, not_18_out, not_19_out, not_20_out, not_21_out, not_22_out, not_23_out, not_24_out,
       not_25_out, not_26_out, ZZ1;

  not not_1 (CLEARN, CLEAR);
  F091 A351 (.N01(ZZ1));  // open: N02
  DECODE_DGA_PFIFC_DELAY decode_dga_pfifc_delay_1 (.PIN_IN(WEL_12_0[1]), .PIN_OUT(decode_dga_pfifc_delay_1_pin_out));
  DECODE_DGA_PFIFC_DELAY decode_dga_pfifc_delay_2 (.PIN_IN(WEL_12_0[2]), .PIN_OUT(decode_dga_pfifc_delay_2_pin_out));
  DECODE_DGA_PFIFC_DELAY decode_dga_pfifc_delay_3 (.PIN_IN(WEL_12_0[3]), .PIN_OUT(decode_dga_pfifc_delay_3_pin_out));
  DECODE_DGA_PFIFC_DELAY decode_dga_pfifc_delay_4 (.PIN_IN(WEL_12_0[4]), .PIN_OUT(decode_dga_pfifc_delay_4_pin_out));
  DECODE_DGA_PFIFC_DELAY decode_dga_pfifc_delay_5 (.PIN_IN(WEL_12_0[5]), .PIN_OUT(decode_dga_pfifc_delay_5_pin_out));
  DECODE_DGA_PFIFC_DELAY decode_dga_pfifc_delay_6 (.PIN_IN(WEL_12_0[6]), .PIN_OUT(decode_dga_pfifc_delay_6_pin_out));
  DECODE_DGA_PFIFC_DELAY decode_dga_pfifc_delay_7 (.PIN_IN(WEL_12_0[7]), .PIN_OUT(decode_dga_pfifc_delay_7_pin_out));
  DECODE_DGA_PFIFC_DELAY decode_dga_pfifc_delay_8 (.PIN_IN(WEL_12_0[8]), .PIN_OUT(decode_dga_pfifc_delay_8_pin_out));
  DECODE_DGA_PFIFC_DELAY decode_dga_pfifc_delay_9 (.PIN_IN(WEL_12_0[9]), .PIN_OUT(decode_dga_pfifc_delay_9_pin_out));
  DECODE_DGA_PFIFC_DELAY decode_dga_pfifc_delay_10 (.PIN_IN(WEL_12_0[10]), .PIN_OUT(decode_dga_pfifc_delay_10_pin_out));
  DECODE_DGA_PFIFC_DELAY decode_dga_pfifc_delay_11 (.PIN_IN(WEL_12_0[11]), .PIN_OUT(decode_dga_pfifc_delay_11_pin_out));
  DECODE_DGA_PFIFC_DELAY decode_dga_pfifc_delay_12 (.PIN_IN(WEL_12_0[12]), .PIN_OUT(decode_dga_pfifc_delay_12_pin_out));
  and and_1 (and_1_out, WEL_12_0[0], WEL_12_0[0], CLEARN);
  nand nand_1 (nand_1_out, CLEARN, not_15_out);
  and and_2 (and_2_out, decode_dga_pfifc_delay_1_pin_out, decode_dga_pfifc_delay_1_pin_out, CLEARN);
  nand nand_2 (nand_2_out, CLEARN, not_16_out);
  and and_3 (and_3_out, decode_dga_pfifc_delay_2_pin_out, decode_dga_pfifc_delay_2_pin_out, CLEARN);
  nand nand_3 (nand_3_out, CLEARN, not_17_out);
  and and_4 (and_4_out, decode_dga_pfifc_delay_3_pin_out, decode_dga_pfifc_delay_3_pin_out, CLEARN);
  nand nand_4 (nand_4_out, CLEARN, not_18_out);
  and and_5 (and_5_out, decode_dga_pfifc_delay_4_pin_out, decode_dga_pfifc_delay_4_pin_out, CLEARN);
  nand nand_5 (nand_5_out, CLEARN, not_19_out);
  and and_6 (and_6_out, decode_dga_pfifc_delay_5_pin_out, decode_dga_pfifc_delay_5_pin_out, CLEARN);
  nand nand_6 (nand_6_out, CLEARN, not_20_out);
  and and_7 (and_7_out, decode_dga_pfifc_delay_6_pin_out, decode_dga_pfifc_delay_6_pin_out, CLEARN);
  nand nand_7 (nand_7_out, CLEARN, not_21_out);
  and and_8 (and_8_out, decode_dga_pfifc_delay_7_pin_out, decode_dga_pfifc_delay_7_pin_out, CLEARN);
  nand nand_8 (nand_8_out, CLEARN, not_22_out);
  and and_9 (and_9_out, decode_dga_pfifc_delay_8_pin_out, decode_dga_pfifc_delay_8_pin_out, CLEARN);
  nand nand_9 (nand_9_out, CLEARN, not_23_out);
  and and_10 (and_10_out, decode_dga_pfifc_delay_9_pin_out, decode_dga_pfifc_delay_9_pin_out, CLEARN);
  nand nand_10 (nand_10_out, CLEARN, not_24_out);
  and and_11 (and_11_out, decode_dga_pfifc_delay_10_pin_out, decode_dga_pfifc_delay_10_pin_out, CLEARN);
  nand nand_11 (nand_11_out, CLEARN, not_25_out);
  and and_12 (and_12_out, decode_dga_pfifc_delay_11_pin_out, decode_dga_pfifc_delay_11_pin_out, CLEARN);
  nand nand_12 (nand_12_out, CLEARN, not_26_out);
  and and_13 (and_13_out, decode_dga_pfifc_delay_12_pin_out, decode_dga_pfifc_delay_12_pin_out, CLEARN);
  nand nand_13 (nand_13_out, CLEARN, RMMN);
  F595 A305 (.H01(and_1_out), .H02(nand_1_out), .H03(ZZ1), .N01(A305_n01), .N02(FULN));
  F595 A314 (.H01(and_2_out), .H02(nand_2_out), .H03(ZZ1), .N01(A314_n01), .N02(A314_n02));
  F595 A321 (.H01(and_3_out), .H02(nand_3_out), .H03(ZZ1), .N01(A321_n01), .N02(A321_n02));
  F595 A316 (.H01(and_4_out), .H02(nand_4_out), .H03(ZZ1), .N01(A316_n01), .N02(A316_n02));
  F595 A308 (.H01(and_5_out), .H02(nand_5_out), .H03(ZZ1), .N01(A308_n01), .N02(A308_n02));
  F595 A322 (.H01(and_6_out), .H02(nand_6_out), .H03(ZZ1), .N01(A322_n01), .N02(A322_n02));
  F595 A302 (.H01(and_7_out), .H02(nand_7_out), .H03(ZZ1), .N01(A302_n01), .N02(A302_n02));
  F595 A304 (.H01(and_8_out), .H02(nand_8_out), .H03(ZZ1), .N01(A304_n01), .N02(A304_n02));
  F595 A301 (.H01(and_9_out), .H02(nand_9_out), .H03(ZZ1), .N01(A301_n01), .N02(A301_n02));
  F595 A315 (.H01(and_10_out), .H02(nand_10_out), .H03(ZZ1), .N01(A315_n01), .N02(A315_n02));
  F595 A339 (.H01(and_11_out), .H02(nand_11_out), .H03(ZZ1), .N01(A339_n01), .N02(A339_n02));
  F595 A334 (.H01(and_12_out), .H02(nand_12_out), .H03(ZZ1), .N01(A334_n01), .N02(A334_n02));
  F595 A343 (.H01(and_13_out), .H02(nand_13_out), .H03(ZZ1), .N01(EMPN), .N02(A343_n02));
  nand A300 (A300_out, LDPANCN, A305_n01, A314_n02, not_16_out);
  nand A292 (A292_out, not_15_out, A314_n01, A321_n02, not_17_out);
  nand nand_14 (nand_14_out, not_16_out, A321_n01, A316_n02, not_18_out);
  nand nand_15 (nand_15_out, not_17_out, A316_n01, A308_n02, not_19_out);
  nand nand_16 (nand_16_out, not_18_out, A308_n01, A322_n02, not_20_out);
  nand nand_17 (nand_17_out, not_19_out, A322_n01, A302_n02, not_21_out);
  nand nand_18 (nand_18_out, not_20_out, A302_n01, A304_n02, not_22_out);
  nand nand_19 (nand_19_out, not_21_out, A304_n01, A301_n02, not_23_out);
  nand nand_20 (nand_20_out, not_22_out, A301_n01, A315_n02, not_24_out);
  nand nand_21 (nand_21_out, not_23_out, A315_n01, A339_n02, not_25_out);
  nand nand_22 (nand_22_out, not_24_out, A339_n01, A334_n02, not_26_out);
  nand nand_23 (nand_23_out, not_25_out, A334_n01, A343_n02, RMMN);
  not not_2 (WEL_12_0[0], LDPANCN);
  not not_3 (WEL_12_0[1], A300_out);
  not not_4 (WEL_12_0[2], A292_out);
  not not_5 (WEL_12_0[3], nand_14_out);
  not not_6 (WEL_12_0[4], nand_15_out);
  not not_7 (WEL_12_0[5], nand_16_out);
  not not_8 (WEL_12_0[6], nand_17_out);
  not not_9 (WEL_12_0[7], nand_18_out);
  not not_10 (WEL_12_0[8], nand_19_out);
  not not_11 (WEL_12_0[9], nand_20_out);
  not not_12 (WEL_12_0[10], nand_21_out);
  not not_13 (WEL_12_0[11], nand_22_out);
  not not_14 (WEL_12_0[12], nand_23_out);
  not not_15 (not_15_out, WEL_12_0[1]);
  not not_16 (not_16_out, WEL_12_0[2]);
  not not_17 (not_17_out, WEL_12_0[3]);
  not not_18 (not_18_out, WEL_12_0[4]);
  not not_19 (not_19_out, WEL_12_0[5]);
  not not_20 (not_20_out, WEL_12_0[6]);
  not not_21 (not_21_out, WEL_12_0[7]);
  not not_22 (not_22_out, WEL_12_0[8]);
  not not_23 (not_23_out, WEL_12_0[9]);
  not not_24 (not_24_out, WEL_12_0[10]);
  not not_25 (not_25_out, WEL_12_0[11]);
  not not_26 (not_26_out, WEL_12_0[12]);

  assign WEU_12_0 = WEL_12_0;

  // Other names for the same wires on the sheet: WEL0 = WEL_12_0[0]; WEU0 = WEL_12_0[0]; WEL1 = WEL_12_0[1];
  //   WEU1 = WEL_12_0[1]; WEL2 = WEL_12_0[2]; WEU2 = WEL_12_0[2]; WEL3 = WEL_12_0[3]; WEU3 = WEL_12_0[3];
  //   WEL4 = WEL_12_0[4]; WEU4 = WEL_12_0[4]; WEL5 = WEL_12_0[5]; WEU5 = WEL_12_0[5]; WEL6 = WEL_12_0[6];
  //   WEU6 = WEL_12_0[6]; WEL7 = WEL_12_0[7]; WEU7 = WEL_12_0[7]; WEL8 = WEL_12_0[8]; WEU8 = WEL_12_0[8];
  //   WEL9 = WEL_12_0[9]; WEU9 = WEL_12_0[9]; WEL10 = WEL_12_0[10]; WEU10 = WEL_12_0[10]; WEL11 = WEL_12_0[11];
  //   WEU11 = WEL_12_0[11]; WEL12 = WEL_12_0[12]; WEU12 = WEL_12_0[12]

  // Notes on the sheet:
  //   Page 12 DECODE - DECODE_DGA_PFIFC Sheet 1 of 1
  //   WEL1
  //   WEL2
endmodule

module DECODE_DGA_PFIFC_DELAY (
  input  PIN_IN,
  output PIN_OUT
);

  wire buffer_1_out, buffer_2_out, buffer_3_out, buffer_4_out, buffer_5_out, buffer_6_out;

  buf buffer_1 (buffer_1_out, PIN_IN);
  buf buffer_2 (buffer_2_out, buffer_1_out);
  buf buffer_3 (buffer_3_out, buffer_2_out);
  buf buffer_4 (buffer_4_out, buffer_3_out);
  buf buffer_5 (buffer_5_out, buffer_4_out);
  buf buffer_6 (buffer_6_out, buffer_5_out);
  buf buffer_7 (PIN_OUT, buffer_6_out);

  // Notes on the sheet:
  //   Page 13 DECODE - DECODE_DGA_PFIFC_DELAY Sheet 1 of 1
endmodule

module DECODE_DGA_IDBS (
  input  [4:0] CSIDBS_4_0,
  input  LCSN,
  input  CLK0,
  input  CLK1,
  input  STAT4,
  input  STAT3,
  output ECSRN,
  output EIORN,
  output EPESN,
  output EPEAN,
  output RUARTN,
  output EDON,
  output EPANSN,
  output RINRN,
  output EPANN,
  output TRAALDN,
  output PRQN,
  output VAL
);

  wire A249_out, A250_out, A251_out, A252_out, A253_out, A254_out, A255_out, A256_out, A258_out, A261_out,
       A262_out, A263_out, A264_out, A265_out, A269_out, A283_out, A284_out, A285_out, A286_out, and_1_out,
       and_2_out, and_3_out, and_4_out, and_5_out, and_6_out, CSEPANSN, f924_1_n02, f924_1_n03, f924_1_n06,
       f924_1_n07, f924_1_n08, ID0N, ID1N, ID2N, ID3N, ID4N, MAPANS, nand_1_out, nand_2_out, ZZ1;

  not not_1 (ID0N, CSIDBS_4_0[0]);
  not not_2 (ID1N, CSIDBS_4_0[1]);
  not not_3 (ID2N, CSIDBS_4_0[2]);
  not not_4 (ID3N, CSIDBS_4_0[3]);
  not not_5 (ID4N, CSIDBS_4_0[4]);
  and and_1 (and_1_out, VAL, STAT4, MAPANS, LCSN);
  and and_2 (and_2_out, ZZ1, STAT4, LCSN, f924_1_n06);
  and and_3 (and_3_out, f924_1_n07, STAT3, LCSN);
  and and_4 (and_4_out, STAT3, LCSN, f924_1_n08);
  and and_5 (and_5_out, STAT3, f924_1_n03, CSEPANSN, LCSN);
  and and_6 (and_6_out, ZZ1, CSEPANSN, f924_1_n08, LCSN);
  nand A286 (A286_out, f924_1_n02, STAT4, LCSN);
  nor A284 (A284_out, and_1_out, and_2_out);
  nor A285 (A285_out, and_3_out, and_4_out);
  nor A283 (A283_out, and_5_out, and_6_out);
  nand A264 (A264_out, ID4N, ID3N, ID2N, LCSN);
  nand A262 (A262_out, CSIDBS_4_0[4], ID3N, CSIDBS_4_0[2], CSIDBS_4_0[1], ID0N, LCSN);
  nand A263 (A263_out, ID4N, ID3N, ID0N, LCSN);
  nand A250 (A250_out, ID4N, CSIDBS_4_0[3], ID1N, LCSN);
  nand A258 (A258_out, CSIDBS_4_0[4], ID3N, CSIDBS_4_0[2], CSIDBS_4_0[1], CSIDBS_4_0[0], LCSN);
  F924 f924_1 (
    .H01(A286_out), .H02(A284_out), .H03(A285_out), .H04(A283_out), .H05(CLK1), .N02(f924_1_n02),
    .N03(f924_1_n03), .N04(PRQN), .N05(VAL), .N06(f924_1_n06), .N07(f924_1_n07), .N08(f924_1_n08));  // open: N01
  nand A256 (A256_out, ID3N, ID2N, CSIDBS_4_0[1], LCSN);
  nand A249 (A249_out, A264_out, A263_out, A250_out, A256_out, A261_out, A269_out, A255_out, ZZ1);
  nand A265 (A265_out, CSIDBS_4_0[4], CSIDBS_4_0[3], CSIDBS_4_0[2], ID1N, CSIDBS_4_0[0], LCSN);
  nand A261 (A261_out, CSIDBS_4_0[4], ID3N, CSIDBS_4_0[2], ID1N, CSIDBS_4_0[0], LCSN);
  nand A260 (CSEPANSN, CSIDBS_4_0[4], ID3N, ID2N, ID1N, LCSN);
  nand A269 (A269_out, CSIDBS_4_0[3], ID2N, ID1N, CSIDBS_4_0[0], LCSN);
  F091 A277 (.N01(ZZ1));  // open: N02
  F924 A259 (
    .H01(CSEPANSN), .H02(A265_out), .H03(A258_out), .H04(A262_out), .H05(CLK1), .N01(EPANSN), .N02(RINRN),
    .N03(EPANN), .N04(TRAALDN));  // open: N05, N06, N07, N08
  nand A255 (A255_out, CSIDBS_4_0[4], CSIDBS_4_0[3], CSIDBS_4_0[2], CSIDBS_4_0[1], ID0N, LCSN);
  nand A251 (A251_out, ID4N, CSIDBS_4_0[3], ID2N, CSIDBS_4_0[1], ID0N, LCSN);
  nand nand_1 (nand_1_out, CSIDBS_4_0[4], ID3N, ID2N, ID1N, CSIDBS_4_0[0], LCSN);
  nand A252 (A252_out, ID4N, CSIDBS_4_0[3], ID2N, CSIDBS_4_0[1], CSIDBS_4_0[0], LCSN);
  nand nand_2 (nand_2_out, CSIDBS_4_0[4], CSIDBS_4_0[3], CSIDBS_4_0[2], CSIDBS_4_0[1], CSIDBS_4_0[0], LCSN);
  nand A253 (A253_out, ID4N, CSIDBS_4_0[3], CSIDBS_4_0[2], CSIDBS_4_0[1], ID0N, LCSN);
  nand A254 (A254_out, CSIDBS_4_0[4], ID3N, CSIDBS_4_0[2], ID1N, ID0N, LCSN);
  F924 A248 (
    .H01(A254_out), .H02(A253_out), .H03(A252_out), .H04(A251_out), .H05(CLK0), .N01(ECSRN), .N02(EIORN),
    .N03(EPESN), .N04(EPEAN));  // open: N05, N06, N07, N08
  F924 A275 (
    .H01(1'b1), .H02(A249_out), .H03(nand_2_out), .H04(nand_1_out), .H05(CLK0), .N03(RUARTN), .N06(EDON),
    .N08(MAPANS));  // open: N01, N02, N04, N05, N07

  // Other names for the same wires on the sheet: ID0 = CSIDBS_4_0[0]; ID1 = CSIDBS_4_0[1]; ID2 = CSIDBS_4_0[2];
  //   ID3 = CSIDBS_4_0[3]; ID4 = CSIDBS_4_0[4]

  // Notes on the sheet:
  //   Page 14 DECODE - DECODE_DGA_IDBS Sheet 1 of 2
  //   Page 15 DECODE - DECODE_DGA_IDBS Sheet 2 of 2
  //   VAL
  //   STAT4
  //   MAPANS
  //   LCSN
  //   STAT4
  //   LCSN
  //   RIWR
  //   DSTAT3
  //   STAT3
  //   LCSN
  //   STAT3
  //   LCSN
  //   PRQ
  //   STAT3
  //   DSTAT3
  //   CSEPANSN
  //   LCSN
  //   CSEPANSN
  //   PRQ
  //   LCSN
  //   RIWRN
  //   STAT4
  //   LCSN
  //   26 -  ALD
  //   27 -  PANEL
  //   RIWRN
  //   DSTAT3N
  //   PRQN
  //   VAL
  //   RIWR
  //   DSTAT3
  //   PRQ
  //   2 - GPR, 3- DBR
  //   35 - RINR
  //   25 - PCR
  //   20 - MIPANS, 21 - MAPANS
  //   11 - SWAP
  //   36 - PICMSK
  //   12-PEA
  //   21 - MAPANS
  //   13-PES
  //   37 - UART
  //   16-IOR
  //   24 - CSR
endmodule

module DECODE_DGA_COMM (
  input  [4:0] CSCOMM_4_0,
  input  LCSN,
  input  [1:0] CSMIS_1_0,
  input  CLK2,
  input  CLK3,
  input  EORFN,
  input  IDBI5,
  input  IDBI7,
  input  CLEAR,
  input  PONI,
  input  IDBI2,
  input  CLK1,
  input  HIT,
  input  BRKN,
  input  LSHADOW,
  input  DAPN,
  input  UCLK,
  output FETCH,
  output FMISS,
  output DTN,
  output WRITE,
  output RTN,
  output FORMN,
  output MREQ,
  output CCLRN,
  output SSTOPN,
  output CLRTIN,
  output CEUARTN,
  output SSEMAN,
  output EMPIDN,
  output SLOWN,
  output LDPANCN,
  output STARTN,
  output WCHIMN,
  output EMCLN,
  output RESET,
  output SIOCN,
  output DVACCN,
  output SHORTN,
  output IORQN,
  output RWCSN,
  output LHIT,
  output ESTOFN,
  output ECREQ,
  output STOCN,
  output CA10
);

  wire A141_out, A142_out, A143_out, A144_out, A145_out, A147_out, A148_out, A149_out, A150_out, A152_out,
       A155_out, A156_out, A158_out, A162_out, A166_out, A167_out, A171_out, A172_out, A177_out, A180_out,
       A182_out, A183_out, A184_out, A185_out, A186_out, A187_n07, A188_n07, A189_out, A190_out, A191_out,
       A192_out, A193_out, A194_n01, A196_out, A197_out, A198_out, A199_out, A200_out, A201_n01, A204_q,
       A206_out, A208_n01, A211_out, A212_out, A213_out, A214_n01, A215_out, A216_out, A217_out, A218_out,
       A219_out, A220_out, A221_n01, A222_out, A223_out, A224_out, A225_n01, A226_q, A226_qn, A228_out,
       A229_out, A230_out, A232_q, A233_out, A235_out, A236_n01, A237_out, A238_out, A242_out, A243_out,
       A245_out, C0N, C1N, C2N, C3N, C4N, EORF, ICA10, IORQ, M0N, M1N, not_8_out, not_9_out, not_11_out,
       not_12_out, not_13_out, not_14_out, RT, SSEMA, ZZ1;

  not not_1 (C0N, CSCOMM_4_0[0]);
  not not_2 (C1N, CSCOMM_4_0[1]);
  not not_3 (C2N, CSCOMM_4_0[2]);
  not not_4 (C3N, CSCOMM_4_0[3]);
  not not_5 (C4N, CSCOMM_4_0[4]);
  not not_6 (M0N, CSMIS_1_0[0]);
  not not_7 (M1N, CSMIS_1_0[1]);
  nand A192 (A192_out, SSEMA, MREQ, LCSN);
  F091 A225 (.N01(A225_n01));  // open: N02
  nand A206 (A206_out, A192_out, A193_out);
  nand A193 (A193_out, M1N, CSMIS_1_0[0], CSCOMM_4_0[4], C3N, C2N, C1N, CSCOMM_4_0[0], LCSN);
  nand A212 (A212_out, A225_n01, CSMIS_1_0[1], CSCOMM_4_0[4], CSCOMM_4_0[3], CSCOMM_4_0[2], CSCOMM_4_0[1], CSCOMM_4_0[0], LCSN);
  nand A156 (A156_out, CSCOMM_4_0[4], C3N, CSCOMM_4_0[2], LCSN);
  nand A149 (A149_out, A156_out, A142_out, A145_out, A152_out, A150_out, A155_out);
  nand A150 (A150_out, CSCOMM_4_0[4], C3N, CSCOMM_4_0[1], CSCOMM_4_0[0], LCSN);
  nand A199 (A199_out, C4N, C3N, CSCOMM_4_0[2], C1N, CSCOMM_4_0[0], LCSN);
  nand A211 (A211_out, M1N, CSMIS_1_0[0], CSCOMM_4_0[4], CSCOMM_4_0[3], CSCOMM_4_0[2], CSCOMM_4_0[1], C0N, LCSN);
  F924 A181 (
    .H01(1'b1), .H02(A191_out), .H03(A199_out), .H04(A206_out), .H05(CLK3), .N02(SSTOPN), .N03(CEUARTN),
    .N04(SSEMA), .N08(SSEMAN));  // open: N01, N05, N06, N07
  nand A155 (A155_out, CSCOMM_4_0[4], CSCOMM_4_0[3], C2N, C1N, LCSN);
  nand A191 (A191_out, C4N, CSCOMM_4_0[3], CSCOMM_4_0[2], C1N, C0N, LCSN);
  not not_8 (not_8_out, LSHADOW);
  nand A152 (A152_out, CSCOMM_4_0[4], CSCOMM_4_0[3], C1N, C0N, LCSN);
  nand A222 (A222_out, CSMIS_1_0[0], C4N, CSCOMM_4_0[2], CSCOMM_4_0[1], LCSN);
  nand A158 (A158_out, A147_out, A141_out, A145_out);
  F924 A214 (
    .H01(A213_out), .H02(A216_out), .H03(A211_out), .H04(A212_out), .H05(CLK2), .N01(A214_n01), .N03(RWCSN),
    .N04(IORQN), .N06(SHORTN), .N08(IORQ));  // open: N02, N05, N07
  F924 A140 (
    .H01(A162_out), .H02(1'b1), .H03(A158_out), .H04(A149_out), .H05(CLK2), .N01(FETCH), .N04(RT), .N07(DTN),
    .N08(RTN));  // open: N02, N03, N05, N06
  nand A185 (A185_out, CSCOMM_4_0[4], CSCOMM_4_0[3], CSCOMM_4_0[2], CSCOMM_4_0[1], C0N, CSMIS_1_0[0]);
  and A242 (A242_out, BRKN, not_8_out, EORF);
  nand A147 (A147_out, CSCOMM_4_0[4], CSCOMM_4_0[3], C2N, CSCOMM_4_0[1], LCSN);
  nand A223 (A223_out, CSMIS_1_0[0], C3N, C2N, C1N, LCSN);
  not not_9 (not_9_out, DAPN);
  nand A237 (A237_out, WRITE, UCLK);
  nand A198 (A198_out, C4N, C3N, CSCOMM_4_0[2], C1N, CSCOMM_4_0[0]);
  nand A200 (A200_out, A185_out, A198_out, LCSN);
  not not_10 (EORF, EORFN);
  D_Flip_Flop d_ff_1 (.D(ICA10), .clk(CLK1), .Q(CA10), .reset(not_11_out));  // open: Qn, preset
  not not_11 (not_11_out, A237_out);
  nand A141 (A141_out, CSCOMM_4_0[4], CSCOMM_4_0[3], C1N, LCSN);
  F091 A178 (.N01(ZZ1));  // open: N02
  nand A228 (A228_out, CSMIS_1_0[1], C3N, C2N, C1N, LCSN);
  and A246 (ESTOFN, LSHADOW, RT);
  nand A233 (A233_out, RT, HIT, A242_out);
  nand A238 (A238_out, WRITE, A242_out);
  nand A235 (A235_out, EORF, IORQ);
  nand A245 (A245_out, RT, not_8_out);
  nand A243 (A243_out, IORQ, not_9_out);
  F571 A221 (.H01(IDBI2), .H02(A226_q), .H03(A214_n01), .H04(1'b0), .N01(A221_n01));
  F571 A236 (.H01(A232_q), .H02(HIT), .H03(RT), .H04(1'b0), .N01(A236_n01));
  nand A162 (A162_out, A156_out, A150_out, A142_out);
  nand A209 (EMPIDN, EORF, A187_n07);
  nand A183 (A183_out, C4N, CSCOMM_4_0[3], C2N, CSCOMM_4_0[1], C0N, LCSN);
  F924 A187 (
    .H01(A184_out), .H02(A182_out), .H03(A183_out), .H04(A200_out), .H05(CLK3), .N01(CLRTIN), .N02(SIOCN),
    .N04(SLOWN), .N07(A187_n07));  // open: N03, N05, N06, N08
  nand A239 (ECREQ, A233_out, A238_out, A235_out);
  nand A244 (STOCN, A245_out, A243_out);
  nand A145 (A145_out, ZZ1, M1N, CSCOMM_4_0[4], C3N, C2N, CSCOMM_4_0[1], C0N, LCSN);
  nand A229 (A229_out, C4N, CSCOMM_4_0[2], C1N, C0N, LCSN);
  nand A216 (A216_out, A225_n01, A222_out, A223_out, A228_out, A229_out, A217_out, A218_out, A219_out);
  D_Flip_Flop A226 (.D(A221_n01), .clk(CLK2), .Q(A226_q), .Qn(A226_qn));  // open: preset, reset
  D_Flip_Flop A232 (.D(A236_n01), .clk(CLK1), .Q(A232_q), .Qn(LHIT));  // open: preset, reset
  nand A167 (A167_out, A147_out, A144_out);
  nand A182 (A182_out, C4N, C3N, CSCOMM_4_0[2], CSCOMM_4_0[1], CSCOMM_4_0[0], LCSN);
  F924 A160 (
    .H01(A171_out), .H02(A166_out), .H03(A148_out), .H04(A167_out), .H05(CLK2), .N01(FMISS), .N04(WRITE),
    .N06(FORMN), .N07(MREQ));  // open: N02, N03, N05, N08
  F571 A208 (.H01(IDBI5), .H02(EMCLN), .H03(SIOCN), .H04(1'b0), .N01(A208_n01));
  nand A217 (A217_out, C3N, C2N, C1N, C0N, LCSN);
  nand A142 (A142_out, CSMIS_1_0[0], CSMIS_1_0[1], CSCOMM_4_0[4], C3N, C2N, CSCOMM_4_0[1], C0N, LCSN);
  nand A184 (A184_out, C4N, CSCOMM_4_0[3], CSCOMM_4_0[2], C1N, CSCOMM_4_0[0], LCSN);
  D_Flip_Flop d_ff_2 (.D(A208_n01), .clk(CLK3), .Q(EMCLN), .reset(not_12_out));  // open: Qn, preset
  not not_12 (not_12_out, CLEAR);
  nand A148 (A148_out, A145_out, A142_out, A156_out, A150_out, A141_out, A147_out);
  nand A218 (A218_out, C4N, C3N, C2N, LCSN);
  nand A143 (A143_out, ZZ1, CSMIS_1_0[1], CSCOMM_4_0[4], C3N, C2N, CSCOMM_4_0[1], C0N, LCSN);
  nand A180 (A180_out, M0N, M1N, CSCOMM_4_0[4], C3N, C2N, C1N, CSCOMM_4_0[0], LCSN);
  nand A219 (A219_out, C4N, CSCOMM_4_0[3], CSCOMM_4_0[2], LCSN);
  nand A166 (A166_out, A143_out, A156_out, A150_out);
  nand A144 (A144_out, CSCOMM_4_0[4], CSCOMM_4_0[3], CSCOMM_4_0[2], C1N, CSCOMM_4_0[0], LCSN);
  nand A195 (LDPANCN, EORF, A188_n07);
  nand A186 (A186_out, M0N, CSMIS_1_0[1], C4N, C3N, CSCOMM_4_0[2], CSCOMM_4_0[1], C0N, LCSN);
  F924 A188 (
    .H01(1'b1), .H02(A190_out), .H03(A186_out), .H04(A180_out), .H05(CLK3), .N02(STARTN), .N04(WCHIMN),
    .N07(A188_n07));  // open: N01, N03, N05, N06, N08
  nand A213 (A213_out, CSMIS_1_0[1], CSMIS_1_0[0], CSCOMM_4_0[4], C3N, C2N, C1N, CSCOMM_4_0[0], LCSN);
  nand A153 (ICA10, A142_out, A150_out, A144_out, A156_out, A147_out);
  nand A190 (A190_out, C4N, CSCOMM_4_0[3], C2N, CSCOMM_4_0[1], CSCOMM_4_0[0], LCSN);
  nand A177 (A177_out, LCSN, MREQ, FMISS);
  nand A215 (A215_out, A226_qn, CSMIS_1_0[1], CSMIS_1_0[0], CSCOMM_4_0[4], CSCOMM_4_0[3], CSCOMM_4_0[2], C1N, LCSN);
  nand A220 (A220_out, A212_out, A215_out, A224_out);
  nand A171 (A171_out, A177_out, A172_out);
  nand A172 (A172_out, LCSN, SSEMA);
  F571 A201 (.H01(IDBI7), .H02(RESET), .H04(1'b0), .N01(A201_n01));  // open: H03
  not A230 (A230_out, PONI);
  D_Flip_Flop A227 (.D(A220_out), .clk(CLK2), .Qn(DVACCN));  // open: Q, preset, reset
  nand A224 (A224_out, A230_out, LCSN);
  nand A189 (A189_out, M0N, CSMIS_1_0[1], CSCOMM_4_0[4], C3N, C2N, C1N, CSCOMM_4_0[0], LCSN);
  not not_13 (not_13_out, CLK3);
  D_Flip_Flop d_ff_3 (.D(A201_n01), .clk(CLK3), .Q(RESET), .reset(not_14_out));  // open: Qn, preset
  not not_14 (not_14_out, CLEAR);
  D_Flip_Flop A204 (.D(A189_out), .clk(not_13_out), .Q(A204_q));  // open: Qn, preset, reset
  not A197 (A197_out, CLK3);
  nor A196 (A196_out, A204_q, A197_out);
  F091 A194 (.N01(A194_n01));  // open: N02
  F595 A207 (.H01(A196_out), .H02(A197_out), .H03(A194_n01), .N02(CCLRN));  // open: N01

  // Other names for the same wires on the sheet: C0 = CSCOMM_4_0[0]; C1 = CSCOMM_4_0[1]; C2 = CSCOMM_4_0[2];
  //   C3 = CSCOMM_4_0[3]; C4 = CSCOMM_4_0[4]; M0 = CSMIS_1_0[0]; M1 = CSMIS_1_0[1]

  // Notes on the sheet:
  //   Page 16 DECODE - DECODE_DGA_COMM - Sheet 1 of 4
  //   Page 17 DECODE - DECODE_DGA_COMM - Sheet 2 of 4
  //   Page 18 DECODE - DECODE_DGA_COMM - Sheet 3 of 4
  //   SSEMA
  //   Page 19 DECODE - DECODE_DGA_COMM - Sheet 4 of 4
  //   IDENT 37,1   - IOXT 37,3
  //   RWCS 36,1
  //   IRT
  //   DT
  //   FETCH
  //   HITN
  //   LHITN
  //   ISLOWN
  //   IEMPIDN
  //   VEX
  //   LHITN
  //   VEXN
  //   ISIOCN
  //   ICRLTIN
  //   IWCHIMN
  //   21,3 - LDEXM
  //   ILDPANC
  //   ISTARTN
  //   35,2 WRITE, HOLD
  //   34,2 READ, HOLD
endmodule

module F091 (
  output N01,
  output N02
);


  assign N01 = 1'b1;
  assign N02 = 1'b0;

  // Notes on the sheet:
  //   This is a wild guess on the functionality for F091. Used in P17
endmodule

module F103 (
  input  F_IN,
  output F_OUT
);

  not not_1 (F_OUT, F_IN);

  // Notes on the sheet:
  //   F103 used in Page 10 (DECODE_DGA_POW)- looks like a NOT gate but can also be some delay ?
endmodule

module F571 (
  input  H01,
  input  H02,
  input  H03,
  input  H04,
  output N01
);

  // NOT_Gate not_1 has open pins: in=H04, out=open
  Multiplexer multiplexer_1 (.in0(H01), .in1(H02), .out(N01), .sel(H03));

  // Notes on the sheet:
  //   This is a wild guess on the functionality for F571. Used in Page 17 and 10
endmodule

module F595 (
  input  H01,
  input  H02,
  input  H03,
  output N01,
  output N02
);

  wire not_1_out;

  not not_1 (not_1_out, H03);
  D_Flip_Flop d_ff_1 (.D(H01), .clk(H02), .Q(N01), .Qn(N02), .reset(not_1_out));  // open: preset

  // Notes on the sheet:
  //   This is a wild guess on the functionality for F595. Used in Page 17
endmodule

module F924 (
  input  H01,
  input  H02,
  input  H03,
  input  H04,
  input  H05,
  output N01,
  output N02,
  output N03,
  output N04,
  output N05,
  output N06,
  output N07,
  output N08
);

  D_Flip_Flop d_ff_1 (.D(H01), .clk(H05), .Q(N01));  // open: Qn, preset, reset
  D_Flip_Flop d_ff_2 (.D(H02), .clk(H05), .Q(N02));  // open: Qn, preset, reset
  D_Flip_Flop d_ff_3 (.D(H03), .clk(H05), .Q(N03));  // open: Qn, preset, reset
  D_Flip_Flop d_ff_4 (.D(H04), .clk(H05), .Q(N04));  // open: Qn, preset, reset

  assign N05 = N01;
  assign N06 = N02;
  assign N07 = N03;
  assign N08 = N04;
endmodule

module F714 (
  input  S,
  input  T,
  input  R,
  output Q,
  output QN
);

  D_Flip_Flop d_ff_1 (.clk(T), .Q(Q), .Qn(QN), .preset(S), .reset(R));  // open: D

  // Notes on the sheet:
  //   This is a wild guess on the functionality for F595. Used in Page 10
endmodule
